// Logisim project projeto1 - raw.circ as structural Verilog: 18 circuits, main circuit main
module main (
  output [3:0] Y,
  output [3:0] X
);

  wire conversor_segmentos_1_a, conversor_segmentos_1_b, conversor_segmentos_1_c, conversor_segmentos_1_d,
       conversor_segmentos_1_e, conversor_segmentos_1_f, conversor_segmentos_1_g, conversor_segmentos_2_a,
       conversor_segmentos_2_b, conversor_segmentos_2_c, conversor_segmentos_2_d, conversor_segmentos_2_e,
       conversor_segmentos_2_f, conversor_segmentos_2_g, conversor_segmentos_3_a, conversor_segmentos_3_b,
       conversor_segmentos_3_c, conversor_segmentos_3_d, conversor_segmentos_3_e, conversor_segmentos_3_f,
       conversor_segmentos_3_g, conversor_segmentos_4_a, conversor_segmentos_4_b, conversor_segmentos_4_c,
       conversor_segmentos_4_d, conversor_segmentos_4_e, conversor_segmentos_4_f, conversor_segmentos_4_g;
  wire [3:0] separador_x_1_dezena, separador_x_1_unidade, separador_y_1_dezena, separador_y_1_unidade;
  wire [14:0] grafico_1_coluna_0, grafico_1_coluna_1, grafico_1_coluna_2, grafico_1_coluna_3,
       grafico_1_coluna_4, grafico_1_coluna_5, grafico_1_coluna_6, grafico_1_coluna_7, grafico_1_coluna_8,
       grafico_1_coluna_9, grafico_1_coluna_10, grafico_1_coluna_11, grafico_1_coluna_12,
       grafico_1_coluna_13, grafico_1_coluna_14;

  DotMatrix #(.matrixcols(15), .matrixrows(15)) dotmatrix_1 (
    .col0(grafico_1_coluna_0), .col1(grafico_1_coluna_1), .col2(grafico_1_coluna_2),
    .col3(grafico_1_coluna_3), .col4(grafico_1_coluna_4), .col5(grafico_1_coluna_5),
    .col6(grafico_1_coluna_6), .col7(grafico_1_coluna_7), .col8(grafico_1_coluna_8),
    .col9(grafico_1_coluna_9), .col10(grafico_1_coluna_10), .col11(grafico_1_coluna_11),
    .col12(grafico_1_coluna_12), .col13(grafico_1_coluna_13), .col14(grafico_1_coluna_14));
  GRAFICO grafico_1 (
    .COLUNA_0(grafico_1_coluna_0), .COLUNA_1(grafico_1_coluna_1), .COLUNA_2(grafico_1_coluna_2),
    .COLUNA_3(grafico_1_coluna_3), .COLUNA_4(grafico_1_coluna_4), .COLUNA_5(grafico_1_coluna_5),
    .COLUNA_6(grafico_1_coluna_6), .COLUNA_7(grafico_1_coluna_7), .COLUNA_8(grafico_1_coluna_8),
    .COLUNA_9(grafico_1_coluna_9), .COLUNA_10(grafico_1_coluna_10), .COLUNA_11(grafico_1_coluna_11),
    .COLUNA_12(grafico_1_coluna_12), .COLUNA_13(grafico_1_coluna_13), .COLUNA_14(grafico_1_coluna_14), .X(X),
    .Y(Y));
  Joystick joystick_1 (.x(X), .y(Y));
  Hex_Digit_Display hex_digit_display_1 (.value(separador_y_1_dezena));  // open: dp
  SEPARADOR_Y separador_y_1 (.DEZENA(separador_y_1_dezena), .UNIDADE(separador_y_1_unidade), .Y(Y));
  Hex_Digit_Display hex_digit_display_2 (.value(separador_y_1_unidade));  // open: dp
  Hex_Digit_Display hex_digit_display_3 (.value(separador_x_1_dezena));  // open: dp
  SEPARADOR_X separador_x_1 (.DEZENA(separador_x_1_dezena), .UNIDADE(separador_x_1_unidade), .X(X));
  Hex_Digit_Display hex_digit_display_4 (.value(separador_x_1_unidade));  // open: dp
  _7_Segment_Display u_7_segment_display_1 (
    .g(conversor_segmentos_1_d), .f(conversor_segmentos_1_e), .a(conversor_segmentos_1_f),
    .b(conversor_segmentos_1_g), .e(conversor_segmentos_1_a), .d(conversor_segmentos_1_b),
    .c(conversor_segmentos_1_c));  // open: dp
  CONVERSOR_SEGMENTOS conversor_segmentos_1 (
    .in_1(separador_y_1_dezena), .g(conversor_segmentos_1_g), .f(conversor_segmentos_1_f),
    .e(conversor_segmentos_1_e), .d(conversor_segmentos_1_d), .a(conversor_segmentos_1_a),
    .b(conversor_segmentos_1_b), .c(conversor_segmentos_1_c));  // open: decimal
  _7_Segment_Display u_7_segment_display_2 (
    .g(conversor_segmentos_2_d), .f(conversor_segmentos_2_e), .a(conversor_segmentos_2_f),
    .b(conversor_segmentos_2_g), .e(conversor_segmentos_2_a), .d(conversor_segmentos_2_b),
    .c(conversor_segmentos_2_c));  // open: dp
  CONVERSOR_SEGMENTOS conversor_segmentos_2 (
    .in_1(separador_y_1_unidade), .g(conversor_segmentos_2_g), .f(conversor_segmentos_2_f),
    .e(conversor_segmentos_2_e), .d(conversor_segmentos_2_d), .a(conversor_segmentos_2_a),
    .b(conversor_segmentos_2_b), .c(conversor_segmentos_2_c));  // open: decimal
  CONVERSOR_SEGMENTOS conversor_segmentos_3 (
    .in_1(separador_x_1_dezena), .g(conversor_segmentos_3_g), .f(conversor_segmentos_3_f),
    .e(conversor_segmentos_3_e), .d(conversor_segmentos_3_d), .a(conversor_segmentos_3_a),
    .b(conversor_segmentos_3_b), .c(conversor_segmentos_3_c));  // open: decimal
  _7_Segment_Display u_7_segment_display_3 (
    .g(conversor_segmentos_3_d), .f(conversor_segmentos_3_e), .a(conversor_segmentos_3_f),
    .b(conversor_segmentos_3_g), .e(conversor_segmentos_3_a), .d(conversor_segmentos_3_b),
    .c(conversor_segmentos_3_c));  // open: dp
  _7_Segment_Display u_7_segment_display_4 (
    .g(conversor_segmentos_4_d), .f(conversor_segmentos_4_e), .a(conversor_segmentos_4_f),
    .b(conversor_segmentos_4_g), .e(conversor_segmentos_4_a), .d(conversor_segmentos_4_b),
    .c(conversor_segmentos_4_c));  // open: dp
  CONVERSOR_SEGMENTOS conversor_segmentos_4 (
    .in_1(separador_x_1_unidade), .g(conversor_segmentos_4_g), .f(conversor_segmentos_4_f),
    .e(conversor_segmentos_4_e), .d(conversor_segmentos_4_d), .a(conversor_segmentos_4_a),
    .b(conversor_segmentos_4_b), .c(conversor_segmentos_4_c));  // open: decimal

  // Notes on the sheet:
  //   CARTESIAN GAME
  //   EIXO Y
  //   COORDENADAS
  //   EIXO X
  //   EIXO Y
  //   EIXO X
endmodule

module GRAFICO (
  input  [3:0] Y,
  input  [3:0] X,
  output [14:0] COLUNA_0,
  output [14:0] COLUNA_1,
  output [14:0] COLUNA_2,
  output [14:0] COLUNA_3,
  output [14:0] COLUNA_4,
  output [14:0] COLUNA_5,
  output [14:0] COLUNA_6,
  output [14:0] COLUNA_7,
  output [14:0] COLUNA_8,
  output [14:0] COLUNA_9,
  output [14:0] COLUNA_10,
  output [14:0] COLUNA_11,
  output [14:0] COLUNA_12,
  output [14:0] COLUNA_13,
  output [14:0] COLUNA_14
);

  wire [14:0] dmx_1_s15;

  DMX dmx_1 (
    .\Seleção (Y), .Entrada(1'b1), .S1(dmx_1_s15[14]), .S2(dmx_1_s15[13]), .S3(dmx_1_s15[12]),
    .S4(dmx_1_s15[11]), .S5(dmx_1_s15[10]), .S6(dmx_1_s15[9]), .S7(dmx_1_s15[8]), .S8(dmx_1_s15[7]),
    .S9(dmx_1_s15[6]), .S10(dmx_1_s15[5]), .S11(dmx_1_s15[4]), .S12(dmx_1_s15[3]), .S13(dmx_1_s15[2]),
    .S14(dmx_1_s15[1]), .S15(dmx_1_s15[0]));  // open: s0
  DMX15 dmx15_1 (
    .\Seleção (X), .Entrada(dmx_1_s15), .S1(COLUNA_0), .S2(COLUNA_1), .S3(COLUNA_2), .S4(COLUNA_3),
    .S5(COLUNA_4), .S6(COLUNA_5), .S7(COLUNA_6), .S8(COLUNA_7), .S9(COLUNA_8), .S10(COLUNA_9),
    .S11(COLUNA_10), .S12(COLUNA_11), .S13(COLUNA_12), .S14(COLUNA_13), .S15(COLUNA_14));  // open: s0
endmodule

// X
module SEPARADOR_X (
  input  [3:0] X,
  output [3:0] DEZENA,
  output [3:0] UNIDADE
);

  wire comparador_1_out_3;
  wire [3:0] subtrator_1_out_3, subtrator_2_out_3;

  MUX mux_1 (.in_1(4'b0000), .in_2(4'b0001), .in_3(comparador_1_out_3), .out_4(DEZENA));
  SUBTRATOR subtrator_1 (.in_1(X), .in_2(4'b0001), .out_3(subtrator_1_out_3));
  SUBTRATOR subtrator_2 (.in_1(subtrator_1_out_3), .in_2(4'b1010), .out_3(subtrator_2_out_3));
  COMPARADOR comparador_1 (
    .\a__número_anterior (subtrator_1_out_3), .\b__número_posterior (4'b1001), .out_3(comparador_1_out_3));  // open: out_4, out_5
  MUX mux_2 (.in_1(subtrator_1_out_3), .in_2(subtrator_2_out_3), .in_3(comparador_1_out_3), .out_4(UNIDADE));
endmodule

// Y
module SEPARADOR_Y (
  input  [3:0] Y,
  output [3:0] DEZENA,
  output [3:0] UNIDADE
);

  wire comparador_1_out_3;
  wire [3:0] subtrator_1_out_3, subtrator_2_out_3;

  MUX mux_1 (.in_1(4'b0000), .in_2(4'b0001), .in_3(comparador_1_out_3), .out_4(DEZENA));
  SUBTRATOR subtrator_1 (.in_1(4'b1111), .in_2(Y), .out_3(subtrator_1_out_3));
  COMPARADOR comparador_1 (
    .\a__número_anterior (subtrator_1_out_3), .\b__número_posterior (4'b1001), .out_3(comparador_1_out_3));  // open: out_4, out_5
  SUBTRATOR subtrator_2 (.in_1(subtrator_1_out_3), .in_2(4'b1010), .out_3(subtrator_2_out_3));
  MUX mux_2 (.in_1(subtrator_1_out_3), .in_2(subtrator_2_out_3), .in_3(comparador_1_out_3), .out_4(UNIDADE));
endmodule

// DMX-E1
module DMX (
  input  [3:0] \Seleção ,
  input  Entrada,
  output s0,
  output S1,
  output S2,
  output S3,
  output S4,
  output S5,
  output S6,
  output S7,
  output S8,
  output S9,
  output S10,
  output S11,
  output S12,
  output S13,
  output S14,
  output S15
);

  wire not_1_out, not_2_out, not_3_out, not_4_out;

  not not_1 (not_1_out, \Seleção [0]);
  not not_2 (not_2_out, \Seleção [1]);
  not not_3 (not_3_out, \Seleção [2]);
  not not_4 (not_4_out, \Seleção [3]);
  and and_1 (s0, not_1_out, not_2_out, Entrada, not_3_out, not_4_out);
  and and_2 (S1, \Seleção [0], not_2_out, Entrada, not_3_out, not_4_out);
  and and_3 (S2, not_1_out, \Seleção [1], Entrada, not_3_out, not_4_out);
  and and_4 (S3, \Seleção [0], \Seleção [1], Entrada, not_3_out, not_4_out);
  and and_5 (S4, not_1_out, not_2_out, Entrada, \Seleção [2], not_4_out);
  and and_6 (S5, \Seleção [0], not_2_out, Entrada, \Seleção [2], not_4_out);
  and and_7 (S6, not_1_out, \Seleção [1], Entrada, \Seleção [2], not_4_out);
  and and_8 (S7, \Seleção [0], \Seleção [1], Entrada, \Seleção [2], not_4_out);
  and and_9 (S8, not_1_out, not_2_out, Entrada, not_3_out, \Seleção [3]);
  and and_10 (S9, \Seleção [0], not_2_out, Entrada, not_3_out, \Seleção [3]);
  and and_11 (S10, not_1_out, \Seleção [1], Entrada, not_3_out, \Seleção [3]);
  and and_12 (S11, \Seleção [0], \Seleção [1], Entrada, not_3_out, \Seleção [3]);
  and and_13 (S12, not_1_out, not_2_out, Entrada, \Seleção [2], \Seleção [3]);
  and and_14 (S13, \Seleção [0], not_2_out, Entrada, \Seleção [2], \Seleção [3]);
  and and_15 (S14, not_1_out, \Seleção [1], Entrada, \Seleção [2], \Seleção [3]);
  and and_16 (S15, \Seleção [0], \Seleção [1], Entrada, \Seleção [2], \Seleção [3]);
endmodule

// DMX-E15
module DMX15 (
  input  [3:0] \Seleção ,
  input  [14:0] Entrada,
  output [14:0] s0,
  output [14:0] S1,
  output [14:0] S2,
  output [14:0] S3,
  output [14:0] S4,
  output [14:0] S5,
  output [14:0] S6,
  output [14:0] S7,
  output [14:0] S8,
  output [14:0] S9,
  output [14:0] S10,
  output [14:0] S11,
  output [14:0] S12,
  output [14:0] S13,
  output [14:0] S14,
  output [14:0] S15
);

  wire and_1_out, and_2_out, and_3_out, and_4_out, and_5_out, and_6_out, and_7_out, and_8_out, and_9_out,
       and_10_out, and_11_out, and_12_out, and_13_out, and_14_out, and_15_out, and_16_out, not_1_out,
       not_2_out, not_3_out, not_4_out;

  not not_1 (not_1_out, \Seleção [0]);
  not not_2 (not_2_out, \Seleção [1]);
  not not_3 (not_3_out, \Seleção [2]);
  not not_4 (not_4_out, \Seleção [3]);
  and and_1 (and_1_out, not_1_out, not_2_out, not_3_out, not_4_out);
  and and_2 (and_2_out, \Seleção [0], not_2_out, not_3_out, not_4_out);
  and and_3 (and_3_out, not_1_out, \Seleção [1], not_3_out, not_4_out);
  and and_4 (and_4_out, \Seleção [0], \Seleção [1], not_3_out, not_4_out);
  and and_5 (and_5_out, not_1_out, not_2_out, \Seleção [2], not_4_out);
  and and_6 (and_6_out, \Seleção [0], not_2_out, \Seleção [2], not_4_out);
  and and_7 (and_7_out, not_1_out, \Seleção [1], \Seleção [2], not_4_out);
  and and_8 (and_8_out, \Seleção [0], \Seleção [1], \Seleção [2], not_4_out);
  and and_9 (and_9_out, not_1_out, not_2_out, not_3_out, \Seleção [3]);
  and and_10 (and_10_out, \Seleção [0], not_2_out, not_3_out, \Seleção [3]);
  and and_11 (and_11_out, not_1_out, \Seleção [1], not_3_out, \Seleção [3]);
  and and_12 (and_12_out, \Seleção [0], \Seleção [1], not_3_out, \Seleção [3]);
  and and_13 (and_13_out, not_1_out, not_2_out, \Seleção [2], \Seleção [3]);
  and and_14 (and_14_out, \Seleção [0], not_2_out, \Seleção [2], \Seleção [3]);
  and and_15 (and_15_out, not_1_out, \Seleção [1], \Seleção [2], \Seleção [3]);
  and and_16 (and_16_out, \Seleção [0], \Seleção [1], \Seleção [2], \Seleção [3]);
  MUX15 mux15_1 (.in_1({15{1'b0}}), .in_2(Entrada), .in_3(and_1_out), .out_4(s0));
  MUX15 mux15_2 (.in_1({15{1'b0}}), .in_2(Entrada), .in_3(and_2_out), .out_4(S1));
  MUX15 mux15_3 (.in_1({15{1'b0}}), .in_2(Entrada), .in_3(and_3_out), .out_4(S2));
  MUX15 mux15_4 (.in_1({15{1'b0}}), .in_2(Entrada), .in_3(and_4_out), .out_4(S3));
  MUX15 mux15_5 (.in_1({15{1'b0}}), .in_2(Entrada), .in_3(and_5_out), .out_4(S4));
  MUX15 mux15_6 (.in_1({15{1'b0}}), .in_2(Entrada), .in_3(and_6_out), .out_4(S5));
  MUX15 mux15_7 (.in_1({15{1'b0}}), .in_2(Entrada), .in_3(and_7_out), .out_4(S6));
  MUX15 mux15_8 (.in_1({15{1'b0}}), .in_2(Entrada), .in_3(and_8_out), .out_4(S7));
  MUX15 mux15_9 (.in_1({15{1'b0}}), .in_2(Entrada), .in_3(and_9_out), .out_4(S8));
  MUX15 mux15_10 (.in_1({15{1'b0}}), .in_2(Entrada), .in_3(and_10_out), .out_4(S9));
  MUX15 mux15_11 (.in_1({15{1'b0}}), .in_2(Entrada), .in_3(and_11_out), .out_4(S10));
  MUX15 mux15_12 (.in_1({15{1'b0}}), .in_2(Entrada), .in_3(and_12_out), .out_4(S11));
  MUX15 mux15_13 (.in_1({15{1'b0}}), .in_2(Entrada), .in_3(and_13_out), .out_4(S12));
  MUX15 mux15_14 (.in_1({15{1'b0}}), .in_2(Entrada), .in_3(and_14_out), .out_4(S13));
  MUX15 mux15_15 (.in_1({15{1'b0}}), .in_2(Entrada), .in_3(and_15_out), .out_4(S14));
  MUX15 mux15_16 (.in_1({15{1'b0}}), .in_2(Entrada), .in_3(and_16_out), .out_4(S15));
endmodule

// M4
module MUX (
  input  [3:0] in_1,
  input  [3:0] in_2,
  input  in_3,
  output [3:0] out_4
);

  wire and_1_out, and_2_out, and_3_out, and_4_out, and_5_out, and_6_out, and_7_out, and_8_out, not_1_out,
       not_2_out, not_3_out, not_4_out;

  not not_1 (not_1_out, in_3);
  not not_2 (not_2_out, in_3);
  not not_3 (not_3_out, in_3);
  not not_4 (not_4_out, in_3);
  and and_1 (and_1_out, in_1[0], not_1_out);
  and and_2 (and_2_out, in_2[0], in_3);
  and and_3 (and_3_out, in_1[1], not_2_out);
  and and_4 (and_4_out, in_2[1], in_3);
  and and_5 (and_5_out, in_1[2], not_3_out);
  and and_6 (and_6_out, in_2[2], in_3);
  and and_7 (and_7_out, in_1[3], not_4_out);
  and and_8 (and_8_out, in_2[3], in_3);
  or or_1 (out_4[0], and_1_out, and_2_out);
  or or_2 (out_4[1], and_3_out, and_4_out);
  or or_3 (out_4[2], and_5_out, and_6_out);
  or or_4 (out_4[3], and_7_out, and_8_out);
endmodule

// M15
module MUX15 (
  input  [14:0] in_1,
  input  [14:0] in_2,
  input  in_3,
  output [14:0] out_4
);

  wire and_1_out, and_2_out, and_3_out, and_4_out, and_5_out, and_6_out, not_1_out, not_2_out, not_3_out;

  not not_1 (not_1_out, in_3);
  not not_2 (not_2_out, in_3);
  not not_3 (not_3_out, in_3);
  MUX mux_1 (.in_1(in_1[6:3]), .in_2(in_2[6:3]), .in_3(in_3), .out_4(out_4[6:3]));
  MUX mux_2 (.in_1(in_1[10:7]), .in_2(in_2[10:7]), .in_3(in_3), .out_4(out_4[10:7]));
  MUX mux_3 (.in_1(in_1[14:11]), .in_2(in_2[14:11]), .in_3(in_3), .out_4(out_4[14:11]));
  and and_1 (and_1_out, in_1[0], not_1_out);
  and and_2 (and_2_out, in_2[0], in_3);
  and and_3 (and_3_out, in_1[1], not_2_out);
  and and_4 (and_4_out, in_2[1], in_3);
  and and_5 (and_5_out, in_1[2], not_3_out);
  and and_6 (and_6_out, in_2[2], in_3);
  or or_1 (out_4[0], and_1_out, and_2_out);
  or or_2 (out_4[1], and_3_out, and_4_out);
  or or_3 (out_4[2], and_5_out, and_6_out);
endmodule

module FA (
  input  A,
  input  B,
  input  Cin,
  output S,
  output Cout
);

  wire and_1_out, and_2_out, and_3_out, xor_1_out;

  xor xor_1 (xor_1_out, B, Cin);
  and and_1 (and_1_out, B, Cin);
  and and_2 (and_2_out, B, A);
  and and_3 (and_3_out, Cin, A);
  xor xor_2 (S, A, xor_1_out);
  or or_1 (Cout, and_1_out, and_2_out, and_3_out);
endmodule

module COMPLEMENTO_2 (
  input  [3:0] in,
  output [3:0] out
);

  wire [3:0] not_1_out;

  not not_1 (not_1_out[0], in[0]);
  not not_2 (not_1_out[1], in[1]);
  not not_3 (not_1_out[2], in[2]);
  not not_4 (not_1_out[3], in[3]);
  SOMADOR somador_1 (.in_1(not_1_out), .in_2(4'b0001), .out_3(out));
endmodule

// +
module SOMADOR (
  input  [3:0] in_1,
  input  [3:0] in_2,
  output [3:0] out_3
);

  wire fa_1_cout, fa_2_cout, fa_3_cout;

  FA fa_1 (.A(in_1[0]), .B(in_2[0]), .Cin(1'b0), .S(out_3[0]), .Cout(fa_1_cout));
  FA fa_2 (.A(in_1[1]), .B(in_2[1]), .Cin(fa_1_cout), .S(out_3[1]), .Cout(fa_2_cout));
  FA fa_3 (.A(in_1[2]), .B(in_2[2]), .Cin(fa_2_cout), .S(out_3[2]), .Cout(fa_3_cout));
  FA fa_4 (.A(in_1[3]), .B(in_2[3]), .Cin(fa_3_cout), .S(out_3[3]));  // open: Cout

  // Notes on the sheet:
  //   +
  //   =
endmodule

// -
module SUBTRATOR (
  input  [3:0] in_1,
  input  [3:0] in_2,
  output [3:0] out_3
);

  wire [3:0] complemento_2_1_out;

  SOMADOR somador_1 (.in_1(in_1), .in_2(complemento_2_1_out), .out_3(out_3));
  COMPLEMENTO_2 complemento_2_1 (.in(in_2), .out(complemento_2_1_out));

  // Notes on the sheet:
  //   -
  //   =
endmodule

module CONVERSOR_GRAFICO (
  input  [3:0] in_1,
  output [3:0] out_2
);

  wire [3:0] subtrator_1_out_3;

  SUBTRATOR subtrator_1 (.in_1(4'b1111), .in_2(in_1), .out_3(subtrator_1_out_3));
  SOMADOR somador_1 (.in_1(subtrator_1_out_3), .in_2(4'b0001), .out_3(out_2));
endmodule

// CONV
module CONVERSOR_SEGMENTOS (
  input  [3:0] in_1,
  output g,
  output f,
  output e,
  output d,
  output a,
  output b,
  output c,
  output decimal
);

  wire and_1_out, and_2_out, and_3_out, and_4_out, and_5_out, and_6_out, and_7_out, and_8_out, and_9_out,
       and_10_out, and_11_out, and_12_out, and_13_out, and_14_out, and_15_out, and_16_out, and_17_out,
       and_18_out, and_19_out, and_20_out, and_21_out, and_22_out, and_23_out, and_24_out, and_25_out,
       and_26_out, and_27_out, and_28_out, and_29_out, and_30_out, and_31_out, and_32_out, and_33_out,
       and_34_out, and_35_out, and_36_out, not_1_out, not_2_out, not_3_out, not_4_out;

  not not_1 (not_1_out, in_1[0]);
  not not_2 (not_2_out, in_1[1]);
  not not_3 (not_3_out, in_1[2]);
  not not_4 (not_4_out, in_1[3]);
  and and_1 (and_1_out, not_1_out, not_2_out, not_4_out);
  and and_2 (and_2_out, in_1[0], in_1[1], not_4_out);
  and and_3 (and_3_out, in_1[0], not_2_out, in_1[3]);
  and and_4 (and_4_out, not_3_out, not_4_out);
  and and_5 (and_5_out, not_1_out, not_3_out);
  and and_6 (and_6_out, in_1[1], in_1[2]);
  and and_7 (and_7_out, in_1[1], not_4_out);
  and and_8 (and_8_out, in_1[0], in_1[2], not_4_out);
  and and_9 (and_9_out, not_2_out, not_3_out, in_1[3]);
  and and_10 (and_10_out, not_1_out, not_2_out, in_1[3]);
  and and_11 (and_11_out, not_1_out, not_3_out);
  and and_12 (and_12_out, in_1[1], in_1[3]);
  and and_13 (and_13_out, not_3_out, in_1[3]);
  and and_14 (and_14_out, not_2_out, in_1[2], not_4_out);
  and and_15 (and_15_out, not_1_out, in_1[1], in_1[2]);
  and and_16 (and_16_out, not_1_out, not_2_out);
  and and_17 (and_17_out, not_3_out, in_1[3]);
  and and_18 (and_18_out, not_1_out, in_1[1]);
  and and_19 (and_19_out, in_1[1], not_3_out, not_4_out);
  and and_20 (and_20_out, not_2_out, in_1[2], not_4_out);
  and and_21 (and_21_out, in_1[0], in_1[3]);
  and and_22 (and_22_out, not_1_out, not_2_out, not_3_out);
  and and_23 (and_23_out, in_1[2], in_1[3]);
  and and_24 (and_24_out, not_1_out, in_1[1]);
  and and_25 (and_25_out, in_1[1], in_1[3]);
  and and_26 (and_26_out, not_1_out, in_1[1], in_1[2]);
  and and_27 (and_27_out, in_1[0], not_2_out, in_1[2]);
  and and_28 (and_28_out, not_2_out, in_1[2], in_1[3]);
  and and_29 (and_29_out, not_1_out, in_1[1], not_4_out);
  and and_30 (and_30_out, in_1[0], in_1[1], not_3_out);
  and and_31 (and_31_out, not_1_out, not_2_out, not_3_out);
  and and_32 (and_32_out, not_2_out, not_4_out);
  and and_33 (and_33_out, in_1[0], not_4_out);
  and and_34 (and_34_out, not_4_out, in_1[2]);
  and and_35 (and_35_out, in_1[0], not_2_out);
  and and_36 (and_36_out, not_3_out, in_1[3]);
  or or_1 (g, and_1_out, and_2_out, and_3_out, and_4_out, and_5_out);
  or or_2 (f, and_6_out, and_7_out, and_8_out, and_9_out, and_10_out, and_11_out);
  or or_3 (e, and_12_out, and_13_out, and_14_out, and_15_out, and_16_out);
  or or_4 (d, and_17_out, and_18_out, and_19_out, and_20_out, and_21_out);
  or or_5 (a, and_22_out, and_23_out, and_24_out, and_25_out);
  or or_6 (b, and_26_out, and_27_out, and_28_out, and_29_out, and_30_out, and_31_out);
  or or_7 (c, and_32_out, and_33_out, and_34_out, and_35_out, and_36_out);

  assign decimal = 1'b0;
endmodule

// >
module MAIOR (
  input  in_1,
  input  in_2,
  output out_3
);

  wire not_1_out;

  and and_1 (out_3, in_1, not_1_out);
  not not_1 (not_1_out, in_2);
endmodule

// <
module MENOR (
  input  in_1,
  input  in_2,
  output out_3
);

  wire not_1_out;

  not not_1 (not_1_out, in_1);
  and and_1 (out_3, not_1_out, in_2);
endmodule

// =
module IGUAL (
  input  in_1,
  input  in_2,
  output out_3
);

  xnor xnor_1 (out_3, in_1, in_2);
endmodule

module COMPARADOR (
  input  [3:0] \a__número_anterior ,
  input  [3:0] \b__número_posterior ,
  output out_3,
  output out_4,
  output out_5
);

  wire and_1_out, and_2_out, and_4_out, and_5_out, and_6_out, and_7_out, igual_1_out_3, igual_2_out_3,
       igual_3_out_3, igual_4_out_3, maior_1_out_3, maior_2_out_3, maior_3_out_3, maior_4_out_3,
       menor_1_out_3, menor_2_out_3, menor_3_out_3, menor_4_out_3, xnor_1_out, xnor_2_out, xnor_3_out,
       xnor_4_out, xnor_5_out, xnor_6_out;

  MAIOR maior_1 (.in_1(\a__número_anterior [3]), .in_2(\b__número_posterior [3]), .out_3(maior_1_out_3));
  MAIOR maior_2 (.in_1(\a__número_anterior [2]), .in_2(\b__número_posterior [2]), .out_3(maior_2_out_3));
  MAIOR maior_3 (.in_1(\a__número_anterior [1]), .in_2(\b__número_posterior [1]), .out_3(maior_3_out_3));
  MAIOR maior_4 (.in_1(\a__número_anterior [0]), .in_2(\b__número_posterior [0]), .out_3(maior_4_out_3));
  IGUAL igual_1 (.in_1(\b__número_posterior [3]), .in_2(\a__número_anterior [3]), .out_3(igual_1_out_3));
  IGUAL igual_2 (.in_1(\b__número_posterior [2]), .in_2(\a__número_anterior [2]), .out_3(igual_2_out_3));
  IGUAL igual_3 (.in_1(\b__número_posterior [1]), .in_2(\a__número_anterior [1]), .out_3(igual_3_out_3));
  IGUAL igual_4 (.in_1(\b__número_posterior [0]), .in_2(\a__número_anterior [0]), .out_3(igual_4_out_3));
  MENOR menor_1 (.in_1(\a__número_anterior [3]), .in_2(\b__número_posterior [3]), .out_3(menor_1_out_3));
  MENOR menor_2 (.in_1(\a__número_anterior [2]), .in_2(\b__número_posterior [2]), .out_3(menor_2_out_3));
  MENOR menor_3 (.in_1(\a__número_anterior [1]), .in_2(\b__número_posterior [1]), .out_3(menor_3_out_3));
  MENOR menor_4 (.in_1(\a__número_anterior [0]), .in_2(\b__número_posterior [0]), .out_3(menor_4_out_3));
  xnor xnor_1 (xnor_1_out, \a__número_anterior [3], \b__número_posterior [3]);
  xnor xnor_2 (xnor_2_out, \b__número_posterior [3], \a__número_anterior [3]);
  xnor xnor_3 (xnor_3_out, \a__número_anterior [2], \b__número_posterior [2]);
  xnor xnor_4 (xnor_4_out, \a__número_anterior [2], \b__número_posterior [2]);
  and and_1 (and_1_out, maior_2_out_3, xnor_1_out);
  xnor xnor_5 (xnor_5_out, \a__número_anterior [1], \b__número_posterior [1]);
  xnor xnor_6 (xnor_6_out, \a__número_anterior [1], \b__número_posterior [1]);
  and and_2 (and_2_out, maior_3_out_3, xnor_1_out, xnor_3_out);
  and and_3 (out_4, igual_1_out_3, igual_2_out_3, igual_3_out_3, igual_4_out_3);
  and and_4 (and_4_out, menor_2_out_3, xnor_2_out);
  and and_5 (and_5_out, xnor_1_out, maior_4_out_3, xnor_5_out, xnor_3_out);
  and and_6 (and_6_out, menor_3_out_3, xnor_2_out, xnor_4_out);
  or or_1 (out_3, maior_1_out_3, and_1_out, and_2_out, and_5_out);
  or or_2 (out_5, menor_1_out_3, and_4_out, and_6_out, and_7_out);
  and and_7 (and_7_out, xnor_4_out, menor_4_out_3, xnor_6_out, xnor_2_out);
endmodule
