// Logisim project projeto1.circ as structural Verilog: 25 circuits, main circuit main
module main (
  output [3:0] Y,
  output [3:0] X
);

  wire conversor_segmentos_1_a, conversor_segmentos_1_b, conversor_segmentos_1_c, conversor_segmentos_1_d,
       conversor_segmentos_1_e, conversor_segmentos_1_f, conversor_segmentos_1_g, conversor_segmentos_2_a,
       conversor_segmentos_2_b, conversor_segmentos_2_c, conversor_segmentos_2_d, conversor_segmentos_2_e,
       conversor_segmentos_2_f, conversor_segmentos_2_g, conversor_segmentos_3_a, conversor_segmentos_3_b,
       conversor_segmentos_3_c, conversor_segmentos_3_d, conversor_segmentos_3_e, conversor_segmentos_3_f,
       conversor_segmentos_3_g, conversor_segmentos_4_a, conversor_segmentos_4_b, conversor_segmentos_4_c,
       conversor_segmentos_4_d, conversor_segmentos_4_e, conversor_segmentos_4_f, conversor_segmentos_4_g;
  wire [3:0] separador_x_1_dezena, separador_x_1_unidade, separador_y_1_dezena, separador_y_1_unidade;
  wire [14:0] grafico_1_coluna_0, grafico_1_coluna_1, grafico_1_coluna_2, grafico_1_coluna_3,
       grafico_1_coluna_4, grafico_1_coluna_5, grafico_1_coluna_6, grafico_1_coluna_7, grafico_1_coluna_8,
       grafico_1_coluna_9, grafico_1_coluna_10, grafico_1_coluna_11, grafico_1_coluna_12,
       grafico_1_coluna_13, grafico_1_coluna_14;

  DotMatrix #(.matrixcols(15), .matrixrows(15)) dotmatrix_1 (
    .col0(grafico_1_coluna_0), .col1(grafico_1_coluna_1), .col2(grafico_1_coluna_2),
    .col3(grafico_1_coluna_3), .col4(grafico_1_coluna_4), .col5(grafico_1_coluna_5),
    .col6(grafico_1_coluna_6), .col7(grafico_1_coluna_7), .col8(grafico_1_coluna_8),
    .col9(grafico_1_coluna_9), .col10(grafico_1_coluna_10), .col11(grafico_1_coluna_11),
    .col12(grafico_1_coluna_12), .col13(grafico_1_coluna_13), .col14(grafico_1_coluna_14));
  GRAFICO grafico_1 (
    .COLUNA_0(grafico_1_coluna_0), .COLUNA_1(grafico_1_coluna_1), .COLUNA_2(grafico_1_coluna_2),
    .COLUNA_3(grafico_1_coluna_3), .COLUNA_4(grafico_1_coluna_4), .COLUNA_5(grafico_1_coluna_5),
    .COLUNA_6(grafico_1_coluna_6), .COLUNA_7(grafico_1_coluna_7), .COLUNA_8(grafico_1_coluna_8),
    .COLUNA_9(grafico_1_coluna_9), .COLUNA_10(grafico_1_coluna_10), .COLUNA_11(grafico_1_coluna_11),
    .COLUNA_12(grafico_1_coluna_12), .COLUNA_13(grafico_1_coluna_13), .COLUNA_14(grafico_1_coluna_14), .X(X),
    .Y(Y));
  Joystick joystick_1 (.x(X), .y(Y));
  Hex_Digit_Display hex_digit_display_1 (.value(separador_y_1_unidade));  // open: dp
  Hex_Digit_Display hex_digit_display_2 (.value(separador_y_1_dezena));  // open: dp
  SEPARADOR_Y separador_y_1 (.DEZENA(separador_y_1_dezena), .UNIDADE(separador_y_1_unidade), .Y(Y));
  Hex_Digit_Display hex_digit_display_3 (.value(separador_x_1_unidade));  // open: dp
  Hex_Digit_Display hex_digit_display_4 (.value(separador_x_1_dezena));  // open: dp
  SEPARADOR_X separador_x_1 (.DEZENA(separador_x_1_dezena), .UNIDADE(separador_x_1_unidade), .X(X));
  CONVERSOR_SEGMENTOS conversor_segmentos_1 (
    .f(conversor_segmentos_1_f), .e(conversor_segmentos_1_e), .d(conversor_segmentos_1_d),
    .a(conversor_segmentos_1_a), .b(conversor_segmentos_1_b), .c(conversor_segmentos_1_c),
    .in_1(separador_y_1_dezena), .g(conversor_segmentos_1_g));  // open: decimal
  _7_Segment_Display u_7_segment_display_1 (
    .g(conversor_segmentos_1_d), .f(conversor_segmentos_1_e), .a(conversor_segmentos_1_f),
    .b(conversor_segmentos_1_g), .e(conversor_segmentos_1_a), .d(conversor_segmentos_1_b),
    .c(conversor_segmentos_1_c));  // open: dp
  _7_Segment_Display u_7_segment_display_2 (
    .g(conversor_segmentos_2_d), .f(conversor_segmentos_2_e), .a(conversor_segmentos_2_f),
    .b(conversor_segmentos_2_g), .e(conversor_segmentos_2_a), .d(conversor_segmentos_2_b),
    .c(conversor_segmentos_2_c));  // open: dp
  CONVERSOR_SEGMENTOS conversor_segmentos_2 (
    .f(conversor_segmentos_2_f), .e(conversor_segmentos_2_e), .d(conversor_segmentos_2_d),
    .a(conversor_segmentos_2_a), .b(conversor_segmentos_2_b), .c(conversor_segmentos_2_c),
    .in_1(separador_y_1_unidade), .g(conversor_segmentos_2_g));  // open: decimal
  CONVERSOR_SEGMENTOS conversor_segmentos_3 (
    .f(conversor_segmentos_3_f), .e(conversor_segmentos_3_e), .d(conversor_segmentos_3_d),
    .a(conversor_segmentos_3_a), .b(conversor_segmentos_3_b), .c(conversor_segmentos_3_c),
    .in_1(separador_x_1_dezena), .g(conversor_segmentos_3_g));  // open: decimal
  _7_Segment_Display u_7_segment_display_3 (
    .g(conversor_segmentos_3_d), .f(conversor_segmentos_3_e), .a(conversor_segmentos_3_f),
    .b(conversor_segmentos_3_g), .e(conversor_segmentos_3_a), .d(conversor_segmentos_3_b),
    .c(conversor_segmentos_3_c));  // open: dp
  _7_Segment_Display u_7_segment_display_4 (
    .g(conversor_segmentos_4_d), .f(conversor_segmentos_4_e), .a(conversor_segmentos_4_f),
    .b(conversor_segmentos_4_g), .e(conversor_segmentos_4_a), .d(conversor_segmentos_4_b),
    .c(conversor_segmentos_4_c));  // open: dp
  CONVERSOR_SEGMENTOS conversor_segmentos_4 (
    .f(conversor_segmentos_4_f), .e(conversor_segmentos_4_e), .d(conversor_segmentos_4_d),
    .a(conversor_segmentos_4_a), .b(conversor_segmentos_4_b), .c(conversor_segmentos_4_c),
    .in_1(separador_x_1_unidade), .g(conversor_segmentos_4_g));  // open: decimal

  // Notes on the sheet:
  //   CARTESIAN GAME
  //   EIXO Y
  //   COORDENADAS
  //   EIXO X
  //   POR CONTA DO TAMANHO DO PROJETO OU DA QUANTIDADE DE SUBCIRCUITOS É COMUM ALGUNS COMPONENTES FALHAREM!
  //   MUITAS PARTES VOLTAM AO NORMAL QUANDO ABRE NOVAMENTE O PROJETO OU COLA NOVAMENTE O CIRCUITO COM PROBLEMA
  //   EIXO Y
  //   EIXO X
endmodule

module GRAFICO (
  input  [3:0] Y,
  input  [3:0] X,
  output [14:0] COLUNA_0,
  output [14:0] COLUNA_1,
  output [14:0] COLUNA_2,
  output [14:0] COLUNA_3,
  output [14:0] COLUNA_4,
  output [14:0] COLUNA_5,
  output [14:0] COLUNA_6,
  output [14:0] COLUNA_7,
  output [14:0] COLUNA_8,
  output [14:0] COLUNA_9,
  output [14:0] COLUNA_10,
  output [14:0] COLUNA_11,
  output [14:0] COLUNA_12,
  output [14:0] COLUNA_13,
  output [14:0] COLUNA_14
);

  wire [14:0] dmx_1_s15;

  DMX dmx_1 (
    .\Seleção (Y), .Entrada(1'b1), .S1(dmx_1_s15[14]), .S2(dmx_1_s15[13]), .S3(dmx_1_s15[12]),
    .S4(dmx_1_s15[11]), .S5(dmx_1_s15[10]), .S6(dmx_1_s15[9]), .S7(dmx_1_s15[8]), .S8(dmx_1_s15[7]),
    .S9(dmx_1_s15[6]), .S10(dmx_1_s15[5]), .S11(dmx_1_s15[4]), .S12(dmx_1_s15[3]), .S13(dmx_1_s15[2]),
    .S14(dmx_1_s15[1]), .S15(dmx_1_s15[0]));  // open: s0
  DMX15 dmx15_1 (
    .\Seleção (X), .Entrada(dmx_1_s15), .S1(COLUNA_0), .S2(COLUNA_1), .S3(COLUNA_2), .S4(COLUNA_3),
    .S5(COLUNA_4), .S6(COLUNA_5), .S7(COLUNA_6), .S8(COLUNA_7), .S9(COLUNA_8), .S10(COLUNA_9),
    .S11(COLUNA_10), .S12(COLUNA_11), .S13(COLUNA_12), .S14(COLUNA_13), .S15(COLUNA_14));  // open: s0
endmodule

// X
module SEPARADOR_X (
  input  [3:0] X,
  output [3:0] DEZENA,
  output [3:0] UNIDADE
);

  wire comparador_1_out_3;
  wire [3:0] subtrator_1_out_3, subtrator_2_out_3;

  MUX mux_1 (.in_1(4'b0000), .in_2(4'b0001), .in_3(comparador_1_out_3), .out_4(DEZENA));
  SUBTRATOR subtrator_1 (.in_1(X), .in_2(4'b0001), .out_3(subtrator_1_out_3));
  SUBTRATOR subtrator_2 (.in_1(subtrator_1_out_3), .in_2(4'b1010), .out_3(subtrator_2_out_3));
  COMPARADOR comparador_1 (
    .\a__número_anterior (subtrator_1_out_3), .\b__número_posterior (4'b1001), .out_3(comparador_1_out_3));  // open: out_4, out_5
  MUX mux_2 (.in_1(subtrator_1_out_3), .in_2(subtrator_2_out_3), .in_3(comparador_1_out_3), .out_4(UNIDADE));
endmodule

// Y
module SEPARADOR_Y (
  input  [3:0] Y,
  output [3:0] DEZENA,
  output [3:0] UNIDADE
);

  wire comparador_1_out_3;
  wire [3:0] subtrator_1_out_3, subtrator_2_out_3;

  MUX mux_1 (.in_1(4'b0000), .in_2(4'b0001), .in_3(comparador_1_out_3), .out_4(DEZENA));
  SUBTRATOR subtrator_1 (.in_1(4'b1111), .in_2(Y), .out_3(subtrator_1_out_3));
  COMPARADOR comparador_1 (
    .\a__número_anterior (subtrator_1_out_3), .\b__número_posterior (4'b1001), .out_3(comparador_1_out_3));  // open: out_4, out_5
  SUBTRATOR subtrator_2 (.in_1(subtrator_1_out_3), .in_2(4'b1010), .out_3(subtrator_2_out_3));
  MUX mux_2 (.in_1(subtrator_1_out_3), .in_2(subtrator_2_out_3), .in_3(comparador_1_out_3), .out_4(UNIDADE));
endmodule

// DMX-E1
module DMX (
  input  [3:0] \Seleção ,
  input  Entrada,
  output s0,
  output S1,
  output S2,
  output S3,
  output S4,
  output S5,
  output S6,
  output S7,
  output S8,
  output S9,
  output S10,
  output S11,
  output S12,
  output S13,
  output S14,
  output S15
);

  wire not_1_out, not_2_out, not_3_out, not_4_out;

  not not_1 (not_1_out, \Seleção [0]);
  not not_2 (not_2_out, \Seleção [1]);
  not not_3 (not_3_out, \Seleção [2]);
  not not_4 (not_4_out, \Seleção [3]);
  and and_1 (s0, not_1_out, not_2_out, Entrada, not_3_out, not_4_out);
  and and_2 (S1, \Seleção [0], not_2_out, Entrada, not_3_out, not_4_out);
  and and_3 (S2, not_1_out, \Seleção [1], Entrada, not_3_out, not_4_out);
  and and_4 (S3, \Seleção [0], \Seleção [1], Entrada, not_3_out, not_4_out);
  and and_5 (S4, not_1_out, not_2_out, Entrada, \Seleção [2], not_4_out);
  and and_6 (S5, \Seleção [0], not_2_out, Entrada, \Seleção [2], not_4_out);
  and and_7 (S6, not_1_out, \Seleção [1], Entrada, \Seleção [2], not_4_out);
  and and_8 (S7, \Seleção [0], \Seleção [1], Entrada, \Seleção [2], not_4_out);
  and and_9 (S8, not_1_out, not_2_out, Entrada, not_3_out, \Seleção [3]);
  and and_10 (S9, \Seleção [0], not_2_out, Entrada, not_3_out, \Seleção [3]);
  and and_11 (S10, not_1_out, \Seleção [1], Entrada, not_3_out, \Seleção [3]);
  and and_12 (S11, \Seleção [0], \Seleção [1], Entrada, not_3_out, \Seleção [3]);
  and and_13 (S12, not_1_out, not_2_out, Entrada, \Seleção [2], \Seleção [3]);
  and and_14 (S13, \Seleção [0], not_2_out, Entrada, \Seleção [2], \Seleção [3]);
  and and_15 (S14, not_1_out, \Seleção [1], Entrada, \Seleção [2], \Seleção [3]);
  and and_16 (S15, \Seleção [0], \Seleção [1], Entrada, \Seleção [2], \Seleção [3]);
endmodule

// DMX-E15
module DMX15 (
  input  [3:0] \Seleção ,
  input  [14:0] Entrada,
  output [14:0] s0,
  output [14:0] S1,
  output [14:0] S2,
  output [14:0] S3,
  output [14:0] S4,
  output [14:0] S5,
  output [14:0] S6,
  output [14:0] S7,
  output [14:0] S8,
  output [14:0] S9,
  output [14:0] S10,
  output [14:0] S11,
  output [14:0] S12,
  output [14:0] S13,
  output [14:0] S14,
  output [14:0] S15
);

  wire and_1_out, and_2_out, and_3_out, and_4_out, and_5_out, and_6_out, and_7_out, and_8_out, and_9_out,
       and_10_out, and_11_out, and_12_out, and_13_out, and_14_out, and_15_out, and_16_out, not_1_out,
       not_2_out, not_3_out, not_4_out;

  not not_1 (not_1_out, \Seleção [0]);
  not not_2 (not_2_out, \Seleção [1]);
  not not_3 (not_3_out, \Seleção [2]);
  not not_4 (not_4_out, \Seleção [3]);
  and and_1 (and_1_out, not_1_out, not_2_out, not_3_out, not_4_out);
  and and_2 (and_2_out, \Seleção [0], not_2_out, not_3_out, not_4_out);
  and and_3 (and_3_out, not_1_out, \Seleção [1], not_3_out, not_4_out);
  and and_4 (and_4_out, \Seleção [0], \Seleção [1], not_3_out, not_4_out);
  and and_5 (and_5_out, not_1_out, not_2_out, \Seleção [2], not_4_out);
  and and_6 (and_6_out, \Seleção [0], not_2_out, \Seleção [2], not_4_out);
  and and_7 (and_7_out, not_1_out, \Seleção [1], \Seleção [2], not_4_out);
  and and_8 (and_8_out, \Seleção [0], \Seleção [1], \Seleção [2], not_4_out);
  and and_9 (and_9_out, not_1_out, not_2_out, not_3_out, \Seleção [3]);
  and and_10 (and_10_out, \Seleção [0], not_2_out, not_3_out, \Seleção [3]);
  and and_11 (and_11_out, not_1_out, \Seleção [1], not_3_out, \Seleção [3]);
  and and_12 (and_12_out, \Seleção [0], \Seleção [1], not_3_out, \Seleção [3]);
  and and_13 (and_13_out, not_1_out, not_2_out, \Seleção [2], \Seleção [3]);
  and and_14 (and_14_out, \Seleção [0], not_2_out, \Seleção [2], \Seleção [3]);
  and and_15 (and_15_out, not_1_out, \Seleção [1], \Seleção [2], \Seleção [3]);
  and and_16 (and_16_out, \Seleção [0], \Seleção [1], \Seleção [2], \Seleção [3]);
  MUX15 mux15_1 (.in_1({15{1'b0}}), .in_2(Entrada), .in_3(and_1_out), .out_4(s0));
  MUX15 mux15_2 (.in_1({15{1'b0}}), .in_2(Entrada), .in_3(and_2_out), .out_4(S1));
  MUX15 mux15_3 (.in_1({15{1'b0}}), .in_2(Entrada), .in_3(and_3_out), .out_4(S2));
  MUX15 mux15_4 (.in_1({15{1'b0}}), .in_2(Entrada), .in_3(and_4_out), .out_4(S3));
  MUX15 mux15_5 (.in_1({15{1'b0}}), .in_2(Entrada), .in_3(and_5_out), .out_4(S4));
  MUX15 mux15_6 (.in_1({15{1'b0}}), .in_2(Entrada), .in_3(and_6_out), .out_4(S5));
  MUX15 mux15_7 (.in_1({15{1'b0}}), .in_2(Entrada), .in_3(and_7_out), .out_4(S6));
  MUX15 mux15_8 (.in_1({15{1'b0}}), .in_2(Entrada), .in_3(and_8_out), .out_4(S7));
  MUX15 mux15_9 (.in_1({15{1'b0}}), .in_2(Entrada), .in_3(and_9_out), .out_4(S8));
  MUX15 mux15_10 (.in_1({15{1'b0}}), .in_2(Entrada), .in_3(and_10_out), .out_4(S9));
  MUX15 mux15_11 (.in_1({15{1'b0}}), .in_2(Entrada), .in_3(and_11_out), .out_4(S10));
  MUX15 mux15_12 (.in_1({15{1'b0}}), .in_2(Entrada), .in_3(and_12_out), .out_4(S11));
  MUX15 mux15_13 (.in_1({15{1'b0}}), .in_2(Entrada), .in_3(and_13_out), .out_4(S12));
  MUX15 mux15_14 (.in_1({15{1'b0}}), .in_2(Entrada), .in_3(and_14_out), .out_4(S13));
  MUX15 mux15_15 (.in_1({15{1'b0}}), .in_2(Entrada), .in_3(and_15_out), .out_4(S14));
  MUX15 mux15_16 (.in_1({15{1'b0}}), .in_2(Entrada), .in_3(and_16_out), .out_4(S15));
endmodule

// M4
module MUX (
  input  [3:0] in_1,
  input  [3:0] in_2,
  input  in_3,
  output [3:0] out_4
);

  wire and_1_out, and_2_out, and_3_out, and_4_out, and_5_out, and_6_out, and_7_out, and_8_out, not_1_out,
       not_2_out, not_3_out, not_4_out;

  not not_1 (not_1_out, in_3);
  not not_2 (not_2_out, in_3);
  not not_3 (not_3_out, in_3);
  not not_4 (not_4_out, in_3);
  and and_1 (and_1_out, in_1[0], not_1_out);
  and and_2 (and_2_out, in_2[0], in_3);
  and and_3 (and_3_out, in_1[1], not_2_out);
  and and_4 (and_4_out, in_2[1], in_3);
  and and_5 (and_5_out, in_1[2], not_3_out);
  and and_6 (and_6_out, in_2[2], in_3);
  and and_7 (and_7_out, in_1[3], not_4_out);
  and and_8 (and_8_out, in_2[3], in_3);
  or or_1 (out_4[0], and_1_out, and_2_out);
  or or_2 (out_4[1], and_3_out, and_4_out);
  or or_3 (out_4[2], and_5_out, and_6_out);
  or or_4 (out_4[3], and_7_out, and_8_out);
endmodule

// M15
module MUX15 (
  input  [14:0] in_1,
  input  [14:0] in_2,
  input  in_3,
  output [14:0] out_4
);

  wire and_1_out, and_2_out, and_3_out, and_4_out, and_5_out, and_6_out, not_1_out, not_2_out, not_3_out;

  not not_1 (not_1_out, in_3);
  not not_2 (not_2_out, in_3);
  not not_3 (not_3_out, in_3);
  MUX mux_1 (.in_1(in_1[6:3]), .in_2(in_2[6:3]), .in_3(in_3), .out_4(out_4[6:3]));
  MUX mux_2 (.in_1(in_1[10:7]), .in_2(in_2[10:7]), .in_3(in_3), .out_4(out_4[10:7]));
  MUX mux_3 (.in_1(in_1[14:11]), .in_2(in_2[14:11]), .in_3(in_3), .out_4(out_4[14:11]));
  and and_1 (and_1_out, in_1[0], not_1_out);
  and and_2 (and_2_out, in_2[0], in_3);
  and and_3 (and_3_out, in_1[1], not_2_out);
  and and_4 (and_4_out, in_2[1], in_3);
  and and_5 (and_5_out, in_1[2], not_3_out);
  and and_6 (and_6_out, in_2[2], in_3);
  or or_1 (out_4[0], and_1_out, and_2_out);
  or or_2 (out_4[1], and_3_out, and_4_out);
  or or_3 (out_4[2], and_5_out, and_6_out);
endmodule

module FA (
  input  A,
  input  B,
  input  Cin,
  output S,
  output Cout
);

  wire and_1_out, and_2_out, and_3_out, xor_1_out;

  xor xor_1 (xor_1_out, B, Cin);
  and and_1 (and_1_out, B, Cin);
  and and_2 (and_2_out, B, A);
  and and_3 (and_3_out, Cin, A);
  xor xor_2 (S, A, xor_1_out);
  or or_1 (Cout, and_1_out, and_2_out, and_3_out);
endmodule

module COMPLEMENTO_2 (
  input  [3:0] in,
  output [3:0] out
);

  wire [3:0] not_1_out;

  not not_1 (not_1_out[0], in[0]);
  not not_2 (not_1_out[1], in[1]);
  not not_3 (not_1_out[2], in[2]);
  not not_4 (not_1_out[3], in[3]);
  SOMADOR somador_1 (.in_1(not_1_out), .in_2(4'b0001), .out_3(out));
endmodule

// +
module SOMADOR (
  input  [3:0] in_1,
  input  [3:0] in_2,
  output [3:0] out_3
);

  wire fa_1_cout, fa_2_cout, fa_3_cout;

  FA fa_1 (.A(in_1[0]), .B(in_2[0]), .Cin(1'b0), .S(out_3[0]), .Cout(fa_1_cout));
  FA fa_2 (.A(in_1[1]), .B(in_2[1]), .Cin(fa_1_cout), .S(out_3[1]), .Cout(fa_2_cout));
  FA fa_3 (.A(in_1[2]), .B(in_2[2]), .Cin(fa_2_cout), .S(out_3[2]), .Cout(fa_3_cout));
  FA fa_4 (.A(in_1[3]), .B(in_2[3]), .Cin(fa_3_cout), .S(out_3[3]));  // open: Cout

  // Notes on the sheet:
  //   +
  //   =
endmodule

// -
module SUBTRATOR (
  input  [3:0] in_1,
  input  [3:0] in_2,
  output [3:0] out_3
);

  wire [3:0] complemento_2_1_out;

  SOMADOR somador_1 (.in_1(in_1), .in_2(complemento_2_1_out), .out_3(out_3));
  COMPLEMENTO_2 complemento_2_1 (.in(in_2), .out(complemento_2_1_out));

  // Notes on the sheet:
  //   -
  //   =
endmodule

// CONV
module CONVERSOR_SEGMENTOS (
  input  [3:0] in_1,
  output g,
  output f,
  output e,
  output d,
  output a,
  output b,
  output c,
  output decimal
);

  wire and_1_out, and_2_out, and_3_out, and_4_out, and_5_out, and_6_out, and_7_out, and_8_out, and_9_out,
       and_10_out, and_11_out, and_12_out, and_13_out, and_14_out, and_15_out, and_16_out, and_17_out,
       and_18_out, and_19_out, and_20_out, and_21_out, and_22_out, and_23_out, and_24_out, and_25_out,
       and_26_out, and_27_out, and_28_out, and_29_out, and_30_out, and_31_out, and_32_out, and_33_out,
       and_34_out, and_35_out, and_36_out, not_1_out, not_2_out, not_3_out, not_4_out;

  not not_1 (not_1_out, in_1[0]);
  not not_2 (not_2_out, in_1[1]);
  not not_3 (not_3_out, in_1[2]);
  not not_4 (not_4_out, in_1[3]);
  and and_1 (and_1_out, not_1_out, not_2_out, not_4_out);
  and and_2 (and_2_out, in_1[0], in_1[1], not_4_out);
  and and_3 (and_3_out, in_1[0], not_2_out, in_1[3]);
  and and_4 (and_4_out, not_3_out, not_4_out);
  and and_5 (and_5_out, not_1_out, not_3_out);
  and and_6 (and_6_out, in_1[1], in_1[2]);
  and and_7 (and_7_out, in_1[1], not_4_out);
  and and_8 (and_8_out, in_1[0], in_1[2], not_4_out);
  and and_9 (and_9_out, not_2_out, not_3_out, in_1[3]);
  and and_10 (and_10_out, not_1_out, not_2_out, in_1[3]);
  and and_11 (and_11_out, not_1_out, not_3_out);
  and and_12 (and_12_out, in_1[1], in_1[3]);
  and and_13 (and_13_out, not_3_out, in_1[3]);
  and and_14 (and_14_out, not_2_out, in_1[2], not_4_out);
  and and_15 (and_15_out, not_1_out, in_1[1], in_1[2]);
  and and_16 (and_16_out, not_1_out, not_2_out);
  and and_17 (and_17_out, not_3_out, in_1[3]);
  and and_18 (and_18_out, not_1_out, in_1[1]);
  and and_19 (and_19_out, in_1[1], not_3_out, not_4_out);
  and and_20 (and_20_out, not_2_out, in_1[2], not_4_out);
  and and_21 (and_21_out, in_1[0], in_1[3]);
  and and_22 (and_22_out, not_1_out, not_2_out, not_3_out);
  and and_23 (and_23_out, in_1[2], in_1[3]);
  and and_24 (and_24_out, not_1_out, in_1[1]);
  and and_25 (and_25_out, in_1[1], in_1[3]);
  and and_26 (and_26_out, not_1_out, in_1[1], in_1[2]);
  and and_27 (and_27_out, in_1[0], not_2_out, in_1[2]);
  and and_28 (and_28_out, not_2_out, in_1[2], in_1[3]);
  and and_29 (and_29_out, not_1_out, in_1[1], not_4_out);
  and and_30 (and_30_out, in_1[0], in_1[1], not_3_out);
  and and_31 (and_31_out, not_1_out, not_2_out, not_3_out);
  and and_32 (and_32_out, not_2_out, not_4_out);
  and and_33 (and_33_out, in_1[0], not_4_out);
  and and_34 (and_34_out, not_4_out, in_1[2]);
  and and_35 (and_35_out, in_1[0], not_2_out);
  and and_36 (and_36_out, not_3_out, in_1[3]);
  or or_1 (g, and_1_out, and_2_out, and_3_out, and_4_out, and_5_out);
  or or_2 (f, and_6_out, and_7_out, and_8_out, and_9_out, and_10_out, and_11_out);
  or or_3 (e, and_12_out, and_13_out, and_14_out, and_15_out, and_16_out);
  or or_4 (d, and_17_out, and_18_out, and_19_out, and_20_out, and_21_out);
  or or_5 (a, and_22_out, and_23_out, and_24_out, and_25_out);
  or or_6 (b, and_26_out, and_27_out, and_28_out, and_29_out, and_30_out, and_31_out);
  or or_7 (c, and_32_out, and_33_out, and_34_out, and_35_out, and_36_out);

  assign decimal = 1'b0;
endmodule

// >
module MAIOR (
  input  in_1,
  input  in_2,
  output out_3
);

  wire not_1_out;

  and and_1 (out_3, in_1, not_1_out);
  not not_1 (not_1_out, in_2);
endmodule

// <
module MENOR (
  input  in_1,
  input  in_2,
  output out_3
);

  wire not_1_out;

  not not_1 (not_1_out, in_1);
  and and_1 (out_3, not_1_out, in_2);
endmodule

// =
module IGUAL (
  input  in_1,
  input  in_2,
  output out_3
);

  xnor xnor_1 (out_3, in_1, in_2);
endmodule

module COMPARADOR (
  input  [3:0] \a__número_anterior ,
  input  [3:0] \b__número_posterior ,
  output out_3,
  output out_4,
  output out_5
);

  wire and_1_out, and_2_out, and_4_out, and_5_out, and_6_out, and_7_out, igual_1_out_3, igual_2_out_3,
       igual_3_out_3, igual_4_out_3, maior_1_out_3, maior_2_out_3, maior_3_out_3, maior_4_out_3,
       menor_1_out_3, menor_2_out_3, menor_3_out_3, menor_4_out_3, xnor_1_out, xnor_2_out, xnor_3_out,
       xnor_4_out, xnor_5_out, xnor_6_out;

  MAIOR maior_1 (.in_1(\a__número_anterior [3]), .in_2(\b__número_posterior [3]), .out_3(maior_1_out_3));
  MAIOR maior_2 (.in_1(\a__número_anterior [2]), .in_2(\b__número_posterior [2]), .out_3(maior_2_out_3));
  MAIOR maior_3 (.in_1(\a__número_anterior [1]), .in_2(\b__número_posterior [1]), .out_3(maior_3_out_3));
  MAIOR maior_4 (.in_1(\a__número_anterior [0]), .in_2(\b__número_posterior [0]), .out_3(maior_4_out_3));
  IGUAL igual_1 (.in_1(\b__número_posterior [3]), .in_2(\a__número_anterior [3]), .out_3(igual_1_out_3));
  IGUAL igual_2 (.in_1(\b__número_posterior [2]), .in_2(\a__número_anterior [2]), .out_3(igual_2_out_3));
  IGUAL igual_3 (.in_1(\b__número_posterior [1]), .in_2(\a__número_anterior [1]), .out_3(igual_3_out_3));
  IGUAL igual_4 (.in_1(\b__número_posterior [0]), .in_2(\a__número_anterior [0]), .out_3(igual_4_out_3));
  MENOR menor_1 (.in_1(\a__número_anterior [3]), .in_2(\b__número_posterior [3]), .out_3(menor_1_out_3));
  MENOR menor_2 (.in_1(\a__número_anterior [2]), .in_2(\b__número_posterior [2]), .out_3(menor_2_out_3));
  MENOR menor_3 (.in_1(\a__número_anterior [1]), .in_2(\b__número_posterior [1]), .out_3(menor_3_out_3));
  MENOR menor_4 (.in_1(\a__número_anterior [0]), .in_2(\b__número_posterior [0]), .out_3(menor_4_out_3));
  xnor xnor_1 (xnor_1_out, \a__número_anterior [3], \b__número_posterior [3]);
  xnor xnor_2 (xnor_2_out, \b__número_posterior [3], \a__número_anterior [3]);
  xnor xnor_3 (xnor_3_out, \a__número_anterior [2], \b__número_posterior [2]);
  xnor xnor_4 (xnor_4_out, \a__número_anterior [2], \b__número_posterior [2]);
  and and_1 (and_1_out, maior_2_out_3, xnor_1_out);
  xnor xnor_5 (xnor_5_out, \a__número_anterior [1], \b__número_posterior [1]);
  xnor xnor_6 (xnor_6_out, \a__número_anterior [1], \b__número_posterior [1]);
  and and_2 (and_2_out, maior_3_out_3, xnor_1_out, xnor_3_out);
  and and_3 (out_4, igual_1_out_3, igual_2_out_3, igual_3_out_3, igual_4_out_3);
  and and_4 (and_4_out, menor_2_out_3, xnor_2_out);
  and and_5 (and_5_out, xnor_1_out, maior_4_out_3, xnor_5_out, xnor_3_out);
  and and_6 (and_6_out, menor_3_out_3, xnor_2_out, xnor_4_out);
  or or_1 (out_3, maior_1_out_3, and_1_out, and_2_out, and_5_out);
  or or_2 (out_5, menor_1_out_3, and_4_out, and_6_out, and_7_out);
  and and_7 (and_7_out, xnor_4_out, menor_4_out_3, xnor_6_out, xnor_2_out);
endmodule

module TESTE_SEGMENTOS (
);

  wire clock_1_out, conversor_segmentos_1_a, conversor_segmentos_1_b, conversor_segmentos_1_c,
       conversor_segmentos_1_d, conversor_segmentos_1_e, conversor_segmentos_1_f, conversor_segmentos_1_g,
       conversor_segmentos_2_a, conversor_segmentos_2_b, conversor_segmentos_2_c, conversor_segmentos_2_d,
       conversor_segmentos_2_e, conversor_segmentos_2_f, conversor_segmentos_2_g, conversor_segmentos_3_a,
       conversor_segmentos_3_b, conversor_segmentos_3_c, conversor_segmentos_3_d, conversor_segmentos_3_e,
       conversor_segmentos_3_f, conversor_segmentos_3_g, conversor_segmentos_4_a, conversor_segmentos_4_b,
       conversor_segmentos_4_c, conversor_segmentos_4_d, conversor_segmentos_4_e, conversor_segmentos_4_f,
       conversor_segmentos_4_g, conversor_segmentos_5_a, conversor_segmentos_5_b, conversor_segmentos_5_c,
       conversor_segmentos_5_d, conversor_segmentos_5_e, conversor_segmentos_5_f, conversor_segmentos_5_g,
       conversor_segmentos_6_a, conversor_segmentos_6_b, conversor_segmentos_6_c, conversor_segmentos_6_d,
       conversor_segmentos_6_e, conversor_segmentos_6_f, conversor_segmentos_6_g, conversor_segmentos_7_a,
       conversor_segmentos_7_b, conversor_segmentos_7_c, conversor_segmentos_7_d, conversor_segmentos_7_e,
       conversor_segmentos_7_f, conversor_segmentos_7_g, conversor_segmentos_8_a, conversor_segmentos_8_b,
       conversor_segmentos_8_c, conversor_segmentos_8_d, conversor_segmentos_8_e, conversor_segmentos_8_f,
       conversor_segmentos_8_g, conversor_segmentos_9_a, conversor_segmentos_9_b, conversor_segmentos_9_c,
       conversor_segmentos_9_d, conversor_segmentos_9_e, conversor_segmentos_9_f, conversor_segmentos_9_g,
       conversor_segmentos_10_a, conversor_segmentos_10_b, conversor_segmentos_10_c,
       conversor_segmentos_10_d, conversor_segmentos_10_e, conversor_segmentos_10_f,
       conversor_segmentos_10_g, conversor_segmentos_11_a, conversor_segmentos_11_b,
       conversor_segmentos_11_c, conversor_segmentos_11_d, conversor_segmentos_11_e,
       conversor_segmentos_11_f, conversor_segmentos_11_g, conversor_segmentos_12_a,
       conversor_segmentos_12_b, conversor_segmentos_12_c, conversor_segmentos_12_d,
       conversor_segmentos_12_e, conversor_segmentos_12_f, conversor_segmentos_12_g,
       conversor_segmentos_13_a, conversor_segmentos_13_b, conversor_segmentos_13_c,
       conversor_segmentos_13_d, conversor_segmentos_13_e, conversor_segmentos_13_f,
       conversor_segmentos_13_g, conversor_segmentos_14_a, conversor_segmentos_14_b,
       conversor_segmentos_14_c, conversor_segmentos_14_d, conversor_segmentos_14_e,
       conversor_segmentos_14_f, conversor_segmentos_14_g, conversor_segmentos_15_a,
       conversor_segmentos_15_b, conversor_segmentos_15_c, conversor_segmentos_15_d,
       conversor_segmentos_15_e, conversor_segmentos_15_f, conversor_segmentos_15_g,
       conversor_segmentos_16_a, conversor_segmentos_16_b, conversor_segmentos_16_c,
       conversor_segmentos_16_d, conversor_segmentos_16_e, conversor_segmentos_16_f,
       conversor_segmentos_16_g, conversor_segmentos_17_a, conversor_segmentos_17_b,
       conversor_segmentos_17_c, conversor_segmentos_17_d, conversor_segmentos_17_e,
       conversor_segmentos_17_f, conversor_segmentos_17_g;
  wire [3:0] counter_1_q;

  CONVERSOR_SEGMENTOS conversor_segmentos_1 (
    .f(conversor_segmentos_1_f), .e(conversor_segmentos_1_e), .d(conversor_segmentos_1_d),
    .a(conversor_segmentos_1_a), .b(conversor_segmentos_1_b), .c(conversor_segmentos_1_c), .in_1(4'b0000),
    .g(conversor_segmentos_1_g));  // open: decimal
  CONVERSOR_SEGMENTOS conversor_segmentos_2 (
    .f(conversor_segmentos_2_f), .e(conversor_segmentos_2_e), .d(conversor_segmentos_2_d),
    .a(conversor_segmentos_2_a), .b(conversor_segmentos_2_b), .c(conversor_segmentos_2_c), .in_1(4'b0001),
    .g(conversor_segmentos_2_g));  // open: decimal
  CONVERSOR_SEGMENTOS conversor_segmentos_3 (
    .f(conversor_segmentos_3_f), .e(conversor_segmentos_3_e), .d(conversor_segmentos_3_d),
    .a(conversor_segmentos_3_a), .b(conversor_segmentos_3_b), .c(conversor_segmentos_3_c), .in_1(4'b0010),
    .g(conversor_segmentos_3_g));  // open: decimal
  CONVERSOR_SEGMENTOS conversor_segmentos_4 (
    .f(conversor_segmentos_4_f), .e(conversor_segmentos_4_e), .d(conversor_segmentos_4_d),
    .a(conversor_segmentos_4_a), .b(conversor_segmentos_4_b), .c(conversor_segmentos_4_c), .in_1(4'b0011),
    .g(conversor_segmentos_4_g));  // open: decimal
  CONVERSOR_SEGMENTOS conversor_segmentos_5 (
    .f(conversor_segmentos_5_f), .e(conversor_segmentos_5_e), .d(conversor_segmentos_5_d),
    .a(conversor_segmentos_5_a), .b(conversor_segmentos_5_b), .c(conversor_segmentos_5_c), .in_1(4'b0100),
    .g(conversor_segmentos_5_g));  // open: decimal
  CONVERSOR_SEGMENTOS conversor_segmentos_6 (
    .f(conversor_segmentos_6_f), .e(conversor_segmentos_6_e), .d(conversor_segmentos_6_d),
    .a(conversor_segmentos_6_a), .b(conversor_segmentos_6_b), .c(conversor_segmentos_6_c), .in_1(4'b0101),
    .g(conversor_segmentos_6_g));  // open: decimal
  CONVERSOR_SEGMENTOS conversor_segmentos_7 (
    .f(conversor_segmentos_7_f), .e(conversor_segmentos_7_e), .d(conversor_segmentos_7_d),
    .a(conversor_segmentos_7_a), .b(conversor_segmentos_7_b), .c(conversor_segmentos_7_c), .in_1(4'b0110),
    .g(conversor_segmentos_7_g));  // open: decimal
  CONVERSOR_SEGMENTOS conversor_segmentos_8 (
    .f(conversor_segmentos_8_f), .e(conversor_segmentos_8_e), .d(conversor_segmentos_8_d),
    .a(conversor_segmentos_8_a), .b(conversor_segmentos_8_b), .c(conversor_segmentos_8_c), .in_1(4'b0111),
    .g(conversor_segmentos_8_g));  // open: decimal
  CONVERSOR_SEGMENTOS conversor_segmentos_9 (
    .f(conversor_segmentos_9_f), .e(conversor_segmentos_9_e), .d(conversor_segmentos_9_d),
    .a(conversor_segmentos_9_a), .b(conversor_segmentos_9_b), .c(conversor_segmentos_9_c), .in_1(4'b1000),
    .g(conversor_segmentos_9_g));  // open: decimal
  _7_Segment_Display u_7_segment_display_1 (
    .g(conversor_segmentos_1_d), .f(conversor_segmentos_1_e), .a(conversor_segmentos_1_f),
    .b(conversor_segmentos_1_g), .e(conversor_segmentos_1_a), .d(conversor_segmentos_1_b),
    .c(conversor_segmentos_1_c));  // open: dp
  _7_Segment_Display u_7_segment_display_2 (
    .g(conversor_segmentos_2_d), .f(conversor_segmentos_2_e), .a(conversor_segmentos_2_f),
    .b(conversor_segmentos_2_g), .e(conversor_segmentos_2_a), .d(conversor_segmentos_2_b),
    .c(conversor_segmentos_2_c));  // open: dp
  _7_Segment_Display u_7_segment_display_3 (
    .g(conversor_segmentos_3_d), .f(conversor_segmentos_3_e), .a(conversor_segmentos_3_f),
    .b(conversor_segmentos_3_g), .e(conversor_segmentos_3_a), .d(conversor_segmentos_3_b),
    .c(conversor_segmentos_3_c));  // open: dp
  _7_Segment_Display u_7_segment_display_4 (
    .g(conversor_segmentos_4_d), .f(conversor_segmentos_4_e), .a(conversor_segmentos_4_f),
    .b(conversor_segmentos_4_g), .e(conversor_segmentos_4_a), .d(conversor_segmentos_4_b),
    .c(conversor_segmentos_4_c));  // open: dp
  _7_Segment_Display u_7_segment_display_5 (
    .g(conversor_segmentos_5_d), .f(conversor_segmentos_5_e), .a(conversor_segmentos_5_f),
    .b(conversor_segmentos_5_g), .e(conversor_segmentos_5_a), .d(conversor_segmentos_5_b),
    .c(conversor_segmentos_5_c));  // open: dp
  _7_Segment_Display u_7_segment_display_6 (
    .g(conversor_segmentos_6_d), .f(conversor_segmentos_6_e), .a(conversor_segmentos_6_f),
    .b(conversor_segmentos_6_g), .e(conversor_segmentos_6_a), .d(conversor_segmentos_6_b),
    .c(conversor_segmentos_6_c));  // open: dp
  _7_Segment_Display u_7_segment_display_7 (
    .g(conversor_segmentos_7_d), .f(conversor_segmentos_7_e), .a(conversor_segmentos_7_f),
    .b(conversor_segmentos_7_g), .e(conversor_segmentos_7_a), .d(conversor_segmentos_7_b),
    .c(conversor_segmentos_7_c));  // open: dp
  _7_Segment_Display u_7_segment_display_8 (
    .g(conversor_segmentos_8_d), .f(conversor_segmentos_8_e), .a(conversor_segmentos_8_f),
    .b(conversor_segmentos_8_g), .e(conversor_segmentos_8_a), .d(conversor_segmentos_8_b),
    .c(conversor_segmentos_8_c));  // open: dp
  _7_Segment_Display u_7_segment_display_9 (
    .g(conversor_segmentos_9_d), .f(conversor_segmentos_9_e), .a(conversor_segmentos_9_f),
    .b(conversor_segmentos_9_g), .e(conversor_segmentos_9_a), .d(conversor_segmentos_9_b),
    .c(conversor_segmentos_9_c));  // open: dp
  Counter #(.width(4), .max('hf)) counter_1 (
    .Q(counter_1_q), .clk(clock_1_out));  // open: load, D, count, carry, clr, preset, down
  Clock clock_1 (.out(clock_1_out));
  CONVERSOR_SEGMENTOS conversor_segmentos_10 (
    .f(conversor_segmentos_10_f), .e(conversor_segmentos_10_e), .d(conversor_segmentos_10_d),
    .a(conversor_segmentos_10_a), .b(conversor_segmentos_10_b), .c(conversor_segmentos_10_c), .in_1(4'b1001),
    .g(conversor_segmentos_10_g));  // open: decimal
  CONVERSOR_SEGMENTOS conversor_segmentos_11 (
    .f(conversor_segmentos_11_f), .e(conversor_segmentos_11_e), .d(conversor_segmentos_11_d),
    .a(conversor_segmentos_11_a), .b(conversor_segmentos_11_b), .c(conversor_segmentos_11_c), .in_1(4'b1010),
    .g(conversor_segmentos_11_g));  // open: decimal
  CONVERSOR_SEGMENTOS conversor_segmentos_12 (
    .f(conversor_segmentos_12_f), .e(conversor_segmentos_12_e), .d(conversor_segmentos_12_d),
    .a(conversor_segmentos_12_a), .b(conversor_segmentos_12_b), .c(conversor_segmentos_12_c), .in_1(4'b1011),
    .g(conversor_segmentos_12_g));  // open: decimal
  CONVERSOR_SEGMENTOS conversor_segmentos_13 (
    .f(conversor_segmentos_13_f), .e(conversor_segmentos_13_e), .d(conversor_segmentos_13_d),
    .a(conversor_segmentos_13_a), .b(conversor_segmentos_13_b), .c(conversor_segmentos_13_c), .in_1(4'b1100),
    .g(conversor_segmentos_13_g));  // open: decimal
  CONVERSOR_SEGMENTOS conversor_segmentos_14 (
    .f(conversor_segmentos_14_f), .e(conversor_segmentos_14_e), .d(conversor_segmentos_14_d),
    .a(conversor_segmentos_14_a), .b(conversor_segmentos_14_b), .c(conversor_segmentos_14_c), .in_1(4'b1101),
    .g(conversor_segmentos_14_g));  // open: decimal
  CONVERSOR_SEGMENTOS conversor_segmentos_15 (
    .f(conversor_segmentos_15_f), .e(conversor_segmentos_15_e), .d(conversor_segmentos_15_d),
    .a(conversor_segmentos_15_a), .b(conversor_segmentos_15_b), .c(conversor_segmentos_15_c), .in_1(4'b1110),
    .g(conversor_segmentos_15_g));  // open: decimal
  CONVERSOR_SEGMENTOS conversor_segmentos_16 (
    .f(conversor_segmentos_16_f), .e(conversor_segmentos_16_e), .d(conversor_segmentos_16_d),
    .a(conversor_segmentos_16_a), .b(conversor_segmentos_16_b), .c(conversor_segmentos_16_c), .in_1(4'b1111),
    .g(conversor_segmentos_16_g));  // open: decimal
  CONVERSOR_SEGMENTOS conversor_segmentos_17 (
    .f(conversor_segmentos_17_f), .e(conversor_segmentos_17_e), .d(conversor_segmentos_17_d),
    .a(conversor_segmentos_17_a), .b(conversor_segmentos_17_b), .c(conversor_segmentos_17_c),
    .in_1(counter_1_q), .g(conversor_segmentos_17_g));  // open: decimal
  _7_Segment_Display u_7_segment_display_10 (
    .g(conversor_segmentos_10_d), .f(conversor_segmentos_10_e), .a(conversor_segmentos_10_f),
    .b(conversor_segmentos_10_g), .e(conversor_segmentos_10_a), .d(conversor_segmentos_10_b),
    .c(conversor_segmentos_10_c));  // open: dp
  _7_Segment_Display u_7_segment_display_11 (
    .g(conversor_segmentos_11_d), .f(conversor_segmentos_11_e), .a(conversor_segmentos_11_f),
    .b(conversor_segmentos_11_g), .e(conversor_segmentos_11_a), .d(conversor_segmentos_11_b),
    .c(conversor_segmentos_11_c));  // open: dp
  _7_Segment_Display u_7_segment_display_12 (
    .g(conversor_segmentos_12_d), .f(conversor_segmentos_12_e), .a(conversor_segmentos_12_f),
    .b(conversor_segmentos_12_g), .e(conversor_segmentos_12_a), .d(conversor_segmentos_12_b),
    .c(conversor_segmentos_12_c));  // open: dp
  _7_Segment_Display u_7_segment_display_13 (
    .g(conversor_segmentos_13_d), .f(conversor_segmentos_13_e), .a(conversor_segmentos_13_f),
    .b(conversor_segmentos_13_g), .e(conversor_segmentos_13_a), .d(conversor_segmentos_13_b),
    .c(conversor_segmentos_13_c));  // open: dp
  _7_Segment_Display u_7_segment_display_14 (
    .g(conversor_segmentos_14_d), .f(conversor_segmentos_14_e), .a(conversor_segmentos_14_f),
    .b(conversor_segmentos_14_g), .e(conversor_segmentos_14_a), .d(conversor_segmentos_14_b),
    .c(conversor_segmentos_14_c));  // open: dp
  _7_Segment_Display u_7_segment_display_15 (
    .g(conversor_segmentos_15_d), .f(conversor_segmentos_15_e), .a(conversor_segmentos_15_f),
    .b(conversor_segmentos_15_g), .e(conversor_segmentos_15_a), .d(conversor_segmentos_15_b),
    .c(conversor_segmentos_15_c));  // open: dp
  _7_Segment_Display u_7_segment_display_16 (
    .g(conversor_segmentos_16_d), .f(conversor_segmentos_16_e), .a(conversor_segmentos_16_f),
    .b(conversor_segmentos_16_g), .e(conversor_segmentos_16_a), .d(conversor_segmentos_16_b),
    .c(conversor_segmentos_16_c));  // open: dp
  _7_Segment_Display u_7_segment_display_17 (
    .g(conversor_segmentos_17_d), .f(conversor_segmentos_17_e), .a(conversor_segmentos_17_f),
    .b(conversor_segmentos_17_g), .e(conversor_segmentos_17_a), .d(conversor_segmentos_17_b),
    .c(conversor_segmentos_17_c));  // open: dp

  // Notes on the sheet:
  //   CTRL + k para iniciar a simulação
  //   Configurar a frequência de pulso para 4 Hz em: Simular > Frequência de pulso > 4 Hz
endmodule

module TESTE_SOMADOR (
);

  wire [3:0] somador_1_out_3, somador_2_out_3, somador_3_out_3, somador_4_out_3, somador_5_out_3,
       somador_6_out_3, somador_7_out_3, somador_8_out_3, somador_9_out_3, somador_10_out_3,
       somador_11_out_3, somador_12_out_3, somador_13_out_3, somador_14_out_3, somador_15_out_3,
       somador_16_out_3;

  SOMADOR somador_1 (.in_1(4'b0001), .in_2(4'b1111), .out_3(somador_1_out_3));
  Hex_Digit_Display hex_digit_display_1 (.value(somador_1_out_3));  // open: dp
  SOMADOR somador_2 (.in_1(4'b0010), .in_2(4'b1111), .out_3(somador_2_out_3));
  Hex_Digit_Display hex_digit_display_2 (.value(somador_2_out_3));  // open: dp
  SOMADOR somador_3 (.in_1(4'b0001), .in_2(4'b0001), .out_3(somador_3_out_3));
  Hex_Digit_Display hex_digit_display_3 (.value(somador_3_out_3));  // open: dp
  SOMADOR somador_4 (.in_1(4'b0001), .in_2(4'b0010), .out_3(somador_4_out_3));
  Hex_Digit_Display hex_digit_display_4 (.value(somador_4_out_3));  // open: dp
  SOMADOR somador_5 (.in_1(4'b1111), .in_2(4'b0101), .out_3(somador_5_out_3));
  Hex_Digit_Display hex_digit_display_5 (.value(somador_5_out_3));  // open: dp
  SOMADOR somador_6 (.in_1(4'b1111), .in_2(4'b0110), .out_3(somador_6_out_3));
  Hex_Digit_Display hex_digit_display_6 (.value(somador_6_out_3));  // open: dp
  SOMADOR somador_7 (.in_1(4'b0011), .in_2(4'b0011), .out_3(somador_7_out_3));
  Hex_Digit_Display hex_digit_display_7 (.value(somador_7_out_3));  // open: dp
  SOMADOR somador_8 (.in_1(4'b0100), .in_2(4'b0011), .out_3(somador_8_out_3));
  Hex_Digit_Display hex_digit_display_8 (.value(somador_8_out_3));  // open: dp
  SOMADOR somador_9 (.in_1(4'b0100), .in_2(4'b0100), .out_3(somador_9_out_3));
  SOMADOR somador_10 (.in_1(4'b1111), .in_2(4'b1010), .out_3(somador_10_out_3));
  SOMADOR somador_11 (.in_1(4'b0000), .in_2(4'b1010), .out_3(somador_11_out_3));
  SOMADOR somador_12 (.in_1(4'b1011), .in_2(4'b0000), .out_3(somador_12_out_3));
  SOMADOR somador_13 (.in_1(4'b1100), .in_2(4'b0000), .out_3(somador_13_out_3));
  SOMADOR somador_14 (.in_1(4'b0111), .in_2(4'b0110), .out_3(somador_14_out_3));
  SOMADOR somador_15 (.in_1(4'b1111), .in_2(4'b1111), .out_3(somador_15_out_3));
  SOMADOR somador_16 (.in_1(4'b1110), .in_2(4'b0001), .out_3(somador_16_out_3));
  Hex_Digit_Display hex_digit_display_9 (.value(somador_9_out_3));  // open: dp
  Hex_Digit_Display hex_digit_display_10 (.value(somador_10_out_3));  // open: dp
  Hex_Digit_Display hex_digit_display_11 (.value(somador_11_out_3));  // open: dp
  Hex_Digit_Display hex_digit_display_12 (.value(somador_12_out_3));  // open: dp
  Hex_Digit_Display hex_digit_display_13 (.value(somador_13_out_3));  // open: dp
  Hex_Digit_Display hex_digit_display_14 (.value(somador_14_out_3));  // open: dp
  Hex_Digit_Display hex_digit_display_15 (.value(somador_15_out_3));  // open: dp
  Hex_Digit_Display hex_digit_display_16 (.value(somador_16_out_3));  // open: dp
endmodule

module TESTE_SUBTRATOR (
);

  wire [3:0] subtrator_1_out_3, subtrator_2_out_3, subtrator_3_out_3, subtrator_4_out_3, subtrator_5_out_3,
       subtrator_6_out_3, subtrator_7_out_3, subtrator_8_out_3, subtrator_9_out_3, subtrator_10_out_3,
       subtrator_11_out_3, subtrator_12_out_3, subtrator_13_out_3, subtrator_14_out_3, subtrator_15_out_3,
       subtrator_16_out_3;

  SUBTRATOR subtrator_1 (.in_1(4'b1110), .in_2(4'b1110), .out_3(subtrator_1_out_3));
  Hex_Digit_Display hex_digit_display_1 (.value(subtrator_1_out_3));  // open: dp
  SUBTRATOR subtrator_2 (.in_1(4'b0000), .in_2(4'b1111), .out_3(subtrator_2_out_3));
  Hex_Digit_Display hex_digit_display_2 (.value(subtrator_2_out_3));  // open: dp
  SUBTRATOR subtrator_3 (.in_1(4'b0011), .in_2(4'b0001), .out_3(subtrator_3_out_3));
  Hex_Digit_Display hex_digit_display_3 (.value(subtrator_3_out_3));  // open: dp
  SUBTRATOR subtrator_4 (.in_1(4'b0101), .in_2(4'b0010), .out_3(subtrator_4_out_3));
  Hex_Digit_Display hex_digit_display_4 (.value(subtrator_4_out_3));  // open: dp
  SUBTRATOR subtrator_5 (.in_1(4'b1111), .in_2(4'b1011), .out_3(subtrator_5_out_3));
  Hex_Digit_Display hex_digit_display_5 (.value(subtrator_5_out_3));  // open: dp
  SUBTRATOR subtrator_6 (.in_1(4'b1111), .in_2(4'b1010), .out_3(subtrator_6_out_3));
  Hex_Digit_Display hex_digit_display_6 (.value(subtrator_6_out_3));  // open: dp
  SUBTRATOR subtrator_7 (.in_1(4'b1111), .in_2(4'b1001), .out_3(subtrator_7_out_3));
  Hex_Digit_Display hex_digit_display_7 (.value(subtrator_7_out_3));  // open: dp
  SUBTRATOR subtrator_8 (.in_1(4'b0110), .in_2(4'b1111), .out_3(subtrator_8_out_3));
  Hex_Digit_Display hex_digit_display_8 (.value(subtrator_8_out_3));  // open: dp
  SUBTRATOR subtrator_9 (.in_1(4'b1000), .in_2(4'b0000), .out_3(subtrator_9_out_3));
  SUBTRATOR subtrator_10 (.in_1(4'b1001), .in_2(4'b0000), .out_3(subtrator_10_out_3));
  SUBTRATOR subtrator_11 (.in_1(4'b1010), .in_2(4'b0000), .out_3(subtrator_11_out_3));
  SUBTRATOR subtrator_12 (.in_1(4'b1011), .in_2(4'b0000), .out_3(subtrator_12_out_3));
  SUBTRATOR subtrator_13 (.in_1(4'b1011), .in_2(4'b1111), .out_3(subtrator_13_out_3));
  SUBTRATOR subtrator_14 (.in_1(4'b1101), .in_2(4'b0000), .out_3(subtrator_14_out_3));
  SUBTRATOR subtrator_15 (.in_1(4'b1111), .in_2(4'b0001), .out_3(subtrator_15_out_3));
  SUBTRATOR subtrator_16 (.in_1(4'b1110), .in_2(4'b1111), .out_3(subtrator_16_out_3));
  Hex_Digit_Display hex_digit_display_9 (.value(subtrator_9_out_3));  // open: dp
  Hex_Digit_Display hex_digit_display_10 (.value(subtrator_10_out_3));  // open: dp
  Hex_Digit_Display hex_digit_display_11 (.value(subtrator_11_out_3));  // open: dp
  Hex_Digit_Display hex_digit_display_12 (.value(subtrator_12_out_3));  // open: dp
  Hex_Digit_Display hex_digit_display_13 (.value(subtrator_13_out_3));  // open: dp
  Hex_Digit_Display hex_digit_display_14 (.value(subtrator_14_out_3));  // open: dp
  Hex_Digit_Display hex_digit_display_15 (.value(subtrator_15_out_3));  // open: dp
  Hex_Digit_Display hex_digit_display_16 (.value(subtrator_16_out_3));  // open: dp
endmodule

module TESTE_COMPARADOR (
);

  wire clock_1_out, clock_2_out, comparador_1_out_3, comparador_1_out_4, comparador_1_out_5,
       comparador_2_out_3, comparador_2_out_4, comparador_2_out_5, comparador_3_out_3, comparador_3_out_4,
       comparador_3_out_5, comparador_4_out_3, comparador_4_out_4, comparador_4_out_5, comparador_5_out_3,
       comparador_5_out_4, comparador_5_out_5, comparador_6_out_3, comparador_6_out_4, comparador_6_out_5,
       comparador_7_out_3, comparador_7_out_4, comparador_7_out_5, comparador_8_out_3, comparador_8_out_4,
       comparador_8_out_5, comparador_9_out_3, comparador_9_out_4, comparador_9_out_5, comparador_10_out_3,
       comparador_10_out_4, comparador_10_out_5, comparador_11_out_3, comparador_11_out_4,
       comparador_11_out_5, comparador_12_out_3, comparador_12_out_4, comparador_12_out_5,
       comparador_13_out_3, comparador_13_out_4, comparador_13_out_5, comparador_14_out_3,
       comparador_14_out_4, comparador_14_out_5, comparador_15_out_3, comparador_15_out_4,
       comparador_15_out_5, comparator_1_eq, comparator_2_eq;
  wire [3:0] adder_1_out, counter_1_q, counter_2_q, multiplexer_1_out, subtractor_1_out;

  COMPARADOR comparador_1 (
    .\a__número_anterior (4'b1111), .\b__número_posterior (4'b0001), .out_3(comparador_1_out_3),
    .out_4(comparador_1_out_4), .out_5(comparador_1_out_5));
  COMPARADOR comparador_2 (
    .\a__número_anterior (4'b1111), .\b__número_posterior (4'b1111), .out_3(comparador_2_out_3),
    .out_4(comparador_2_out_4), .out_5(comparador_2_out_5));
  COMPARADOR comparador_3 (
    .\a__número_anterior (4'b0001), .\b__número_posterior (4'b1111), .out_3(comparador_3_out_3),
    .out_4(comparador_3_out_4), .out_5(comparador_3_out_5));
  LED led (.in(comparador_1_out_3));
  LED led_2 (.in(comparador_1_out_4));
  LED led_3 (.in(comparador_1_out_5));
  LED led_4 (.in(comparador_2_out_3));
  LED led_5 (.in(comparador_2_out_4));
  LED led_6 (.in(comparador_2_out_5));
  LED led_7 (.in(comparador_3_out_3));
  LED led_8 (.in(comparador_3_out_4));
  LED led_9 (.in(comparador_3_out_5));
  Clock clock_1 (.out(clock_1_out));
  Clock clock_2 (.out(clock_2_out));
  Counter #(.width(4), .max('hf)) counter_1 (
    .Q(counter_1_q), .clk(clock_1_out), .clr(comparator_1_eq));  // open: load, D, count, carry, preset, down
  Counter #(.width(4), .max('hf)) counter_2 (
    .Q(counter_2_q), .clk(clock_2_out));  // open: load, D, count, carry, clr, preset, down
  COMPARADOR comparador_4 (
    .\a__número_anterior (4'b0011), .\b__número_posterior (4'b0010), .out_3(comparador_4_out_3),
    .out_4(comparador_4_out_4), .out_5(comparador_4_out_5));
  COMPARADOR comparador_5 (
    .\a__número_anterior (4'b0100), .\b__número_posterior (4'b0100), .out_3(comparador_5_out_3),
    .out_4(comparador_5_out_4), .out_5(comparador_5_out_5));
  COMPARADOR comparador_6 (
    .\a__número_anterior (4'b0111), .\b__número_posterior (4'b1001), .out_3(comparador_6_out_3),
    .out_4(comparador_6_out_4), .out_5(comparador_6_out_5));
  Comparator #(.width(4), .mode("unsigned")) comparator_1 (
    .a(counter_1_q), .b(4'b1111), .eq(comparator_1_eq));  // open: gt, lt
  Comparator #(.width(4), .mode("unsigned")) comparator_2 (
    .a(counter_2_q), .b(4'b0000), .eq(comparator_2_eq));  // open: gt, lt
  LED led_10 (.in(comparador_4_out_3));
  LED led_11 (.in(comparador_4_out_4));
  LED led_12 (.in(comparador_4_out_5));
  LED led_13 (.in(comparador_5_out_3));
  LED led_14 (.in(comparador_5_out_4));
  LED led_15 (.in(comparador_5_out_5));
  LED led_16 (.in(comparador_6_out_3));
  LED led_17 (.in(comparador_6_out_4));
  LED led_18 (.in(comparador_6_out_5));
  Multiplexer #(.width(4), .enable("false")) multiplexer_1 (
    .in0(counter_2_q), .in1(4'b0001), .out(multiplexer_1_out), .sel(comparator_2_eq));
  COMPARADOR comparador_7 (
    .\a__número_anterior (4'b1101), .\b__número_posterior (4'b0011), .out_3(comparador_7_out_3),
    .out_4(comparador_7_out_4), .out_5(comparador_7_out_5));
  COMPARADOR comparador_8 (
    .\a__número_anterior (4'b0000), .\b__número_posterior (4'b0000), .out_3(comparador_8_out_3),
    .out_4(comparador_8_out_4), .out_5(comparador_8_out_5));
  COMPARADOR comparador_9 (
    .\a__número_anterior (4'b0011), .\b__número_posterior (4'b1001), .out_3(comparador_9_out_3),
    .out_4(comparador_9_out_4), .out_5(comparador_9_out_5));
  Adder #(.width(4)) adder_1 (.a(4'b0001), .b(counter_1_q), .out(adder_1_out));  // open: cin, cout
  Subtractor #(.width(4)) subtractor_1 (.a(multiplexer_1_out), .b(4'b0001), .out(subtractor_1_out));  // open: bin, bout
  LED led_19 (.in(comparador_7_out_3));
  LED led_20 (.in(comparador_7_out_4));
  LED led_21 (.in(comparador_7_out_5));
  LED led_22 (.in(comparador_8_out_3));
  LED led_23 (.in(comparador_8_out_4));
  LED led_24 (.in(comparador_8_out_5));
  LED led_25 (.in(comparador_9_out_3));
  LED led_26 (.in(comparador_9_out_4));
  LED led_27 (.in(comparador_9_out_5));
  COMPARADOR comparador_10 (
    .\a__número_anterior (adder_1_out), .\b__número_posterior (counter_1_q), .out_3(comparador_10_out_3),
    .out_4(comparador_10_out_4), .out_5(comparador_10_out_5));
  COMPARADOR comparador_11 (
    .\a__número_anterior (counter_2_q), .\b__número_posterior (counter_2_q), .out_3(comparador_11_out_3),
    .out_4(comparador_11_out_4), .out_5(comparador_11_out_5));
  COMPARADOR comparador_12 (
    .\a__número_anterior (subtractor_1_out), .\b__número_posterior (multiplexer_1_out),
    .out_3(comparador_12_out_3), .out_4(comparador_12_out_4), .out_5(comparador_12_out_5));
  LED led_28 (.in(comparador_10_out_3));
  LED led_29 (.in(comparador_10_out_4));
  LED led_30 (.in(comparador_10_out_5));
  LED led_31 (.in(comparador_11_out_3));
  LED led_32 (.in(comparador_11_out_4));
  LED led_33 (.in(comparador_11_out_5));
  LED led_34 (.in(comparador_12_out_3));
  LED led_35 (.in(comparador_12_out_4));
  LED led_36 (.in(comparador_12_out_5));
  COMPARADOR comparador_13 (
    .\a__número_anterior (4'b1101), .\b__número_posterior (4'b1001), .out_3(comparador_13_out_3),
    .out_4(comparador_13_out_4), .out_5(comparador_13_out_5));
  COMPARADOR comparador_14 (
    .\a__número_anterior (4'b1010), .\b__número_posterior (4'b1010), .out_3(comparador_14_out_3),
    .out_4(comparador_14_out_4), .out_5(comparador_14_out_5));
  COMPARADOR comparador_15 (
    .\a__número_anterior (4'b0000), .\b__número_posterior (4'b1111), .out_3(comparador_15_out_3),
    .out_4(comparador_15_out_4), .out_5(comparador_15_out_5));
  LED led_37 (.in(comparador_13_out_3));
  LED led_38 (.in(comparador_13_out_4));
  LED led_39 (.in(comparador_13_out_5));
  LED led_40 (.in(comparador_14_out_3));
  LED led_41 (.in(comparador_14_out_4));
  LED led_42 (.in(comparador_14_out_5));
  LED led_43 (.in(comparador_15_out_3));
  LED led_44 (.in(comparador_15_out_4));
  LED led_45 (.in(comparador_15_out_5));

  // Notes on the sheet:
  //   CTRL + k para iniciar a simulação
  //   Configurar a frequência de pulso para 4 Hz em: Simular > Frequência de pulso > 4 Hz
endmodule

module TESTE_DMX (
);

  wire dmx_1_s0, dmx_1_s1, dmx_1_s2, dmx_1_s3, dmx_1_s4, dmx_1_s5, dmx_1_s6, dmx_1_s7, dmx_1_s8, dmx_1_s9,
       dmx_1_s10, dmx_1_s11, dmx_1_s12, dmx_1_s13, dmx_1_s14, dmx_1_s15, dmx_2_s0, dmx_2_s1, dmx_2_s2,
       dmx_2_s3, dmx_2_s4, dmx_2_s5, dmx_2_s6, dmx_2_s7, dmx_2_s8, dmx_2_s9, dmx_2_s10, dmx_2_s11, dmx_2_s12,
       dmx_2_s13, dmx_2_s14, dmx_2_s15, dmx_3_s0, dmx_3_s1, dmx_3_s2, dmx_3_s3, dmx_3_s4, dmx_3_s5, dmx_3_s6,
       dmx_3_s7, dmx_3_s8, dmx_3_s9, dmx_3_s10, dmx_3_s11, dmx_3_s12, dmx_3_s13, dmx_3_s14, dmx_3_s15,
       dmx_4_s0, dmx_4_s1, dmx_4_s2, dmx_4_s3, dmx_4_s4, dmx_4_s5, dmx_4_s6, dmx_4_s7, dmx_4_s8, dmx_4_s9,
       dmx_4_s10, dmx_4_s11, dmx_4_s12, dmx_4_s13, dmx_4_s14, dmx_4_s15, dmx_5_s0, dmx_5_s1, dmx_5_s2,
       dmx_5_s3, dmx_5_s4, dmx_5_s5, dmx_5_s6, dmx_5_s7, dmx_5_s8, dmx_5_s9, dmx_5_s10, dmx_5_s11, dmx_5_s12,
       dmx_5_s13, dmx_5_s14, dmx_5_s15, dmx_6_s0, dmx_6_s1, dmx_6_s2, dmx_6_s3, dmx_6_s4, dmx_6_s5, dmx_6_s6,
       dmx_6_s7, dmx_6_s8, dmx_6_s9, dmx_6_s10, dmx_6_s11, dmx_6_s12, dmx_6_s13, dmx_6_s14, dmx_6_s15,
       dmx_7_s0, dmx_7_s1, dmx_7_s2, dmx_7_s3, dmx_7_s4, dmx_7_s5, dmx_7_s6, dmx_7_s7, dmx_7_s8, dmx_7_s9,
       dmx_7_s10, dmx_7_s11, dmx_7_s12, dmx_7_s13, dmx_7_s14, dmx_7_s15, dmx_8_s0, dmx_8_s1, dmx_8_s2,
       dmx_8_s3, dmx_8_s4, dmx_8_s5, dmx_8_s6, dmx_8_s7, dmx_8_s8, dmx_8_s9, dmx_8_s10, dmx_8_s11, dmx_8_s12,
       dmx_8_s13, dmx_8_s14, dmx_8_s15, dmx_9_s0, dmx_9_s1, dmx_9_s2, dmx_9_s3, dmx_9_s4, dmx_9_s5, dmx_9_s6,
       dmx_9_s7, dmx_9_s8, dmx_9_s9, dmx_9_s10, dmx_9_s11, dmx_9_s12, dmx_9_s13, dmx_9_s14, dmx_9_s15,
       dmx_10_s0, dmx_10_s1, dmx_10_s2, dmx_10_s3, dmx_10_s4, dmx_10_s5, dmx_10_s6, dmx_10_s7, dmx_10_s8,
       dmx_10_s9, dmx_10_s10, dmx_10_s11, dmx_10_s12, dmx_10_s13, dmx_10_s14, dmx_10_s15, dmx_11_s0,
       dmx_11_s1, dmx_11_s2, dmx_11_s3, dmx_11_s4, dmx_11_s5, dmx_11_s6, dmx_11_s7, dmx_11_s8, dmx_11_s9,
       dmx_11_s10, dmx_11_s11, dmx_11_s12, dmx_11_s13, dmx_11_s14, dmx_11_s15, dmx_12_s0, dmx_12_s1,
       dmx_12_s2, dmx_12_s3, dmx_12_s4, dmx_12_s5, dmx_12_s6, dmx_12_s7, dmx_12_s8, dmx_12_s9, dmx_12_s10,
       dmx_12_s11, dmx_12_s12, dmx_12_s13, dmx_12_s14, dmx_12_s15, dmx_13_s0, dmx_13_s1, dmx_13_s2,
       dmx_13_s3, dmx_13_s4, dmx_13_s5, dmx_13_s6, dmx_13_s7, dmx_13_s8, dmx_13_s9, dmx_13_s10, dmx_13_s11,
       dmx_13_s12, dmx_13_s13, dmx_13_s14, dmx_13_s15, dmx_14_s0, dmx_14_s1, dmx_14_s2, dmx_14_s3, dmx_14_s4,
       dmx_14_s5, dmx_14_s6, dmx_14_s7, dmx_14_s8, dmx_14_s9, dmx_14_s10, dmx_14_s11, dmx_14_s12, dmx_14_s13,
       dmx_14_s14, dmx_14_s15, dmx_15_s0, dmx_15_s1, dmx_15_s2, dmx_15_s3, dmx_15_s4, dmx_15_s5, dmx_15_s6,
       dmx_15_s7, dmx_15_s8, dmx_15_s9, dmx_15_s10, dmx_15_s11, dmx_15_s12, dmx_15_s13, dmx_15_s14,
       dmx_15_s15, dmx_16_s0, dmx_16_s1, dmx_16_s2, dmx_16_s3, dmx_16_s4, dmx_16_s5, dmx_16_s6, dmx_16_s7,
       dmx_16_s8, dmx_16_s9, dmx_16_s10, dmx_16_s11, dmx_16_s12, dmx_16_s13, dmx_16_s14, dmx_16_s15;
  wire [14:0] dmx15_1_s0, dmx15_2_s15, dmx15_3_s0, dmx15_4_s15, dmx15_5_s0, dmx15_6_s15, dmx15_7_s0,
       dmx15_8_s15, dmx15_9_s0, dmx15_10_s15, dmx15_11_s0, dmx15_12_s15, dmx15_13_s0, dmx15_14_s15,
       dmx15_15_s0, dmx15_16_s15;

  DotMatrix #(.matrixcols(16), .matrixrows(1)) dotmatrix_1 (
    .col0(dmx_1_s0), .col1(dmx_1_s1), .col2(dmx_1_s2), .col3(dmx_1_s3), .col4(dmx_1_s4), .col5(dmx_1_s5),
    .col6(dmx_1_s6), .col7(dmx_1_s7), .col8(dmx_1_s8), .col9(dmx_1_s9), .col10(dmx_1_s10), .col11(dmx_1_s11),
    .col12(dmx_1_s12), .col13(dmx_1_s13), .col14(dmx_1_s14), .col15(dmx_1_s15));
  DMX dmx_1 (
    .\Seleção (4'b0000), .Entrada(1'b1), .s0(dmx_1_s0), .S1(dmx_1_s1), .S2(dmx_1_s2), .S3(dmx_1_s3),
    .S4(dmx_1_s4), .S5(dmx_1_s5), .S6(dmx_1_s6), .S7(dmx_1_s7), .S8(dmx_1_s8), .S9(dmx_1_s9),
    .S10(dmx_1_s10), .S11(dmx_1_s11), .S12(dmx_1_s12), .S13(dmx_1_s13), .S14(dmx_1_s14), .S15(dmx_1_s15));
  DotMatrix #(.matrixcols(16), .matrixrows(1)) dotmatrix_2 (
    .col0(dmx_2_s0), .col1(dmx_2_s1), .col2(dmx_2_s2), .col3(dmx_2_s3), .col4(dmx_2_s4), .col5(dmx_2_s5),
    .col6(dmx_2_s6), .col7(dmx_2_s7), .col8(dmx_2_s8), .col9(dmx_2_s9), .col10(dmx_2_s10), .col11(dmx_2_s11),
    .col12(dmx_2_s12), .col13(dmx_2_s13), .col14(dmx_2_s14), .col15(dmx_2_s15));
  DMX dmx_2 (
    .\Seleção (4'b0001), .Entrada(1'b1), .s0(dmx_2_s0), .S1(dmx_2_s1), .S2(dmx_2_s2), .S3(dmx_2_s3),
    .S4(dmx_2_s4), .S5(dmx_2_s5), .S6(dmx_2_s6), .S7(dmx_2_s7), .S8(dmx_2_s8), .S9(dmx_2_s9),
    .S10(dmx_2_s10), .S11(dmx_2_s11), .S12(dmx_2_s12), .S13(dmx_2_s13), .S14(dmx_2_s14), .S15(dmx_2_s15));
  DotMatrix #(.matrixcols(16), .matrixrows(1)) dotmatrix_3 (
    .col0(dmx_3_s0), .col1(dmx_3_s1), .col2(dmx_3_s2), .col3(dmx_3_s3), .col4(dmx_3_s4), .col5(dmx_3_s5),
    .col6(dmx_3_s6), .col7(dmx_3_s7), .col8(dmx_3_s8), .col9(dmx_3_s9), .col10(dmx_3_s10), .col11(dmx_3_s11),
    .col12(dmx_3_s12), .col13(dmx_3_s13), .col14(dmx_3_s14), .col15(dmx_3_s15));
  DMX dmx_3 (
    .\Seleção (4'b0010), .Entrada(1'b1), .s0(dmx_3_s0), .S1(dmx_3_s1), .S2(dmx_3_s2), .S3(dmx_3_s3),
    .S4(dmx_3_s4), .S5(dmx_3_s5), .S6(dmx_3_s6), .S7(dmx_3_s7), .S8(dmx_3_s8), .S9(dmx_3_s9),
    .S10(dmx_3_s10), .S11(dmx_3_s11), .S12(dmx_3_s12), .S13(dmx_3_s13), .S14(dmx_3_s14), .S15(dmx_3_s15));
  DotMatrix #(.matrixcols(16), .matrixrows(1)) dotmatrix_4 (
    .col0(dmx_4_s0), .col1(dmx_4_s1), .col2(dmx_4_s2), .col3(dmx_4_s3), .col4(dmx_4_s4), .col5(dmx_4_s5),
    .col6(dmx_4_s6), .col7(dmx_4_s7), .col8(dmx_4_s8), .col9(dmx_4_s9), .col10(dmx_4_s10), .col11(dmx_4_s11),
    .col12(dmx_4_s12), .col13(dmx_4_s13), .col14(dmx_4_s14), .col15(dmx_4_s15));
  DMX dmx_4 (
    .\Seleção (4'b0011), .Entrada(1'b1), .s0(dmx_4_s0), .S1(dmx_4_s1), .S2(dmx_4_s2), .S3(dmx_4_s3),
    .S4(dmx_4_s4), .S5(dmx_4_s5), .S6(dmx_4_s6), .S7(dmx_4_s7), .S8(dmx_4_s8), .S9(dmx_4_s9),
    .S10(dmx_4_s10), .S11(dmx_4_s11), .S12(dmx_4_s12), .S13(dmx_4_s13), .S14(dmx_4_s14), .S15(dmx_4_s15));
  DotMatrix #(.matrixcols(16), .matrixrows(1)) dotmatrix_5 (
    .col0(dmx_5_s0), .col1(dmx_5_s1), .col2(dmx_5_s2), .col3(dmx_5_s3), .col4(dmx_5_s4), .col5(dmx_5_s5),
    .col6(dmx_5_s6), .col7(dmx_5_s7), .col8(dmx_5_s8), .col9(dmx_5_s9), .col10(dmx_5_s10), .col11(dmx_5_s11),
    .col12(dmx_5_s12), .col13(dmx_5_s13), .col14(dmx_5_s14), .col15(dmx_5_s15));
  DMX dmx_5 (
    .\Seleção (4'b0100), .Entrada(1'b1), .s0(dmx_5_s0), .S1(dmx_5_s1), .S2(dmx_5_s2), .S3(dmx_5_s3),
    .S4(dmx_5_s4), .S5(dmx_5_s5), .S6(dmx_5_s6), .S7(dmx_5_s7), .S8(dmx_5_s8), .S9(dmx_5_s9),
    .S10(dmx_5_s10), .S11(dmx_5_s11), .S12(dmx_5_s12), .S13(dmx_5_s13), .S14(dmx_5_s14), .S15(dmx_5_s15));
  DotMatrix #(.matrixcols(16), .matrixrows(1)) dotmatrix_6 (
    .col0(dmx_6_s0), .col1(dmx_6_s1), .col2(dmx_6_s2), .col3(dmx_6_s3), .col4(dmx_6_s4), .col5(dmx_6_s5),
    .col6(dmx_6_s6), .col7(dmx_6_s7), .col8(dmx_6_s8), .col9(dmx_6_s9), .col10(dmx_6_s10), .col11(dmx_6_s11),
    .col12(dmx_6_s12), .col13(dmx_6_s13), .col14(dmx_6_s14), .col15(dmx_6_s15));
  DMX dmx_6 (
    .\Seleção (4'b0101), .Entrada(1'b1), .s0(dmx_6_s0), .S1(dmx_6_s1), .S2(dmx_6_s2), .S3(dmx_6_s3),
    .S4(dmx_6_s4), .S5(dmx_6_s5), .S6(dmx_6_s6), .S7(dmx_6_s7), .S8(dmx_6_s8), .S9(dmx_6_s9),
    .S10(dmx_6_s10), .S11(dmx_6_s11), .S12(dmx_6_s12), .S13(dmx_6_s13), .S14(dmx_6_s14), .S15(dmx_6_s15));
  DotMatrix #(.matrixcols(16), .matrixrows(1)) dotmatrix_7 (
    .col0(dmx_7_s0), .col1(dmx_7_s1), .col2(dmx_7_s2), .col3(dmx_7_s3), .col4(dmx_7_s4), .col5(dmx_7_s5),
    .col6(dmx_7_s6), .col7(dmx_7_s7), .col8(dmx_7_s8), .col9(dmx_7_s9), .col10(dmx_7_s10), .col11(dmx_7_s11),
    .col12(dmx_7_s12), .col13(dmx_7_s13), .col14(dmx_7_s14), .col15(dmx_7_s15));
  DMX dmx_7 (
    .\Seleção (4'b0110), .Entrada(1'b1), .s0(dmx_7_s0), .S1(dmx_7_s1), .S2(dmx_7_s2), .S3(dmx_7_s3),
    .S4(dmx_7_s4), .S5(dmx_7_s5), .S6(dmx_7_s6), .S7(dmx_7_s7), .S8(dmx_7_s8), .S9(dmx_7_s9),
    .S10(dmx_7_s10), .S11(dmx_7_s11), .S12(dmx_7_s12), .S13(dmx_7_s13), .S14(dmx_7_s14), .S15(dmx_7_s15));
  DotMatrix #(.matrixcols(16), .matrixrows(1)) dotmatrix_8 (
    .col0(dmx_8_s0), .col1(dmx_8_s1), .col2(dmx_8_s2), .col3(dmx_8_s3), .col4(dmx_8_s4), .col5(dmx_8_s5),
    .col6(dmx_8_s6), .col7(dmx_8_s7), .col8(dmx_8_s8), .col9(dmx_8_s9), .col10(dmx_8_s10), .col11(dmx_8_s11),
    .col12(dmx_8_s12), .col13(dmx_8_s13), .col14(dmx_8_s14), .col15(dmx_8_s15));
  DMX dmx_8 (
    .\Seleção (4'b0111), .Entrada(1'b1), .s0(dmx_8_s0), .S1(dmx_8_s1), .S2(dmx_8_s2), .S3(dmx_8_s3),
    .S4(dmx_8_s4), .S5(dmx_8_s5), .S6(dmx_8_s6), .S7(dmx_8_s7), .S8(dmx_8_s8), .S9(dmx_8_s9),
    .S10(dmx_8_s10), .S11(dmx_8_s11), .S12(dmx_8_s12), .S13(dmx_8_s13), .S14(dmx_8_s14), .S15(dmx_8_s15));
  DotMatrix #(.matrixcols(16), .matrixrows(1)) dotmatrix_9 (
    .col0(dmx_9_s0), .col1(dmx_9_s1), .col2(dmx_9_s2), .col3(dmx_9_s3), .col4(dmx_9_s4), .col5(dmx_9_s5),
    .col6(dmx_9_s6), .col7(dmx_9_s7), .col8(dmx_9_s8), .col9(dmx_9_s9), .col10(dmx_9_s10), .col11(dmx_9_s11),
    .col12(dmx_9_s12), .col13(dmx_9_s13), .col14(dmx_9_s14), .col15(dmx_9_s15));
  DMX dmx_9 (
    .\Seleção (4'b1000), .Entrada(1'b1), .s0(dmx_9_s0), .S1(dmx_9_s1), .S2(dmx_9_s2), .S3(dmx_9_s3),
    .S4(dmx_9_s4), .S5(dmx_9_s5), .S6(dmx_9_s6), .S7(dmx_9_s7), .S8(dmx_9_s8), .S9(dmx_9_s9),
    .S10(dmx_9_s10), .S11(dmx_9_s11), .S12(dmx_9_s12), .S13(dmx_9_s13), .S14(dmx_9_s14), .S15(dmx_9_s15));
  DotMatrix #(.matrixcols(16), .matrixrows(1)) dotmatrix_10 (
    .col0(dmx_10_s0), .col1(dmx_10_s1), .col2(dmx_10_s2), .col3(dmx_10_s3), .col4(dmx_10_s4),
    .col5(dmx_10_s5), .col6(dmx_10_s6), .col7(dmx_10_s7), .col8(dmx_10_s8), .col9(dmx_10_s9),
    .col10(dmx_10_s10), .col11(dmx_10_s11), .col12(dmx_10_s12), .col13(dmx_10_s13), .col14(dmx_10_s14),
    .col15(dmx_10_s15));
  DMX dmx_10 (
    .\Seleção (4'b1001), .Entrada(1'b1), .s0(dmx_10_s0), .S1(dmx_10_s1), .S2(dmx_10_s2), .S3(dmx_10_s3),
    .S4(dmx_10_s4), .S5(dmx_10_s5), .S6(dmx_10_s6), .S7(dmx_10_s7), .S8(dmx_10_s8), .S9(dmx_10_s9),
    .S10(dmx_10_s10), .S11(dmx_10_s11), .S12(dmx_10_s12), .S13(dmx_10_s13), .S14(dmx_10_s14), .S15(dmx_10_s15));
  DotMatrix #(.matrixcols(16), .matrixrows(1)) dotmatrix_11 (
    .col0(dmx_11_s0), .col1(dmx_11_s1), .col2(dmx_11_s2), .col3(dmx_11_s3), .col4(dmx_11_s4),
    .col5(dmx_11_s5), .col6(dmx_11_s6), .col7(dmx_11_s7), .col8(dmx_11_s8), .col9(dmx_11_s9),
    .col10(dmx_11_s10), .col11(dmx_11_s11), .col12(dmx_11_s12), .col13(dmx_11_s13), .col14(dmx_11_s14),
    .col15(dmx_11_s15));
  DMX dmx_11 (
    .\Seleção (4'b1010), .Entrada(1'b1), .s0(dmx_11_s0), .S1(dmx_11_s1), .S2(dmx_11_s2), .S3(dmx_11_s3),
    .S4(dmx_11_s4), .S5(dmx_11_s5), .S6(dmx_11_s6), .S7(dmx_11_s7), .S8(dmx_11_s8), .S9(dmx_11_s9),
    .S10(dmx_11_s10), .S11(dmx_11_s11), .S12(dmx_11_s12), .S13(dmx_11_s13), .S14(dmx_11_s14), .S15(dmx_11_s15));
  DotMatrix #(.matrixcols(16), .matrixrows(1)) dotmatrix_12 (
    .col0(dmx_12_s0), .col1(dmx_12_s1), .col2(dmx_12_s2), .col3(dmx_12_s3), .col4(dmx_12_s4),
    .col5(dmx_12_s5), .col6(dmx_12_s6), .col7(dmx_12_s7), .col8(dmx_12_s8), .col9(dmx_12_s9),
    .col10(dmx_12_s10), .col11(dmx_12_s11), .col12(dmx_12_s12), .col13(dmx_12_s13), .col14(dmx_12_s14),
    .col15(dmx_12_s15));
  DMX dmx_12 (
    .\Seleção (4'b1011), .Entrada(1'b1), .s0(dmx_12_s0), .S1(dmx_12_s1), .S2(dmx_12_s2), .S3(dmx_12_s3),
    .S4(dmx_12_s4), .S5(dmx_12_s5), .S6(dmx_12_s6), .S7(dmx_12_s7), .S8(dmx_12_s8), .S9(dmx_12_s9),
    .S10(dmx_12_s10), .S11(dmx_12_s11), .S12(dmx_12_s12), .S13(dmx_12_s13), .S14(dmx_12_s14), .S15(dmx_12_s15));
  DotMatrix #(.matrixcols(16), .matrixrows(1)) dotmatrix_13 (
    .col0(dmx_13_s0), .col1(dmx_13_s1), .col2(dmx_13_s2), .col3(dmx_13_s3), .col4(dmx_13_s4),
    .col5(dmx_13_s5), .col6(dmx_13_s6), .col7(dmx_13_s7), .col8(dmx_13_s8), .col9(dmx_13_s9),
    .col10(dmx_13_s10), .col11(dmx_13_s11), .col12(dmx_13_s12), .col13(dmx_13_s13), .col14(dmx_13_s14),
    .col15(dmx_13_s15));
  DMX dmx_13 (
    .\Seleção (4'b1100), .Entrada(1'b1), .s0(dmx_13_s0), .S1(dmx_13_s1), .S2(dmx_13_s2), .S3(dmx_13_s3),
    .S4(dmx_13_s4), .S5(dmx_13_s5), .S6(dmx_13_s6), .S7(dmx_13_s7), .S8(dmx_13_s8), .S9(dmx_13_s9),
    .S10(dmx_13_s10), .S11(dmx_13_s11), .S12(dmx_13_s12), .S13(dmx_13_s13), .S14(dmx_13_s14), .S15(dmx_13_s15));
  DotMatrix #(.matrixcols(16), .matrixrows(1)) dotmatrix_14 (
    .col0(dmx_14_s0), .col1(dmx_14_s1), .col2(dmx_14_s2), .col3(dmx_14_s3), .col4(dmx_14_s4),
    .col5(dmx_14_s5), .col6(dmx_14_s6), .col7(dmx_14_s7), .col8(dmx_14_s8), .col9(dmx_14_s9),
    .col10(dmx_14_s10), .col11(dmx_14_s11), .col12(dmx_14_s12), .col13(dmx_14_s13), .col14(dmx_14_s14),
    .col15(dmx_14_s15));
  DMX dmx_14 (
    .\Seleção (4'b1101), .Entrada(1'b1), .s0(dmx_14_s0), .S1(dmx_14_s1), .S2(dmx_14_s2), .S3(dmx_14_s3),
    .S4(dmx_14_s4), .S5(dmx_14_s5), .S6(dmx_14_s6), .S7(dmx_14_s7), .S8(dmx_14_s8), .S9(dmx_14_s9),
    .S10(dmx_14_s10), .S11(dmx_14_s11), .S12(dmx_14_s12), .S13(dmx_14_s13), .S14(dmx_14_s14), .S15(dmx_14_s15));
  DotMatrix #(.matrixcols(16), .matrixrows(1)) dotmatrix_15 (
    .col0(dmx_15_s0), .col1(dmx_15_s1), .col2(dmx_15_s2), .col3(dmx_15_s3), .col4(dmx_15_s4),
    .col5(dmx_15_s5), .col6(dmx_15_s6), .col7(dmx_15_s7), .col8(dmx_15_s8), .col9(dmx_15_s9),
    .col10(dmx_15_s10), .col11(dmx_15_s11), .col12(dmx_15_s12), .col13(dmx_15_s13), .col14(dmx_15_s14),
    .col15(dmx_15_s15));
  DMX dmx_15 (
    .\Seleção (4'b1110), .Entrada(1'b1), .s0(dmx_15_s0), .S1(dmx_15_s1), .S2(dmx_15_s2), .S3(dmx_15_s3),
    .S4(dmx_15_s4), .S5(dmx_15_s5), .S6(dmx_15_s6), .S7(dmx_15_s7), .S8(dmx_15_s8), .S9(dmx_15_s9),
    .S10(dmx_15_s10), .S11(dmx_15_s11), .S12(dmx_15_s12), .S13(dmx_15_s13), .S14(dmx_15_s14), .S15(dmx_15_s15));
  DotMatrix #(.matrixcols(16), .matrixrows(1)) dotmatrix_16 (
    .col0(dmx_16_s0), .col1(dmx_16_s1), .col2(dmx_16_s2), .col3(dmx_16_s3), .col4(dmx_16_s4),
    .col5(dmx_16_s5), .col6(dmx_16_s6), .col7(dmx_16_s7), .col8(dmx_16_s8), .col9(dmx_16_s9),
    .col10(dmx_16_s10), .col11(dmx_16_s11), .col12(dmx_16_s12), .col13(dmx_16_s13), .col14(dmx_16_s14),
    .col15(dmx_16_s15));
  DMX dmx_16 (
    .\Seleção (4'b1111), .Entrada(1'b1), .s0(dmx_16_s0), .S1(dmx_16_s1), .S2(dmx_16_s2), .S3(dmx_16_s3),
    .S4(dmx_16_s4), .S5(dmx_16_s5), .S6(dmx_16_s6), .S7(dmx_16_s7), .S8(dmx_16_s8), .S9(dmx_16_s9),
    .S10(dmx_16_s10), .S11(dmx_16_s11), .S12(dmx_16_s12), .S13(dmx_16_s13), .S14(dmx_16_s14), .S15(dmx_16_s15));
  DotMatrix #(.matrixcols(15), .matrixrows(1)) dotmatrix_17 (
    .col0(dmx15_1_s0[14]), .col1(dmx15_1_s0[13]), .col2(dmx15_1_s0[12]), .col3(dmx15_1_s0[11]),
    .col4(dmx15_1_s0[10]), .col5(dmx15_1_s0[9]), .col6(dmx15_1_s0[8]), .col7(dmx15_1_s0[7]),
    .col8(dmx15_1_s0[6]), .col9(dmx15_1_s0[5]), .col10(dmx15_1_s0[4]), .col11(dmx15_1_s0[3]),
    .col12(dmx15_1_s0[2]), .col13(dmx15_1_s0[1]), .col14(dmx15_1_s0[0]));
  DMX15 dmx15_1 (
    .\Seleção (4'b0000), .Entrada(15'h1), .s0(dmx15_1_s0));  // open: S1, S2, S3, S4, S5, S6, S7, S8, S9, S10, S11, S12, S13, S14, S15
  DotMatrix #(.matrixcols(15), .matrixrows(1)) dotmatrix_18 (
    .col0(dmx15_2_s15[14]), .col1(dmx15_2_s15[13]), .col2(dmx15_2_s15[12]), .col3(dmx15_2_s15[11]),
    .col4(dmx15_2_s15[10]), .col5(dmx15_2_s15[9]), .col6(dmx15_2_s15[8]), .col7(dmx15_2_s15[7]),
    .col8(dmx15_2_s15[6]), .col9(dmx15_2_s15[5]), .col10(dmx15_2_s15[4]), .col11(dmx15_2_s15[3]),
    .col12(dmx15_2_s15[2]), .col13(dmx15_2_s15[1]), .col14(dmx15_2_s15[0]));
  DMX15 dmx15_2 (
    .\Seleção (4'b1111), .Entrada(15'h1), .S15(dmx15_2_s15));  // open: s0, S1, S2, S3, S4, S5, S6, S7, S8, S9, S10, S11, S12, S13, S14
  DotMatrix #(.matrixcols(15), .matrixrows(1)) dotmatrix_19 (
    .col0(dmx15_3_s0[14]), .col1(dmx15_3_s0[13]), .col2(dmx15_3_s0[12]), .col3(dmx15_3_s0[11]),
    .col4(dmx15_3_s0[10]), .col5(dmx15_3_s0[9]), .col6(dmx15_3_s0[8]), .col7(dmx15_3_s0[7]),
    .col8(dmx15_3_s0[6]), .col9(dmx15_3_s0[5]), .col10(dmx15_3_s0[4]), .col11(dmx15_3_s0[3]),
    .col12(dmx15_3_s0[2]), .col13(dmx15_3_s0[1]), .col14(dmx15_3_s0[0]));
  DMX15 dmx15_3 (
    .\Seleção (4'b0000), .Entrada(15'h2), .s0(dmx15_3_s0));  // open: S1, S2, S3, S4, S5, S6, S7, S8, S9, S10, S11, S12, S13, S14, S15
  DotMatrix #(.matrixcols(15), .matrixrows(1)) dotmatrix_20 (
    .col0(dmx15_4_s15[14]), .col1(dmx15_4_s15[13]), .col2(dmx15_4_s15[12]), .col3(dmx15_4_s15[11]),
    .col4(dmx15_4_s15[10]), .col5(dmx15_4_s15[9]), .col6(dmx15_4_s15[8]), .col7(dmx15_4_s15[7]),
    .col8(dmx15_4_s15[6]), .col9(dmx15_4_s15[5]), .col10(dmx15_4_s15[4]), .col11(dmx15_4_s15[3]),
    .col12(dmx15_4_s15[2]), .col13(dmx15_4_s15[1]), .col14(dmx15_4_s15[0]));
  DMX15 dmx15_4 (
    .\Seleção (4'b1111), .Entrada(15'h2), .S15(dmx15_4_s15));  // open: s0, S1, S2, S3, S4, S5, S6, S7, S8, S9, S10, S11, S12, S13, S14
  DotMatrix #(.matrixcols(15), .matrixrows(1)) dotmatrix_21 (
    .col0(dmx15_5_s0[14]), .col1(dmx15_5_s0[13]), .col2(dmx15_5_s0[12]), .col3(dmx15_5_s0[11]),
    .col4(dmx15_5_s0[10]), .col5(dmx15_5_s0[9]), .col6(dmx15_5_s0[8]), .col7(dmx15_5_s0[7]),
    .col8(dmx15_5_s0[6]), .col9(dmx15_5_s0[5]), .col10(dmx15_5_s0[4]), .col11(dmx15_5_s0[3]),
    .col12(dmx15_5_s0[2]), .col13(dmx15_5_s0[1]), .col14(dmx15_5_s0[0]));
  DMX15 dmx15_5 (
    .\Seleção (4'b0000), .Entrada(15'h3), .s0(dmx15_5_s0));  // open: S1, S2, S3, S4, S5, S6, S7, S8, S9, S10, S11, S12, S13, S14, S15
  DotMatrix #(.matrixcols(15), .matrixrows(1)) dotmatrix_22 (
    .col0(dmx15_6_s15[14]), .col1(dmx15_6_s15[13]), .col2(dmx15_6_s15[12]), .col3(dmx15_6_s15[11]),
    .col4(dmx15_6_s15[10]), .col5(dmx15_6_s15[9]), .col6(dmx15_6_s15[8]), .col7(dmx15_6_s15[7]),
    .col8(dmx15_6_s15[6]), .col9(dmx15_6_s15[5]), .col10(dmx15_6_s15[4]), .col11(dmx15_6_s15[3]),
    .col12(dmx15_6_s15[2]), .col13(dmx15_6_s15[1]), .col14(dmx15_6_s15[0]));
  DMX15 dmx15_6 (
    .\Seleção (4'b1111), .Entrada(15'h3), .S15(dmx15_6_s15));  // open: s0, S1, S2, S3, S4, S5, S6, S7, S8, S9, S10, S11, S12, S13, S14
  DotMatrix #(.matrixcols(15), .matrixrows(1)) dotmatrix_23 (
    .col0(dmx15_7_s0[14]), .col1(dmx15_7_s0[13]), .col2(dmx15_7_s0[12]), .col3(dmx15_7_s0[11]),
    .col4(dmx15_7_s0[10]), .col5(dmx15_7_s0[9]), .col6(dmx15_7_s0[8]), .col7(dmx15_7_s0[7]),
    .col8(dmx15_7_s0[6]), .col9(dmx15_7_s0[5]), .col10(dmx15_7_s0[4]), .col11(dmx15_7_s0[3]),
    .col12(dmx15_7_s0[2]), .col13(dmx15_7_s0[1]), .col14(dmx15_7_s0[0]));
  DMX15 dmx15_7 (
    .\Seleção (4'b0000), .Entrada(15'h4), .s0(dmx15_7_s0));  // open: S1, S2, S3, S4, S5, S6, S7, S8, S9, S10, S11, S12, S13, S14, S15
  DotMatrix #(.matrixcols(15), .matrixrows(1)) dotmatrix_24 (
    .col0(dmx15_8_s15[14]), .col1(dmx15_8_s15[13]), .col2(dmx15_8_s15[12]), .col3(dmx15_8_s15[11]),
    .col4(dmx15_8_s15[10]), .col5(dmx15_8_s15[9]), .col6(dmx15_8_s15[8]), .col7(dmx15_8_s15[7]),
    .col8(dmx15_8_s15[6]), .col9(dmx15_8_s15[5]), .col10(dmx15_8_s15[4]), .col11(dmx15_8_s15[3]),
    .col12(dmx15_8_s15[2]), .col13(dmx15_8_s15[1]), .col14(dmx15_8_s15[0]));
  DMX15 dmx15_8 (
    .\Seleção (4'b1111), .Entrada(15'h4), .S15(dmx15_8_s15));  // open: s0, S1, S2, S3, S4, S5, S6, S7, S8, S9, S10, S11, S12, S13, S14
  DotMatrix #(.matrixcols(15), .matrixrows(1)) dotmatrix_25 (
    .col0(dmx15_9_s0[14]), .col1(dmx15_9_s0[13]), .col2(dmx15_9_s0[12]), .col3(dmx15_9_s0[11]),
    .col4(dmx15_9_s0[10]), .col5(dmx15_9_s0[9]), .col6(dmx15_9_s0[8]), .col7(dmx15_9_s0[7]),
    .col8(dmx15_9_s0[6]), .col9(dmx15_9_s0[5]), .col10(dmx15_9_s0[4]), .col11(dmx15_9_s0[3]),
    .col12(dmx15_9_s0[2]), .col13(dmx15_9_s0[1]), .col14(dmx15_9_s0[0]));
  DMX15 dmx15_9 (
    .\Seleção (4'b0000), .Entrada(15'h5), .s0(dmx15_9_s0));  // open: S1, S2, S3, S4, S5, S6, S7, S8, S9, S10, S11, S12, S13, S14, S15
  DotMatrix #(.matrixcols(15), .matrixrows(1)) dotmatrix_26 (
    .col0(dmx15_10_s15[14]), .col1(dmx15_10_s15[13]), .col2(dmx15_10_s15[12]), .col3(dmx15_10_s15[11]),
    .col4(dmx15_10_s15[10]), .col5(dmx15_10_s15[9]), .col6(dmx15_10_s15[8]), .col7(dmx15_10_s15[7]),
    .col8(dmx15_10_s15[6]), .col9(dmx15_10_s15[5]), .col10(dmx15_10_s15[4]), .col11(dmx15_10_s15[3]),
    .col12(dmx15_10_s15[2]), .col13(dmx15_10_s15[1]), .col14(dmx15_10_s15[0]));
  DMX15 dmx15_10 (
    .\Seleção (4'b1111), .Entrada(15'h5), .S15(dmx15_10_s15));  // open: s0, S1, S2, S3, S4, S5, S6, S7, S8, S9, S10, S11, S12, S13, S14
  DotMatrix #(.matrixcols(15), .matrixrows(1)) dotmatrix_27 (
    .col0(dmx15_11_s0[14]), .col1(dmx15_11_s0[13]), .col2(dmx15_11_s0[12]), .col3(dmx15_11_s0[11]),
    .col4(dmx15_11_s0[10]), .col5(dmx15_11_s0[9]), .col6(dmx15_11_s0[8]), .col7(dmx15_11_s0[7]),
    .col8(dmx15_11_s0[6]), .col9(dmx15_11_s0[5]), .col10(dmx15_11_s0[4]), .col11(dmx15_11_s0[3]),
    .col12(dmx15_11_s0[2]), .col13(dmx15_11_s0[1]), .col14(dmx15_11_s0[0]));
  DMX15 dmx15_11 (
    .\Seleção (4'b0000), .Entrada(15'h6), .s0(dmx15_11_s0));  // open: S1, S2, S3, S4, S5, S6, S7, S8, S9, S10, S11, S12, S13, S14, S15
  DotMatrix #(.matrixcols(15), .matrixrows(1)) dotmatrix_28 (
    .col0(dmx15_12_s15[14]), .col1(dmx15_12_s15[13]), .col2(dmx15_12_s15[12]), .col3(dmx15_12_s15[11]),
    .col4(dmx15_12_s15[10]), .col5(dmx15_12_s15[9]), .col6(dmx15_12_s15[8]), .col7(dmx15_12_s15[7]),
    .col8(dmx15_12_s15[6]), .col9(dmx15_12_s15[5]), .col10(dmx15_12_s15[4]), .col11(dmx15_12_s15[3]),
    .col12(dmx15_12_s15[2]), .col13(dmx15_12_s15[1]), .col14(dmx15_12_s15[0]));
  DMX15 dmx15_12 (
    .\Seleção (4'b1111), .Entrada(15'h6), .S15(dmx15_12_s15));  // open: s0, S1, S2, S3, S4, S5, S6, S7, S8, S9, S10, S11, S12, S13, S14
  DotMatrix #(.matrixcols(15), .matrixrows(1)) dotmatrix_29 (
    .col0(dmx15_13_s0[14]), .col1(dmx15_13_s0[13]), .col2(dmx15_13_s0[12]), .col3(dmx15_13_s0[11]),
    .col4(dmx15_13_s0[10]), .col5(dmx15_13_s0[9]), .col6(dmx15_13_s0[8]), .col7(dmx15_13_s0[7]),
    .col8(dmx15_13_s0[6]), .col9(dmx15_13_s0[5]), .col10(dmx15_13_s0[4]), .col11(dmx15_13_s0[3]),
    .col12(dmx15_13_s0[2]), .col13(dmx15_13_s0[1]), .col14(dmx15_13_s0[0]));
  DMX15 dmx15_13 (
    .\Seleção (4'b0000), .Entrada(15'h7), .s0(dmx15_13_s0));  // open: S1, S2, S3, S4, S5, S6, S7, S8, S9, S10, S11, S12, S13, S14, S15
  DotMatrix #(.matrixcols(15), .matrixrows(1)) dotmatrix_30 (
    .col0(dmx15_14_s15[14]), .col1(dmx15_14_s15[13]), .col2(dmx15_14_s15[12]), .col3(dmx15_14_s15[11]),
    .col4(dmx15_14_s15[10]), .col5(dmx15_14_s15[9]), .col6(dmx15_14_s15[8]), .col7(dmx15_14_s15[7]),
    .col8(dmx15_14_s15[6]), .col9(dmx15_14_s15[5]), .col10(dmx15_14_s15[4]), .col11(dmx15_14_s15[3]),
    .col12(dmx15_14_s15[2]), .col13(dmx15_14_s15[1]), .col14(dmx15_14_s15[0]));
  DMX15 dmx15_14 (
    .\Seleção (4'b1111), .Entrada(15'h7), .S15(dmx15_14_s15));  // open: s0, S1, S2, S3, S4, S5, S6, S7, S8, S9, S10, S11, S12, S13, S14
  DotMatrix #(.matrixcols(15), .matrixrows(1)) dotmatrix_31 (
    .col0(dmx15_15_s0[14]), .col1(dmx15_15_s0[13]), .col2(dmx15_15_s0[12]), .col3(dmx15_15_s0[11]),
    .col4(dmx15_15_s0[10]), .col5(dmx15_15_s0[9]), .col6(dmx15_15_s0[8]), .col7(dmx15_15_s0[7]),
    .col8(dmx15_15_s0[6]), .col9(dmx15_15_s0[5]), .col10(dmx15_15_s0[4]), .col11(dmx15_15_s0[3]),
    .col12(dmx15_15_s0[2]), .col13(dmx15_15_s0[1]), .col14(dmx15_15_s0[0]));
  DMX15 dmx15_15 (
    .\Seleção (4'b0000), .Entrada({15{1'b1}}), .s0(dmx15_15_s0));  // open: S1, S2, S3, S4, S5, S6, S7, S8, S9, S10, S11, S12, S13, S14, S15
  DotMatrix #(.matrixcols(15), .matrixrows(1)) dotmatrix_32 (
    .col0(dmx15_16_s15[14]), .col1(dmx15_16_s15[13]), .col2(dmx15_16_s15[12]), .col3(dmx15_16_s15[11]),
    .col4(dmx15_16_s15[10]), .col5(dmx15_16_s15[9]), .col6(dmx15_16_s15[8]), .col7(dmx15_16_s15[7]),
    .col8(dmx15_16_s15[6]), .col9(dmx15_16_s15[5]), .col10(dmx15_16_s15[4]), .col11(dmx15_16_s15[3]),
    .col12(dmx15_16_s15[2]), .col13(dmx15_16_s15[1]), .col14(dmx15_16_s15[0]));
  DMX15 dmx15_16 (
    .\Seleção (4'b1111), .Entrada({15{1'b1}}), .S15(dmx15_16_s15));  // open: s0, S1, S2, S3, S4, S5, S6, S7, S8, S9, S10, S11, S12, S13, S14
endmodule

module TESTE_MUX (
);

  wire comparator_1_eq, comparator_2_eq, comparator_3_eq, comparator_4_eq, comparator_5_eq, comparator_6_eq,
       comparator_7_eq, comparator_8_eq, comparator_9_eq, comparator_10_eq, comparator_11_eq,
       comparator_12_eq, comparator_13_eq, comparator_14_eq, comparator_15_eq, comparator_16_eq;
  wire [3:0] mux_1_out_4, mux_2_out_4, mux_3_out_4, mux_4_out_4, mux_5_out_4, mux_6_out_4, mux_7_out_4,
       mux_8_out_4;
  wire [14:0] mux15_1_out_4, mux15_2_out_4, mux15_3_out_4, mux15_4_out_4, mux15_5_out_4, mux15_6_out_4,
       mux15_7_out_4, mux15_8_out_4;

  MUX mux_1 (.in_1(4'b1010), .in_2(4'b0101), .in_3(1'b0), .out_4(mux_1_out_4));
  MUX mux_2 (.in_1(4'b1010), .in_2(4'b0101), .in_3(1'b1), .out_4(mux_2_out_4));
  MUX15 mux15_1 (.in_1(15'ha), .in_2(15'h5), .in_3(1'b0), .out_4(mux15_1_out_4));
  MUX15 mux15_2 (.in_1(15'ha), .in_2(15'h5), .in_3(1'b1), .out_4(mux15_2_out_4));
  LED led_1 (.in(comparator_1_eq));
  Comparator #(.width(4)) comparator_1 (.a(mux_1_out_4), .b(4'b1010), .eq(comparator_1_eq));  // open: gt, lt
  LED led_2 (.in(comparator_2_eq));
  Comparator #(.width(4)) comparator_2 (.a(mux_2_out_4), .b(4'b0101), .eq(comparator_2_eq));  // open: gt, lt
  LED led_3 (.in(comparator_3_eq));
  Comparator #(.width(15)) comparator_3 (.a(mux15_1_out_4), .b(15'ha), .eq(comparator_3_eq));  // open: gt, lt
  LED led_4 (.in(comparator_4_eq));
  Comparator #(.width(15)) comparator_4 (.a(mux15_2_out_4), .b(15'h5), .eq(comparator_4_eq));  // open: gt, lt
  MUX mux_3 (.in_1(4'b0000), .in_2(4'b0001), .in_3(1'b0), .out_4(mux_3_out_4));
  MUX mux_4 (.in_1(4'b0000), .in_2(4'b0001), .in_3(1'b1), .out_4(mux_4_out_4));
  MUX15 mux15_3 (.in_1(15'h7ff9), .in_2(15'h7ffa), .in_3(1'b0), .out_4(mux15_3_out_4));
  MUX15 mux15_4 (.in_1(15'h7ff9), .in_2(15'h7ffa), .in_3(1'b1), .out_4(mux15_4_out_4));
  Comparator #(.width(4)) comparator_5 (.a(mux_3_out_4), .b(4'b0000), .eq(comparator_5_eq));  // open: gt, lt
  LED led_5 (.in(comparator_5_eq));
  Comparator #(.width(4)) comparator_6 (.a(mux_4_out_4), .b(4'b0001), .eq(comparator_6_eq));  // open: gt, lt
  LED led_6 (.in(comparator_6_eq));
  LED led_7 (.in(comparator_7_eq));
  Comparator #(.width(15)) comparator_7 (.a(mux15_3_out_4), .b(15'h7ff9), .eq(comparator_7_eq));  // open: gt, lt
  LED led_8 (.in(comparator_8_eq));
  Comparator #(.width(15)) comparator_8 (.a(mux15_4_out_4), .b(15'h7ffa), .eq(comparator_8_eq));  // open: gt, lt
  LED led_9 ();  // open: in
  LED led_10 ();  // open: in
  MUX mux_5 (.in_1(4'b1111), .in_2(4'b1111), .in_3(1'b0), .out_4(mux_5_out_4));
  MUX mux_6 (.in_1(4'b1111), .in_2(4'b1111), .in_3(1'b1), .out_4(mux_6_out_4));
  MUX15 mux15_5 (.in_1(15'h1), .in_2(15'h2), .in_3(1'b0), .out_4(mux15_5_out_4));
  MUX15 mux15_6 (.in_1(15'h1), .in_2(15'h2), .in_3(1'b1), .out_4(mux15_6_out_4));
  LED led_11 (.in(comparator_9_eq));
  Comparator #(.width(4)) comparator_9 (.a(mux_5_out_4), .b(4'b1111), .eq(comparator_9_eq));  // open: gt, lt
  Comparator #(.width(4)) comparator_10 (.a(mux_6_out_4), .b(4'b1111), .eq(comparator_10_eq));  // open: gt, lt
  LED led_12 (.in(comparator_10_eq));
  LED led_13 (.in(comparator_11_eq));
  Comparator #(.width(15)) comparator_11 (.a(mux15_5_out_4), .b(15'h1), .eq(comparator_11_eq));  // open: gt, lt
  Comparator #(.width(15)) comparator_12 (.a(mux15_6_out_4), .b(15'h2), .eq(comparator_12_eq));  // open: gt, lt
  LED led_14 (.in(comparator_12_eq));
  MUX mux_7 (.in_1(4'b0000), .in_2(4'b0001), .in_3(1'b0), .out_4(mux_7_out_4));
  MUX mux_8 (.in_1(4'b0000), .in_2(4'b0001), .in_3(1'b1), .out_4(mux_8_out_4));
  MUX15 mux15_7 (.in_1(15'h7ff1), .in_2(15'h7fef), .in_3(1'b0), .out_4(mux15_7_out_4));
  MUX15 mux15_8 (.in_1(15'h7ff1), .in_2(15'h7fef), .in_3(1'b1), .out_4(mux15_8_out_4));
  LED led_15 (.in(comparator_13_eq));
  Comparator #(.width(4)) comparator_13 (.a(mux_7_out_4), .b(4'b0000), .eq(comparator_13_eq));  // open: gt, lt
  LED led_16 (.in(comparator_14_eq));
  Comparator #(.width(4)) comparator_14 (.a(mux_8_out_4), .b(4'b0001), .eq(comparator_14_eq));  // open: gt, lt
  LED led_17 (.in(comparator_15_eq));
  Comparator #(.width(15)) comparator_15 (.a(mux15_7_out_4), .b(15'h7ff1), .eq(comparator_15_eq));  // open: gt, lt
  LED led_18 (.in(comparator_16_eq));
  Comparator #(.width(15)) comparator_16 (.a(mux15_8_out_4), .b(15'h7fef), .eq(comparator_16_eq));  // open: gt, lt

  // Notes on the sheet:
  //   FUNCIONANDO!
  //   ERRO!
endmodule

module TESTE_SEPARADOR (
);

  wire clock_1_out, clock_2_out;
  wire [3:0] counter_1_q, counter_2_q, separador_x_1_dezena, separador_x_1_unidade, separador_x_2_dezena,
       separador_x_2_unidade, separador_x_3_dezena, separador_x_3_unidade, separador_x_4_dezena,
       separador_x_4_unidade, separador_x_5_dezena, separador_x_5_unidade, separador_x_6_dezena,
       separador_x_6_unidade, separador_x_7_dezena, separador_x_7_unidade, separador_x_8_dezena,
       separador_x_8_unidade, separador_x_9_dezena, separador_x_9_unidade, separador_x_10_dezena,
       separador_x_10_unidade, separador_x_11_dezena, separador_x_11_unidade, separador_x_12_dezena,
       separador_x_12_unidade, separador_x_13_dezena, separador_x_13_unidade, separador_x_14_dezena,
       separador_x_14_unidade, separador_x_15_dezena, separador_x_15_unidade, separador_x_16_dezena,
       separador_x_16_unidade, separador_y_1_dezena, separador_y_1_unidade, separador_y_2_dezena,
       separador_y_2_unidade, separador_y_3_dezena, separador_y_3_unidade, separador_y_4_dezena,
       separador_y_4_unidade, separador_y_5_dezena, separador_y_5_unidade, separador_y_6_dezena,
       separador_y_6_unidade, separador_y_7_dezena, separador_y_7_unidade, separador_y_8_dezena,
       separador_y_8_unidade, separador_y_9_dezena, separador_y_9_unidade, separador_y_10_dezena,
       separador_y_10_unidade, separador_y_11_dezena, separador_y_11_unidade, separador_y_12_dezena,
       separador_y_12_unidade, separador_y_13_dezena, separador_y_13_unidade, separador_y_14_dezena,
       separador_y_14_unidade, separador_y_15_dezena, separador_y_15_unidade, separador_y_16_dezena,
       separador_y_16_unidade;

  Hex_Digit_Display hex_digit_display_1 (.value(separador_x_1_dezena));  // open: dp
  Hex_Digit_Display hex_digit_display_2 (.value(separador_x_1_unidade));  // open: dp
  SEPARADOR_X separador_x_1 (.DEZENA(separador_x_1_dezena), .UNIDADE(separador_x_1_unidade), .X(4'b0001));
  Hex_Digit_Display hex_digit_display_3 (.value(separador_x_2_dezena));  // open: dp
  Hex_Digit_Display hex_digit_display_4 (.value(separador_x_2_unidade));  // open: dp
  SEPARADOR_X separador_x_2 (.DEZENA(separador_x_2_dezena), .UNIDADE(separador_x_2_unidade), .X(4'b1001));
  Hex_Digit_Display hex_digit_display_5 (.value(separador_x_3_unidade));  // open: dp
  Hex_Digit_Display hex_digit_display_6 (.value(separador_x_3_dezena));  // open: dp
  SEPARADOR_X separador_x_3 (.DEZENA(separador_x_3_dezena), .UNIDADE(separador_x_3_unidade), .X(4'b0010));
  Hex_Digit_Display hex_digit_display_7 (.value(separador_x_4_dezena));  // open: dp
  Hex_Digit_Display hex_digit_display_8 (.value(separador_x_4_unidade));  // open: dp
  SEPARADOR_X separador_x_4 (.DEZENA(separador_x_4_dezena), .UNIDADE(separador_x_4_unidade), .X(4'b1010));
  Hex_Digit_Display hex_digit_display_9 (.value(separador_x_5_dezena));  // open: dp
  SEPARADOR_X separador_x_5 (.DEZENA(separador_x_5_dezena), .UNIDADE(separador_x_5_unidade), .X(4'b0011));
  Hex_Digit_Display hex_digit_display_10 (.value(separador_x_6_dezena));  // open: dp
  SEPARADOR_X separador_x_6 (.DEZENA(separador_x_6_dezena), .UNIDADE(separador_x_6_unidade), .X(4'b1011));
  Hex_Digit_Display hex_digit_display_11 (.value(separador_x_7_dezena));  // open: dp
  Hex_Digit_Display hex_digit_display_12 (.value(separador_x_5_unidade));  // open: dp
  Hex_Digit_Display hex_digit_display_13 (.value(separador_x_6_unidade));  // open: dp
  Hex_Digit_Display hex_digit_display_14 (.value(separador_x_8_dezena));  // open: dp
  Hex_Digit_Display hex_digit_display_15 (.value(separador_x_7_unidade));  // open: dp
  SEPARADOR_X separador_x_7 (.DEZENA(separador_x_7_dezena), .UNIDADE(separador_x_7_unidade), .X(4'b0100));
  Hex_Digit_Display hex_digit_display_16 (.value(separador_x_8_unidade));  // open: dp
  SEPARADOR_X separador_x_8 (.DEZENA(separador_x_8_dezena), .UNIDADE(separador_x_8_unidade), .X(4'b1100));
  Hex_Digit_Display hex_digit_display_17 (.value(separador_x_9_dezena));  // open: dp
  Hex_Digit_Display hex_digit_display_18 (.value(separador_x_9_unidade));  // open: dp
  SEPARADOR_X separador_x_9 (.DEZENA(separador_x_9_dezena), .UNIDADE(separador_x_9_unidade), .X(4'b0101));
  Hex_Digit_Display hex_digit_display_19 (.value(separador_x_10_unidade));  // open: dp
  Hex_Digit_Display hex_digit_display_20 (.value(separador_x_10_dezena));  // open: dp
  SEPARADOR_X separador_x_10 (.DEZENA(separador_x_10_dezena), .UNIDADE(separador_x_10_unidade), .X(4'b1101));
  Hex_Digit_Display hex_digit_display_21 (.value(separador_x_11_unidade));  // open: dp
  Hex_Digit_Display hex_digit_display_22 (.value(separador_x_11_dezena));  // open: dp
  SEPARADOR_X separador_x_11 (.DEZENA(separador_x_11_dezena), .UNIDADE(separador_x_11_unidade), .X(4'b0110));
  Hex_Digit_Display hex_digit_display_23 (.value(separador_x_12_unidade));  // open: dp
  Hex_Digit_Display hex_digit_display_24 (.value(separador_x_12_dezena));  // open: dp
  SEPARADOR_X separador_x_12 (.DEZENA(separador_x_12_dezena), .UNIDADE(separador_x_12_unidade), .X(4'b1110));
  Hex_Digit_Display hex_digit_display_25 (.value(separador_x_13_dezena));  // open: dp
  SEPARADOR_X separador_x_13 (.DEZENA(separador_x_13_dezena), .UNIDADE(separador_x_13_unidade), .X(4'b0111));
  Hex_Digit_Display hex_digit_display_26 (.value(separador_x_14_dezena));  // open: dp
  SEPARADOR_X separador_x_14 (.DEZENA(separador_x_14_dezena), .UNIDADE(separador_x_14_unidade), .X(4'b1111));
  Hex_Digit_Display hex_digit_display_27 (.value(separador_x_13_unidade));  // open: dp
  Hex_Digit_Display hex_digit_display_28 (.value(separador_x_15_dezena));  // open: dp
  Hex_Digit_Display hex_digit_display_29 (.value(separador_x_14_unidade));  // open: dp
  Hex_Digit_Display hex_digit_display_30 (.value(separador_x_16_dezena));  // open: dp
  Counter #(.width(4), .max('hf)) counter_1 (
    .Q(counter_1_q), .clk(clock_1_out));  // open: load, D, count, carry, clr, preset, down
  Clock clock_1 (.out(clock_1_out));
  Hex_Digit_Display hex_digit_display_31 (.value(separador_x_15_unidade));  // open: dp
  SEPARADOR_X separador_x_15 (.DEZENA(separador_x_15_dezena), .UNIDADE(separador_x_15_unidade), .X(4'b1000));
  Hex_Digit_Display hex_digit_display_32 (.value(separador_x_16_unidade));  // open: dp
  SEPARADOR_X separador_x_16 (.DEZENA(separador_x_16_dezena), .UNIDADE(separador_x_16_unidade), .X(counter_1_q));
  Clock clock_2 (.out(clock_2_out));
  Hex_Digit_Display hex_digit_display_33 (.value(separador_y_1_unidade));  // open: dp
  Hex_Digit_Display hex_digit_display_34 (.value(separador_y_1_dezena));  // open: dp
  SEPARADOR_Y separador_y_1 (.DEZENA(separador_y_1_dezena), .UNIDADE(separador_y_1_unidade), .Y(counter_2_q));
  Counter #(.width(4), .max('hf)) counter_2 (
    .Q(counter_2_q), .clk(clock_2_out));  // open: load, D, count, carry, clr, preset, down
  Hex_Digit_Display hex_digit_display_35 (.value(separador_y_2_dezena));  // open: dp
  Hex_Digit_Display hex_digit_display_36 (.value(separador_y_2_unidade));  // open: dp
  SEPARADOR_Y separador_y_2 (.DEZENA(separador_y_2_dezena), .UNIDADE(separador_y_2_unidade), .Y(4'b0001));
  Hex_Digit_Display hex_digit_display_37 (.value(separador_y_3_unidade));  // open: dp
  Hex_Digit_Display hex_digit_display_38 (.value(separador_y_3_dezena));  // open: dp
  SEPARADOR_Y separador_y_3 (.DEZENA(separador_y_3_dezena), .UNIDADE(separador_y_3_unidade), .Y(4'b1001));
  Hex_Digit_Display hex_digit_display_39 (.value(separador_y_4_dezena));  // open: dp
  SEPARADOR_Y separador_y_4 (.DEZENA(separador_y_4_dezena), .UNIDADE(separador_y_4_unidade), .Y(4'b0010));
  Hex_Digit_Display hex_digit_display_40 (.value(separador_y_5_dezena));  // open: dp
  SEPARADOR_Y separador_y_5 (.DEZENA(separador_y_5_dezena), .UNIDADE(separador_y_5_unidade), .Y(4'b1010));
  Hex_Digit_Display hex_digit_display_41 (.value(separador_y_4_unidade));  // open: dp
  Hex_Digit_Display hex_digit_display_42 (.value(separador_y_6_dezena));  // open: dp
  Hex_Digit_Display hex_digit_display_43 (.value(separador_y_7_dezena));  // open: dp
  Hex_Digit_Display hex_digit_display_44 (.value(separador_y_5_unidade));  // open: dp
  Hex_Digit_Display hex_digit_display_45 (.value(separador_y_6_unidade));  // open: dp
  SEPARADOR_Y separador_y_6 (.DEZENA(separador_y_6_dezena), .UNIDADE(separador_y_6_unidade), .Y(4'b0011));
  Hex_Digit_Display hex_digit_display_46 (.value(separador_y_7_unidade));  // open: dp
  SEPARADOR_Y separador_y_7 (.DEZENA(separador_y_7_dezena), .UNIDADE(separador_y_7_unidade), .Y(4'b1011));
  Hex_Digit_Display hex_digit_display_47 (.value(separador_y_8_unidade));  // open: dp
  Hex_Digit_Display hex_digit_display_48 (.value(separador_y_8_dezena));  // open: dp
  SEPARADOR_Y separador_y_8 (.DEZENA(separador_y_8_dezena), .UNIDADE(separador_y_8_unidade), .Y(4'b0100));
  Hex_Digit_Display hex_digit_display_49 (.value(separador_y_9_unidade));  // open: dp
  Hex_Digit_Display hex_digit_display_50 (.value(separador_y_9_dezena));  // open: dp
  SEPARADOR_Y separador_y_9 (.DEZENA(separador_y_9_dezena), .UNIDADE(separador_y_9_unidade), .Y(4'b1100));
  Hex_Digit_Display hex_digit_display_51 (.value(separador_y_10_unidade));  // open: dp
  Hex_Digit_Display hex_digit_display_52 (.value(separador_y_10_dezena));  // open: dp
  SEPARADOR_Y separador_y_10 (.DEZENA(separador_y_10_dezena), .UNIDADE(separador_y_10_unidade), .Y(4'b0101));
  Hex_Digit_Display hex_digit_display_53 (.value(separador_y_11_unidade));  // open: dp
  Hex_Digit_Display hex_digit_display_54 (.value(separador_y_11_dezena));  // open: dp
  SEPARADOR_Y separador_y_11 (.DEZENA(separador_y_11_dezena), .UNIDADE(separador_y_11_unidade), .Y(4'b1101));
  Hex_Digit_Display hex_digit_display_55 (.value(separador_y_12_dezena));  // open: dp
  SEPARADOR_Y separador_y_12 (.DEZENA(separador_y_12_dezena), .UNIDADE(separador_y_12_unidade), .Y(4'b0110));
  Hex_Digit_Display hex_digit_display_56 (.value(separador_y_13_dezena));  // open: dp
  SEPARADOR_Y separador_y_13 (.DEZENA(separador_y_13_dezena), .UNIDADE(separador_y_13_unidade), .Y(4'b1110));
  Hex_Digit_Display hex_digit_display_57 (.value(separador_y_14_dezena));  // open: dp
  Hex_Digit_Display hex_digit_display_58 (.value(separador_y_12_unidade));  // open: dp
  Hex_Digit_Display hex_digit_display_59 (.value(separador_y_13_unidade));  // open: dp
  Hex_Digit_Display hex_digit_display_60 (.value(separador_y_15_dezena));  // open: dp
  Hex_Digit_Display hex_digit_display_61 (.value(separador_y_14_unidade));  // open: dp
  SEPARADOR_Y separador_y_14 (.DEZENA(separador_y_14_dezena), .UNIDADE(separador_y_14_unidade), .Y(4'b0111));
  Hex_Digit_Display hex_digit_display_62 (.value(separador_y_15_unidade));  // open: dp
  SEPARADOR_Y separador_y_15 (.DEZENA(separador_y_15_dezena), .UNIDADE(separador_y_15_unidade), .Y(4'b1111));
  Hex_Digit_Display hex_digit_display_63 (.value(separador_y_16_unidade));  // open: dp
  Hex_Digit_Display hex_digit_display_64 (.value(separador_y_16_dezena));  // open: dp
  SEPARADOR_Y separador_y_16 (.DEZENA(separador_y_16_dezena), .UNIDADE(separador_y_16_unidade), .Y(4'b1000));

  // Notes on the sheet:
  //   VALIDAÇÃO X
  //   CTRL + k para iniciar a simulação
  //   Configurar a frequência de pulso para 4 Hz em: Simular > Frequência de pulso > 4 Hz
  //   VALIDAÇÃO Y
endmodule
module TESTE_GRAFICO (
);

  wire clock_1_out, clock_2_out, clock_3_out, counter_4_carry, subtractor_1_bout;
  wire [3:0] adder_1_out, counter_1_q, counter_2_q, counter_3_q, counter_4_q, subtractor_1_out;
  wire [14:0] grafico_1_coluna_0, grafico_1_coluna_1, grafico_1_coluna_2, grafico_1_coluna_3,
       grafico_1_coluna_4, grafico_1_coluna_5, grafico_1_coluna_6, grafico_1_coluna_7, grafico_1_coluna_8,
       grafico_1_coluna_9, grafico_1_coluna_10, grafico_1_coluna_11, grafico_1_coluna_12,
       grafico_1_coluna_13, grafico_1_coluna_14, grafico_2_coluna_0, grafico_2_coluna_1, grafico_2_coluna_2,
       grafico_2_coluna_3, grafico_2_coluna_4, grafico_2_coluna_5, grafico_2_coluna_6, grafico_2_coluna_7,
       grafico_2_coluna_8, grafico_2_coluna_9, grafico_2_coluna_10, grafico_2_coluna_11, grafico_2_coluna_12,
       grafico_2_coluna_13, grafico_2_coluna_14, grafico_3_coluna_0, grafico_3_coluna_1, grafico_3_coluna_2,
       grafico_3_coluna_3, grafico_3_coluna_4, grafico_3_coluna_5, grafico_3_coluna_6, grafico_3_coluna_7,
       grafico_3_coluna_8, grafico_3_coluna_9, grafico_3_coluna_10, grafico_3_coluna_11, grafico_3_coluna_12,
       grafico_3_coluna_13, grafico_3_coluna_14, grafico_4_coluna_0, grafico_4_coluna_1, grafico_4_coluna_2,
       grafico_4_coluna_3, grafico_4_coluna_4, grafico_4_coluna_5, grafico_4_coluna_6, grafico_4_coluna_7,
       grafico_4_coluna_8, grafico_4_coluna_9, grafico_4_coluna_10, grafico_4_coluna_11, grafico_4_coluna_12,
       grafico_4_coluna_13, grafico_4_coluna_14, grafico_5_coluna_0, grafico_5_coluna_1, grafico_5_coluna_2,
       grafico_5_coluna_3, grafico_5_coluna_4, grafico_5_coluna_5, grafico_5_coluna_6, grafico_5_coluna_7,
       grafico_5_coluna_8, grafico_5_coluna_9, grafico_5_coluna_10, grafico_5_coluna_11, grafico_5_coluna_12,
       grafico_5_coluna_13, grafico_5_coluna_14, grafico_6_coluna_0, grafico_6_coluna_1, grafico_6_coluna_2,
       grafico_6_coluna_3, grafico_6_coluna_4, grafico_6_coluna_5, grafico_6_coluna_6, grafico_6_coluna_7,
       grafico_6_coluna_8, grafico_6_coluna_9, grafico_6_coluna_10, grafico_6_coluna_11, grafico_6_coluna_12,
       grafico_6_coluna_13, grafico_6_coluna_14, grafico_7_coluna_0, grafico_7_coluna_1, grafico_7_coluna_2,
       grafico_7_coluna_3, grafico_7_coluna_4, grafico_7_coluna_5, grafico_7_coluna_6, grafico_7_coluna_7,
       grafico_7_coluna_8, grafico_7_coluna_9, grafico_7_coluna_10, grafico_7_coluna_11, grafico_7_coluna_12,
       grafico_7_coluna_13, grafico_7_coluna_14, grafico_8_coluna_0, grafico_8_coluna_1, grafico_8_coluna_2,
       grafico_8_coluna_3, grafico_8_coluna_4, grafico_8_coluna_5, grafico_8_coluna_6, grafico_8_coluna_7,
       grafico_8_coluna_8, grafico_8_coluna_9, grafico_8_coluna_10, grafico_8_coluna_11, grafico_8_coluna_12,
       grafico_8_coluna_13, grafico_8_coluna_14, grafico_9_coluna_0, grafico_9_coluna_1, grafico_9_coluna_2,
       grafico_9_coluna_3, grafico_9_coluna_4, grafico_9_coluna_5, grafico_9_coluna_6, grafico_9_coluna_7,
       grafico_9_coluna_8, grafico_9_coluna_9, grafico_9_coluna_10, grafico_9_coluna_11, grafico_9_coluna_12,
       grafico_9_coluna_13, grafico_9_coluna_14, grafico_10_coluna_0, grafico_10_coluna_1,
       grafico_10_coluna_2, grafico_10_coluna_3, grafico_10_coluna_4, grafico_10_coluna_5,
       grafico_10_coluna_6, grafico_10_coluna_7, grafico_10_coluna_8, grafico_10_coluna_9,
       grafico_10_coluna_10, grafico_10_coluna_11, grafico_10_coluna_12, grafico_10_coluna_13,
       grafico_10_coluna_14, grafico_11_coluna_0, grafico_11_coluna_1, grafico_11_coluna_2,
       grafico_11_coluna_3, grafico_11_coluna_4, grafico_11_coluna_5, grafico_11_coluna_6,
       grafico_11_coluna_7, grafico_11_coluna_8, grafico_11_coluna_9, grafico_11_coluna_10,
       grafico_11_coluna_11, grafico_11_coluna_12, grafico_11_coluna_13, grafico_11_coluna_14,
       grafico_12_coluna_0, grafico_12_coluna_1, grafico_12_coluna_2, grafico_12_coluna_3,
       grafico_12_coluna_4, grafico_12_coluna_5, grafico_12_coluna_6, grafico_12_coluna_7,
       grafico_12_coluna_8, grafico_12_coluna_9, grafico_12_coluna_10, grafico_12_coluna_11,
       grafico_12_coluna_12, grafico_12_coluna_13, grafico_12_coluna_14, grafico_13_coluna_0,
       grafico_13_coluna_1, grafico_13_coluna_2, grafico_13_coluna_3, grafico_13_coluna_4,
       grafico_13_coluna_5, grafico_13_coluna_6, grafico_13_coluna_7, grafico_13_coluna_8,
       grafico_13_coluna_9, grafico_13_coluna_10, grafico_13_coluna_11, grafico_13_coluna_12,
       grafico_13_coluna_13, grafico_13_coluna_14, grafico_14_coluna_0, grafico_14_coluna_1,
       grafico_14_coluna_2, grafico_14_coluna_3, grafico_14_coluna_4, grafico_14_coluna_5,
       grafico_14_coluna_6, grafico_14_coluna_7, grafico_14_coluna_8, grafico_14_coluna_9,
       grafico_14_coluna_10, grafico_14_coluna_11, grafico_14_coluna_12, grafico_14_coluna_13,
       grafico_14_coluna_14, grafico_15_coluna_0, grafico_15_coluna_1, grafico_15_coluna_2,
       grafico_15_coluna_3, grafico_15_coluna_4, grafico_15_coluna_5, grafico_15_coluna_6,
       grafico_15_coluna_7, grafico_15_coluna_8, grafico_15_coluna_9, grafico_15_coluna_10,
       grafico_15_coluna_11, grafico_15_coluna_12, grafico_15_coluna_13, grafico_15_coluna_14,
       grafico_16_coluna_0, grafico_16_coluna_1, grafico_16_coluna_2, grafico_16_coluna_3,
       grafico_16_coluna_4, grafico_16_coluna_5, grafico_16_coluna_6, grafico_16_coluna_7,
       grafico_16_coluna_8, grafico_16_coluna_9, grafico_16_coluna_10, grafico_16_coluna_11,
       grafico_16_coluna_12, grafico_16_coluna_13, grafico_16_coluna_14, grafico_17_coluna_0,
       grafico_17_coluna_1, grafico_17_coluna_2, grafico_17_coluna_3, grafico_17_coluna_4,
       grafico_17_coluna_5, grafico_17_coluna_6, grafico_17_coluna_7, grafico_17_coluna_8,
       grafico_17_coluna_9, grafico_17_coluna_10, grafico_17_coluna_11, grafico_17_coluna_12,
       grafico_17_coluna_13, grafico_17_coluna_14, grafico_18_coluna_0, grafico_18_coluna_1,
       grafico_18_coluna_2, grafico_18_coluna_3, grafico_18_coluna_4, grafico_18_coluna_5,
       grafico_18_coluna_6, grafico_18_coluna_7, grafico_18_coluna_8, grafico_18_coluna_9,
       grafico_18_coluna_10, grafico_18_coluna_11, grafico_18_coluna_12, grafico_18_coluna_13,
       grafico_18_coluna_14, grafico_19_coluna_0, grafico_19_coluna_1, grafico_19_coluna_2,
       grafico_19_coluna_3, grafico_19_coluna_4, grafico_19_coluna_5, grafico_19_coluna_6,
       grafico_19_coluna_7, grafico_19_coluna_8, grafico_19_coluna_9, grafico_19_coluna_10,
       grafico_19_coluna_11, grafico_19_coluna_12, grafico_19_coluna_13, grafico_19_coluna_14,
       grafico_20_coluna_0, grafico_20_coluna_1, grafico_20_coluna_2, grafico_20_coluna_3,
       grafico_20_coluna_4, grafico_20_coluna_5, grafico_20_coluna_6, grafico_20_coluna_7,
       grafico_20_coluna_8, grafico_20_coluna_9, grafico_20_coluna_10, grafico_20_coluna_11,
       grafico_20_coluna_12, grafico_20_coluna_13, grafico_20_coluna_14, grafico_21_coluna_0,
       grafico_21_coluna_1, grafico_21_coluna_2, grafico_21_coluna_3, grafico_21_coluna_4,
       grafico_21_coluna_5, grafico_21_coluna_6, grafico_21_coluna_7, grafico_21_coluna_8,
       grafico_21_coluna_9, grafico_21_coluna_10, grafico_21_coluna_11, grafico_21_coluna_12,
       grafico_21_coluna_13, grafico_21_coluna_14, grafico_22_coluna_0, grafico_22_coluna_1,
       grafico_22_coluna_2, grafico_22_coluna_3, grafico_22_coluna_4, grafico_22_coluna_5,
       grafico_22_coluna_6, grafico_22_coluna_7, grafico_22_coluna_8, grafico_22_coluna_9,
       grafico_22_coluna_10, grafico_22_coluna_11, grafico_22_coluna_12, grafico_22_coluna_13,
       grafico_22_coluna_14, grafico_23_coluna_0, grafico_23_coluna_1, grafico_23_coluna_2,
       grafico_23_coluna_3, grafico_23_coluna_4, grafico_23_coluna_5, grafico_23_coluna_6,
       grafico_23_coluna_7, grafico_23_coluna_8, grafico_23_coluna_9, grafico_23_coluna_10,
       grafico_23_coluna_11, grafico_23_coluna_12, grafico_23_coluna_13, grafico_23_coluna_14,
       grafico_24_coluna_0, grafico_24_coluna_1, grafico_24_coluna_2, grafico_24_coluna_3,
       grafico_24_coluna_4, grafico_24_coluna_5, grafico_24_coluna_6, grafico_24_coluna_7,
       grafico_24_coluna_8, grafico_24_coluna_9, grafico_24_coluna_10, grafico_24_coluna_11,
       grafico_24_coluna_12, grafico_24_coluna_13, grafico_24_coluna_14, grafico_25_coluna_0,
       grafico_25_coluna_1, grafico_25_coluna_2, grafico_25_coluna_3, grafico_25_coluna_4,
       grafico_25_coluna_5, grafico_25_coluna_6, grafico_25_coluna_7, grafico_25_coluna_8,
       grafico_25_coluna_9, grafico_25_coluna_10, grafico_25_coluna_11, grafico_25_coluna_12,
       grafico_25_coluna_13, grafico_25_coluna_14, grafico_26_coluna_0, grafico_26_coluna_1,
       grafico_26_coluna_2, grafico_26_coluna_3, grafico_26_coluna_4, grafico_26_coluna_5,
       grafico_26_coluna_6, grafico_26_coluna_7, grafico_26_coluna_8, grafico_26_coluna_9,
       grafico_26_coluna_10, grafico_26_coluna_11, grafico_26_coluna_12, grafico_26_coluna_13,
       grafico_26_coluna_14, grafico_27_coluna_0, grafico_27_coluna_1, grafico_27_coluna_2,
       grafico_27_coluna_3, grafico_27_coluna_4, grafico_27_coluna_5, grafico_27_coluna_6,
       grafico_27_coluna_7, grafico_27_coluna_8, grafico_27_coluna_9, grafico_27_coluna_10,
       grafico_27_coluna_11, grafico_27_coluna_12, grafico_27_coluna_13, grafico_27_coluna_14,
       grafico_28_coluna_0, grafico_28_coluna_1, grafico_28_coluna_2, grafico_28_coluna_3,
       grafico_28_coluna_4, grafico_28_coluna_5, grafico_28_coluna_6, grafico_28_coluna_7,
       grafico_28_coluna_8, grafico_28_coluna_9, grafico_28_coluna_10, grafico_28_coluna_11,
       grafico_28_coluna_12, grafico_28_coluna_13, grafico_28_coluna_14, grafico_29_coluna_0,
       grafico_29_coluna_1, grafico_29_coluna_2, grafico_29_coluna_3, grafico_29_coluna_4,
       grafico_29_coluna_5, grafico_29_coluna_6, grafico_29_coluna_7, grafico_29_coluna_8,
       grafico_29_coluna_9, grafico_29_coluna_10, grafico_29_coluna_11, grafico_29_coluna_12,
       grafico_29_coluna_13, grafico_29_coluna_14, grafico_30_coluna_0, grafico_30_coluna_1,
       grafico_30_coluna_2, grafico_30_coluna_3, grafico_30_coluna_4, grafico_30_coluna_5,
       grafico_30_coluna_6, grafico_30_coluna_7, grafico_30_coluna_8, grafico_30_coluna_9,
       grafico_30_coluna_10, grafico_30_coluna_11, grafico_30_coluna_12, grafico_30_coluna_13,
       grafico_30_coluna_14, grafico_31_coluna_0, grafico_31_coluna_1, grafico_31_coluna_2,
       grafico_31_coluna_3, grafico_31_coluna_4, grafico_31_coluna_5, grafico_31_coluna_6,
       grafico_31_coluna_7, grafico_31_coluna_8, grafico_31_coluna_9, grafico_31_coluna_10,
       grafico_31_coluna_11, grafico_31_coluna_12, grafico_31_coluna_13, grafico_31_coluna_14,
       grafico_32_coluna_0, grafico_32_coluna_1, grafico_32_coluna_2, grafico_32_coluna_3,
       grafico_32_coluna_4, grafico_32_coluna_5, grafico_32_coluna_6, grafico_32_coluna_7,
       grafico_32_coluna_8, grafico_32_coluna_9, grafico_32_coluna_10, grafico_32_coluna_11,
       grafico_32_coluna_12, grafico_32_coluna_13, grafico_32_coluna_14, grafico_33_coluna_0,
       grafico_33_coluna_1, grafico_33_coluna_2, grafico_33_coluna_3, grafico_33_coluna_4,
       grafico_33_coluna_5, grafico_33_coluna_6, grafico_33_coluna_7, grafico_33_coluna_8,
       grafico_33_coluna_9, grafico_33_coluna_10, grafico_33_coluna_11, grafico_33_coluna_12,
       grafico_33_coluna_13, grafico_33_coluna_14;

  DotMatrix #(.matrixcols(15), .matrixrows(15)) dotmatrix_1 (
    .col0(grafico_1_coluna_0), .col1(grafico_1_coluna_1), .col2(grafico_1_coluna_2),
    .col3(grafico_1_coluna_3), .col4(grafico_1_coluna_4), .col5(grafico_1_coluna_5),
    .col6(grafico_1_coluna_6), .col7(grafico_1_coluna_7), .col8(grafico_1_coluna_8),
    .col9(grafico_1_coluna_9), .col10(grafico_1_coluna_10), .col11(grafico_1_coluna_11),
    .col12(grafico_1_coluna_12), .col13(grafico_1_coluna_13), .col14(grafico_1_coluna_14));
  GRAFICO grafico_1 (
    .COLUNA_0(grafico_1_coluna_0), .COLUNA_1(grafico_1_coluna_1), .COLUNA_2(grafico_1_coluna_2),
    .COLUNA_3(grafico_1_coluna_3), .COLUNA_4(grafico_1_coluna_4), .COLUNA_5(grafico_1_coluna_5),
    .COLUNA_6(grafico_1_coluna_6), .COLUNA_7(grafico_1_coluna_7), .COLUNA_8(grafico_1_coluna_8),
    .COLUNA_9(grafico_1_coluna_9), .COLUNA_10(grafico_1_coluna_10), .COLUNA_11(grafico_1_coluna_11),
    .COLUNA_12(grafico_1_coluna_12), .COLUNA_13(grafico_1_coluna_13), .COLUNA_14(grafico_1_coluna_14),
    .X(4'b0001), .Y(4'b0001));
  DotMatrix #(.matrixcols(15), .matrixrows(15)) dotmatrix_2 (
    .col0(grafico_2_coluna_0), .col1(grafico_2_coluna_1), .col2(grafico_2_coluna_2),
    .col3(grafico_2_coluna_3), .col4(grafico_2_coluna_4), .col5(grafico_2_coluna_5),
    .col6(grafico_2_coluna_6), .col7(grafico_2_coluna_7), .col8(grafico_2_coluna_8),
    .col9(grafico_2_coluna_9), .col10(grafico_2_coluna_10), .col11(grafico_2_coluna_11),
    .col12(grafico_2_coluna_12), .col13(grafico_2_coluna_13), .col14(grafico_2_coluna_14));
  GRAFICO grafico_2 (
    .COLUNA_0(grafico_2_coluna_0), .COLUNA_1(grafico_2_coluna_1), .COLUNA_2(grafico_2_coluna_2),
    .COLUNA_3(grafico_2_coluna_3), .COLUNA_4(grafico_2_coluna_4), .COLUNA_5(grafico_2_coluna_5),
    .COLUNA_6(grafico_2_coluna_6), .COLUNA_7(grafico_2_coluna_7), .COLUNA_8(grafico_2_coluna_8),
    .COLUNA_9(grafico_2_coluna_9), .COLUNA_10(grafico_2_coluna_10), .COLUNA_11(grafico_2_coluna_11),
    .COLUNA_12(grafico_2_coluna_12), .COLUNA_13(grafico_2_coluna_13), .COLUNA_14(grafico_2_coluna_14),
    .X(4'b1001), .Y(4'b1001));
  DotMatrix #(.matrixcols(15), .matrixrows(15)) dotmatrix_3 (
    .col0(grafico_3_coluna_0), .col1(grafico_3_coluna_1), .col2(grafico_3_coluna_2),
    .col3(grafico_3_coluna_3), .col4(grafico_3_coluna_4), .col5(grafico_3_coluna_5),
    .col6(grafico_3_coluna_6), .col7(grafico_3_coluna_7), .col8(grafico_3_coluna_8),
    .col9(grafico_3_coluna_9), .col10(grafico_3_coluna_10), .col11(grafico_3_coluna_11),
    .col12(grafico_3_coluna_12), .col13(grafico_3_coluna_13), .col14(grafico_3_coluna_14));
  GRAFICO grafico_3 (
    .COLUNA_0(grafico_3_coluna_0), .COLUNA_1(grafico_3_coluna_1), .COLUNA_2(grafico_3_coluna_2),
    .COLUNA_3(grafico_3_coluna_3), .COLUNA_4(grafico_3_coluna_4), .COLUNA_5(grafico_3_coluna_5),
    .COLUNA_6(grafico_3_coluna_6), .COLUNA_7(grafico_3_coluna_7), .COLUNA_8(grafico_3_coluna_8),
    .COLUNA_9(grafico_3_coluna_9), .COLUNA_10(grafico_3_coluna_10), .COLUNA_11(grafico_3_coluna_11),
    .COLUNA_12(grafico_3_coluna_12), .COLUNA_13(grafico_3_coluna_13), .COLUNA_14(grafico_3_coluna_14),
    .X(4'b0010), .Y(4'b0010));
  DotMatrix #(.matrixcols(15), .matrixrows(15)) dotmatrix_4 (
    .col0(grafico_4_coluna_0), .col1(grafico_4_coluna_1), .col2(grafico_4_coluna_2),
    .col3(grafico_4_coluna_3), .col4(grafico_4_coluna_4), .col5(grafico_4_coluna_5),
    .col6(grafico_4_coluna_6), .col7(grafico_4_coluna_7), .col8(grafico_4_coluna_8),
    .col9(grafico_4_coluna_9), .col10(grafico_4_coluna_10), .col11(grafico_4_coluna_11),
    .col12(grafico_4_coluna_12), .col13(grafico_4_coluna_13), .col14(grafico_4_coluna_14));
  GRAFICO grafico_4 (
    .COLUNA_0(grafico_4_coluna_0), .COLUNA_1(grafico_4_coluna_1), .COLUNA_2(grafico_4_coluna_2),
    .COLUNA_3(grafico_4_coluna_3), .COLUNA_4(grafico_4_coluna_4), .COLUNA_5(grafico_4_coluna_5),
    .COLUNA_6(grafico_4_coluna_6), .COLUNA_7(grafico_4_coluna_7), .COLUNA_8(grafico_4_coluna_8),
    .COLUNA_9(grafico_4_coluna_9), .COLUNA_10(grafico_4_coluna_10), .COLUNA_11(grafico_4_coluna_11),
    .COLUNA_12(grafico_4_coluna_12), .COLUNA_13(grafico_4_coluna_13), .COLUNA_14(grafico_4_coluna_14),
    .X(4'b1010), .Y(4'b1010));
  DotMatrix #(.matrixcols(15), .matrixrows(15)) dotmatrix_5 (
    .col0(grafico_5_coluna_0), .col1(grafico_5_coluna_1), .col2(grafico_5_coluna_2),
    .col3(grafico_5_coluna_3), .col4(grafico_5_coluna_4), .col5(grafico_5_coluna_5),
    .col6(grafico_5_coluna_6), .col7(grafico_5_coluna_7), .col8(grafico_5_coluna_8),
    .col9(grafico_5_coluna_9), .col10(grafico_5_coluna_10), .col11(grafico_5_coluna_11),
    .col12(grafico_5_coluna_12), .col13(grafico_5_coluna_13), .col14(grafico_5_coluna_14));
  GRAFICO grafico_5 (
    .COLUNA_0(grafico_5_coluna_0), .COLUNA_1(grafico_5_coluna_1), .COLUNA_2(grafico_5_coluna_2),
    .COLUNA_3(grafico_5_coluna_3), .COLUNA_4(grafico_5_coluna_4), .COLUNA_5(grafico_5_coluna_5),
    .COLUNA_6(grafico_5_coluna_6), .COLUNA_7(grafico_5_coluna_7), .COLUNA_8(grafico_5_coluna_8),
    .COLUNA_9(grafico_5_coluna_9), .COLUNA_10(grafico_5_coluna_10), .COLUNA_11(grafico_5_coluna_11),
    .COLUNA_12(grafico_5_coluna_12), .COLUNA_13(grafico_5_coluna_13), .COLUNA_14(grafico_5_coluna_14),
    .X(4'b0011), .Y(4'b0011));
  DotMatrix #(.matrixcols(15), .matrixrows(15)) dotmatrix_6 (
    .col0(grafico_6_coluna_0), .col1(grafico_6_coluna_1), .col2(grafico_6_coluna_2),
    .col3(grafico_6_coluna_3), .col4(grafico_6_coluna_4), .col5(grafico_6_coluna_5),
    .col6(grafico_6_coluna_6), .col7(grafico_6_coluna_7), .col8(grafico_6_coluna_8),
    .col9(grafico_6_coluna_9), .col10(grafico_6_coluna_10), .col11(grafico_6_coluna_11),
    .col12(grafico_6_coluna_12), .col13(grafico_6_coluna_13), .col14(grafico_6_coluna_14));
  GRAFICO grafico_6 (
    .COLUNA_0(grafico_6_coluna_0), .COLUNA_1(grafico_6_coluna_1), .COLUNA_2(grafico_6_coluna_2),
    .COLUNA_3(grafico_6_coluna_3), .COLUNA_4(grafico_6_coluna_4), .COLUNA_5(grafico_6_coluna_5),
    .COLUNA_6(grafico_6_coluna_6), .COLUNA_7(grafico_6_coluna_7), .COLUNA_8(grafico_6_coluna_8),
    .COLUNA_9(grafico_6_coluna_9), .COLUNA_10(grafico_6_coluna_10), .COLUNA_11(grafico_6_coluna_11),
    .COLUNA_12(grafico_6_coluna_12), .COLUNA_13(grafico_6_coluna_13), .COLUNA_14(grafico_6_coluna_14),
    .X(4'b1011), .Y(4'b1011));
  DotMatrix #(.matrixcols(15), .matrixrows(15)) dotmatrix_7 (
    .col0(grafico_7_coluna_0), .col1(grafico_7_coluna_1), .col2(grafico_7_coluna_2),
    .col3(grafico_7_coluna_3), .col4(grafico_7_coluna_4), .col5(grafico_7_coluna_5),
    .col6(grafico_7_coluna_6), .col7(grafico_7_coluna_7), .col8(grafico_7_coluna_8),
    .col9(grafico_7_coluna_9), .col10(grafico_7_coluna_10), .col11(grafico_7_coluna_11),
    .col12(grafico_7_coluna_12), .col13(grafico_7_coluna_13), .col14(grafico_7_coluna_14));
  GRAFICO grafico_7 (
    .COLUNA_0(grafico_7_coluna_0), .COLUNA_1(grafico_7_coluna_1), .COLUNA_2(grafico_7_coluna_2),
    .COLUNA_3(grafico_7_coluna_3), .COLUNA_4(grafico_7_coluna_4), .COLUNA_5(grafico_7_coluna_5),
    .COLUNA_6(grafico_7_coluna_6), .COLUNA_7(grafico_7_coluna_7), .COLUNA_8(grafico_7_coluna_8),
    .COLUNA_9(grafico_7_coluna_9), .COLUNA_10(grafico_7_coluna_10), .COLUNA_11(grafico_7_coluna_11),
    .COLUNA_12(grafico_7_coluna_12), .COLUNA_13(grafico_7_coluna_13), .COLUNA_14(grafico_7_coluna_14),
    .X(4'b0100), .Y(4'b0100));
  DotMatrix #(.matrixcols(15), .matrixrows(15)) dotmatrix_8 (
    .col0(grafico_8_coluna_0), .col1(grafico_8_coluna_1), .col2(grafico_8_coluna_2),
    .col3(grafico_8_coluna_3), .col4(grafico_8_coluna_4), .col5(grafico_8_coluna_5),
    .col6(grafico_8_coluna_6), .col7(grafico_8_coluna_7), .col8(grafico_8_coluna_8),
    .col9(grafico_8_coluna_9), .col10(grafico_8_coluna_10), .col11(grafico_8_coluna_11),
    .col12(grafico_8_coluna_12), .col13(grafico_8_coluna_13), .col14(grafico_8_coluna_14));
  GRAFICO grafico_8 (
    .COLUNA_0(grafico_8_coluna_0), .COLUNA_1(grafico_8_coluna_1), .COLUNA_2(grafico_8_coluna_2),
    .COLUNA_3(grafico_8_coluna_3), .COLUNA_4(grafico_8_coluna_4), .COLUNA_5(grafico_8_coluna_5),
    .COLUNA_6(grafico_8_coluna_6), .COLUNA_7(grafico_8_coluna_7), .COLUNA_8(grafico_8_coluna_8),
    .COLUNA_9(grafico_8_coluna_9), .COLUNA_10(grafico_8_coluna_10), .COLUNA_11(grafico_8_coluna_11),
    .COLUNA_12(grafico_8_coluna_12), .COLUNA_13(grafico_8_coluna_13), .COLUNA_14(grafico_8_coluna_14),
    .X(4'b1100), .Y(4'b1100));
  DotMatrix #(.matrixcols(15), .matrixrows(15)) dotmatrix_9 (
    .col0(grafico_9_coluna_0), .col1(grafico_9_coluna_1), .col2(grafico_9_coluna_2),
    .col3(grafico_9_coluna_3), .col4(grafico_9_coluna_4), .col5(grafico_9_coluna_5),
    .col6(grafico_9_coluna_6), .col7(grafico_9_coluna_7), .col8(grafico_9_coluna_8),
    .col9(grafico_9_coluna_9), .col10(grafico_9_coluna_10), .col11(grafico_9_coluna_11),
    .col12(grafico_9_coluna_12), .col13(grafico_9_coluna_13), .col14(grafico_9_coluna_14));
  GRAFICO grafico_9 (
    .COLUNA_0(grafico_9_coluna_0), .COLUNA_1(grafico_9_coluna_1), .COLUNA_2(grafico_9_coluna_2),
    .COLUNA_3(grafico_9_coluna_3), .COLUNA_4(grafico_9_coluna_4), .COLUNA_5(grafico_9_coluna_5),
    .COLUNA_6(grafico_9_coluna_6), .COLUNA_7(grafico_9_coluna_7), .COLUNA_8(grafico_9_coluna_8),
    .COLUNA_9(grafico_9_coluna_9), .COLUNA_10(grafico_9_coluna_10), .COLUNA_11(grafico_9_coluna_11),
    .COLUNA_12(grafico_9_coluna_12), .COLUNA_13(grafico_9_coluna_13), .COLUNA_14(grafico_9_coluna_14),
    .X(4'b0101), .Y(4'b0101));
  DotMatrix #(.matrixcols(15), .matrixrows(15)) dotmatrix_10 (
    .col0(grafico_10_coluna_0), .col1(grafico_10_coluna_1), .col2(grafico_10_coluna_2),
    .col3(grafico_10_coluna_3), .col4(grafico_10_coluna_4), .col5(grafico_10_coluna_5),
    .col6(grafico_10_coluna_6), .col7(grafico_10_coluna_7), .col8(grafico_10_coluna_8),
    .col9(grafico_10_coluna_9), .col10(grafico_10_coluna_10), .col11(grafico_10_coluna_11),
    .col12(grafico_10_coluna_12), .col13(grafico_10_coluna_13), .col14(grafico_10_coluna_14));
  GRAFICO grafico_10 (
    .COLUNA_0(grafico_10_coluna_0), .COLUNA_1(grafico_10_coluna_1), .COLUNA_2(grafico_10_coluna_2),
    .COLUNA_3(grafico_10_coluna_3), .COLUNA_4(grafico_10_coluna_4), .COLUNA_5(grafico_10_coluna_5),
    .COLUNA_6(grafico_10_coluna_6), .COLUNA_7(grafico_10_coluna_7), .COLUNA_8(grafico_10_coluna_8),
    .COLUNA_9(grafico_10_coluna_9), .COLUNA_10(grafico_10_coluna_10), .COLUNA_11(grafico_10_coluna_11),
    .COLUNA_12(grafico_10_coluna_12), .COLUNA_13(grafico_10_coluna_13), .COLUNA_14(grafico_10_coluna_14),
    .X(4'b1101), .Y(4'b1101));
  DotMatrix #(.matrixcols(15), .matrixrows(15)) dotmatrix_11 (
    .col0(grafico_11_coluna_0), .col1(grafico_11_coluna_1), .col2(grafico_11_coluna_2),
    .col3(grafico_11_coluna_3), .col4(grafico_11_coluna_4), .col5(grafico_11_coluna_5),
    .col6(grafico_11_coluna_6), .col7(grafico_11_coluna_7), .col8(grafico_11_coluna_8),
    .col9(grafico_11_coluna_9), .col10(grafico_11_coluna_10), .col11(grafico_11_coluna_11),
    .col12(grafico_11_coluna_12), .col13(grafico_11_coluna_13), .col14(grafico_11_coluna_14));
  GRAFICO grafico_11 (
    .COLUNA_0(grafico_11_coluna_0), .COLUNA_1(grafico_11_coluna_1), .COLUNA_2(grafico_11_coluna_2),
    .COLUNA_3(grafico_11_coluna_3), .COLUNA_4(grafico_11_coluna_4), .COLUNA_5(grafico_11_coluna_5),
    .COLUNA_6(grafico_11_coluna_6), .COLUNA_7(grafico_11_coluna_7), .COLUNA_8(grafico_11_coluna_8),
    .COLUNA_9(grafico_11_coluna_9), .COLUNA_10(grafico_11_coluna_10), .COLUNA_11(grafico_11_coluna_11),
    .COLUNA_12(grafico_11_coluna_12), .COLUNA_13(grafico_11_coluna_13), .COLUNA_14(grafico_11_coluna_14),
    .X(4'b0110), .Y(4'b0110));
  DotMatrix #(.matrixcols(15), .matrixrows(15)) dotmatrix_12 (
    .col0(grafico_12_coluna_0), .col1(grafico_12_coluna_1), .col2(grafico_12_coluna_2),
    .col3(grafico_12_coluna_3), .col4(grafico_12_coluna_4), .col5(grafico_12_coluna_5),
    .col6(grafico_12_coluna_6), .col7(grafico_12_coluna_7), .col8(grafico_12_coluna_8),
    .col9(grafico_12_coluna_9), .col10(grafico_12_coluna_10), .col11(grafico_12_coluna_11),
    .col12(grafico_12_coluna_12), .col13(grafico_12_coluna_13), .col14(grafico_12_coluna_14));
  GRAFICO grafico_12 (
    .COLUNA_0(grafico_12_coluna_0), .COLUNA_1(grafico_12_coluna_1), .COLUNA_2(grafico_12_coluna_2),
    .COLUNA_3(grafico_12_coluna_3), .COLUNA_4(grafico_12_coluna_4), .COLUNA_5(grafico_12_coluna_5),
    .COLUNA_6(grafico_12_coluna_6), .COLUNA_7(grafico_12_coluna_7), .COLUNA_8(grafico_12_coluna_8),
    .COLUNA_9(grafico_12_coluna_9), .COLUNA_10(grafico_12_coluna_10), .COLUNA_11(grafico_12_coluna_11),
    .COLUNA_12(grafico_12_coluna_12), .COLUNA_13(grafico_12_coluna_13), .COLUNA_14(grafico_12_coluna_14),
    .X(4'b1110), .Y(4'b1110));
  DotMatrix #(.matrixcols(15), .matrixrows(15)) dotmatrix_13 (
    .col0(grafico_13_coluna_0), .col1(grafico_13_coluna_1), .col2(grafico_13_coluna_2),
    .col3(grafico_13_coluna_3), .col4(grafico_13_coluna_4), .col5(grafico_13_coluna_5),
    .col6(grafico_13_coluna_6), .col7(grafico_13_coluna_7), .col8(grafico_13_coluna_8),
    .col9(grafico_13_coluna_9), .col10(grafico_13_coluna_10), .col11(grafico_13_coluna_11),
    .col12(grafico_13_coluna_12), .col13(grafico_13_coluna_13), .col14(grafico_13_coluna_14));
  GRAFICO grafico_13 (
    .COLUNA_0(grafico_13_coluna_0), .COLUNA_1(grafico_13_coluna_1), .COLUNA_2(grafico_13_coluna_2),
    .COLUNA_3(grafico_13_coluna_3), .COLUNA_4(grafico_13_coluna_4), .COLUNA_5(grafico_13_coluna_5),
    .COLUNA_6(grafico_13_coluna_6), .COLUNA_7(grafico_13_coluna_7), .COLUNA_8(grafico_13_coluna_8),
    .COLUNA_9(grafico_13_coluna_9), .COLUNA_10(grafico_13_coluna_10), .COLUNA_11(grafico_13_coluna_11),
    .COLUNA_12(grafico_13_coluna_12), .COLUNA_13(grafico_13_coluna_13), .COLUNA_14(grafico_13_coluna_14),
    .X(4'b0111), .Y(4'b0111));
  DotMatrix #(.matrixcols(15), .matrixrows(15)) dotmatrix_14 (
    .col0(grafico_14_coluna_0), .col1(grafico_14_coluna_1), .col2(grafico_14_coluna_2),
    .col3(grafico_14_coluna_3), .col4(grafico_14_coluna_4), .col5(grafico_14_coluna_5),
    .col6(grafico_14_coluna_6), .col7(grafico_14_coluna_7), .col8(grafico_14_coluna_8),
    .col9(grafico_14_coluna_9), .col10(grafico_14_coluna_10), .col11(grafico_14_coluna_11),
    .col12(grafico_14_coluna_12), .col13(grafico_14_coluna_13), .col14(grafico_14_coluna_14));
  GRAFICO grafico_14 (
    .COLUNA_0(grafico_14_coluna_0), .COLUNA_1(grafico_14_coluna_1), .COLUNA_2(grafico_14_coluna_2),
    .COLUNA_3(grafico_14_coluna_3), .COLUNA_4(grafico_14_coluna_4), .COLUNA_5(grafico_14_coluna_5),
    .COLUNA_6(grafico_14_coluna_6), .COLUNA_7(grafico_14_coluna_7), .COLUNA_8(grafico_14_coluna_8),
    .COLUNA_9(grafico_14_coluna_9), .COLUNA_10(grafico_14_coluna_10), .COLUNA_11(grafico_14_coluna_11),
    .COLUNA_12(grafico_14_coluna_12), .COLUNA_13(grafico_14_coluna_13), .COLUNA_14(grafico_14_coluna_14),
    .X(4'b1111), .Y(4'b1111));
  DotMatrix #(.matrixcols(15), .matrixrows(15)) dotmatrix_15 (
    .col0(grafico_15_coluna_0), .col1(grafico_15_coluna_1), .col2(grafico_15_coluna_2),
    .col3(grafico_15_coluna_3), .col4(grafico_15_coluna_4), .col5(grafico_15_coluna_5),
    .col6(grafico_15_coluna_6), .col7(grafico_15_coluna_7), .col8(grafico_15_coluna_8),
    .col9(grafico_15_coluna_9), .col10(grafico_15_coluna_10), .col11(grafico_15_coluna_11),
    .col12(grafico_15_coluna_12), .col13(grafico_15_coluna_13), .col14(grafico_15_coluna_14));
  GRAFICO grafico_15 (
    .COLUNA_0(grafico_15_coluna_0), .COLUNA_1(grafico_15_coluna_1), .COLUNA_2(grafico_15_coluna_2),
    .COLUNA_3(grafico_15_coluna_3), .COLUNA_4(grafico_15_coluna_4), .COLUNA_5(grafico_15_coluna_5),
    .COLUNA_6(grafico_15_coluna_6), .COLUNA_7(grafico_15_coluna_7), .COLUNA_8(grafico_15_coluna_8),
    .COLUNA_9(grafico_15_coluna_9), .COLUNA_10(grafico_15_coluna_10), .COLUNA_11(grafico_15_coluna_11),
    .COLUNA_12(grafico_15_coluna_12), .COLUNA_13(grafico_15_coluna_13), .COLUNA_14(grafico_15_coluna_14),
    .X(counter_1_q), .Y(counter_1_q));
  Counter #(.width(4), .max('hf)) counter_1 (
    .Q(counter_1_q), .clk(clock_1_out));  // open: load, D, count, carry, clr, preset, down
  Clock clock_1 (.out(clock_1_out));
  DotMatrix #(.matrixcols(15), .matrixrows(15)) dotmatrix_16 (
    .col0(grafico_16_coluna_0), .col1(grafico_16_coluna_1), .col2(grafico_16_coluna_2),
    .col3(grafico_16_coluna_3), .col4(grafico_16_coluna_4), .col5(grafico_16_coluna_5),
    .col6(grafico_16_coluna_6), .col7(grafico_16_coluna_7), .col8(grafico_16_coluna_8),
    .col9(grafico_16_coluna_9), .col10(grafico_16_coluna_10), .col11(grafico_16_coluna_11),
    .col12(grafico_16_coluna_12), .col13(grafico_16_coluna_13), .col14(grafico_16_coluna_14));
  GRAFICO grafico_16 (
    .COLUNA_0(grafico_16_coluna_0), .COLUNA_1(grafico_16_coluna_1), .COLUNA_2(grafico_16_coluna_2),
    .COLUNA_3(grafico_16_coluna_3), .COLUNA_4(grafico_16_coluna_4), .COLUNA_5(grafico_16_coluna_5),
    .COLUNA_6(grafico_16_coluna_6), .COLUNA_7(grafico_16_coluna_7), .COLUNA_8(grafico_16_coluna_8),
    .COLUNA_9(grafico_16_coluna_9), .COLUNA_10(grafico_16_coluna_10), .COLUNA_11(grafico_16_coluna_11),
    .COLUNA_12(grafico_16_coluna_12), .COLUNA_13(grafico_16_coluna_13), .COLUNA_14(grafico_16_coluna_14),
    .X(4'b1000), .Y(4'b1000));
  DotMatrix #(.matrixcols(15), .matrixrows(15)) dotmatrix_17 (
    .col0(grafico_17_coluna_0), .col1(grafico_17_coluna_1), .col2(grafico_17_coluna_2),
    .col3(grafico_17_coluna_3), .col4(grafico_17_coluna_4), .col5(grafico_17_coluna_5),
    .col6(grafico_17_coluna_6), .col7(grafico_17_coluna_7), .col8(grafico_17_coluna_8),
    .col9(grafico_17_coluna_9), .col10(grafico_17_coluna_10), .col11(grafico_17_coluna_11),
    .col12(grafico_17_coluna_12), .col13(grafico_17_coluna_13), .col14(grafico_17_coluna_14));
  GRAFICO grafico_17 (
    .COLUNA_0(grafico_17_coluna_0), .COLUNA_1(grafico_17_coluna_1), .COLUNA_2(grafico_17_coluna_2),
    .COLUNA_3(grafico_17_coluna_3), .COLUNA_4(grafico_17_coluna_4), .COLUNA_5(grafico_17_coluna_5),
    .COLUNA_6(grafico_17_coluna_6), .COLUNA_7(grafico_17_coluna_7), .COLUNA_8(grafico_17_coluna_8),
    .COLUNA_9(grafico_17_coluna_9), .COLUNA_10(grafico_17_coluna_10), .COLUNA_11(grafico_17_coluna_11),
    .COLUNA_12(grafico_17_coluna_12), .COLUNA_13(grafico_17_coluna_13), .COLUNA_14(grafico_17_coluna_14),
    .X(adder_1_out), .Y(counter_2_q));
  Counter #(.width(4), .max('hf)) counter_2 (
    .Q(counter_2_q), .clk(clock_2_out));  // open: load, D, count, carry, clr, preset, down
  Clock clock_2 (.out(clock_2_out));
  DotMatrix #(.matrixcols(15), .matrixrows(15)) dotmatrix_18 (
    .col0(grafico_18_coluna_0), .col1(grafico_18_coluna_1), .col2(grafico_18_coluna_2),
    .col3(grafico_18_coluna_3), .col4(grafico_18_coluna_4), .col5(grafico_18_coluna_5),
    .col6(grafico_18_coluna_6), .col7(grafico_18_coluna_7), .col8(grafico_18_coluna_8),
    .col9(grafico_18_coluna_9), .col10(grafico_18_coluna_10), .col11(grafico_18_coluna_11),
    .col12(grafico_18_coluna_12), .col13(grafico_18_coluna_13), .col14(grafico_18_coluna_14));
  GRAFICO grafico_18 (
    .COLUNA_0(grafico_18_coluna_0), .COLUNA_1(grafico_18_coluna_1), .COLUNA_2(grafico_18_coluna_2),
    .COLUNA_3(grafico_18_coluna_3), .COLUNA_4(grafico_18_coluna_4), .COLUNA_5(grafico_18_coluna_5),
    .COLUNA_6(grafico_18_coluna_6), .COLUNA_7(grafico_18_coluna_7), .COLUNA_8(grafico_18_coluna_8),
    .COLUNA_9(grafico_18_coluna_9), .COLUNA_10(grafico_18_coluna_10), .COLUNA_11(grafico_18_coluna_11),
    .COLUNA_12(grafico_18_coluna_12), .COLUNA_13(grafico_18_coluna_13), .COLUNA_14(grafico_18_coluna_14),
    .X(4'b1111), .Y(4'b0001));
  DotMatrix #(.matrixcols(15), .matrixrows(15)) dotmatrix_19 (
    .col0(grafico_19_coluna_0), .col1(grafico_19_coluna_1), .col2(grafico_19_coluna_2),
    .col3(grafico_19_coluna_3), .col4(grafico_19_coluna_4), .col5(grafico_19_coluna_5),
    .col6(grafico_19_coluna_6), .col7(grafico_19_coluna_7), .col8(grafico_19_coluna_8),
    .col9(grafico_19_coluna_9), .col10(grafico_19_coluna_10), .col11(grafico_19_coluna_11),
    .col12(grafico_19_coluna_12), .col13(grafico_19_coluna_13), .col14(grafico_19_coluna_14));
  GRAFICO grafico_19 (
    .COLUNA_0(grafico_19_coluna_0), .COLUNA_1(grafico_19_coluna_1), .COLUNA_2(grafico_19_coluna_2),
    .COLUNA_3(grafico_19_coluna_3), .COLUNA_4(grafico_19_coluna_4), .COLUNA_5(grafico_19_coluna_5),
    .COLUNA_6(grafico_19_coluna_6), .COLUNA_7(grafico_19_coluna_7), .COLUNA_8(grafico_19_coluna_8),
    .COLUNA_9(grafico_19_coluna_9), .COLUNA_10(grafico_19_coluna_10), .COLUNA_11(grafico_19_coluna_11),
    .COLUNA_12(grafico_19_coluna_12), .COLUNA_13(grafico_19_coluna_13), .COLUNA_14(grafico_19_coluna_14),
    .X(4'b0111), .Y(4'b1001));
  Adder #(.width(4)) adder_1 (.a(4'b0001), .b(subtractor_1_out), .out(adder_1_out));  // open: cin, cout
  DotMatrix #(.matrixcols(15), .matrixrows(15)) dotmatrix_20 (
    .col0(grafico_20_coluna_0), .col1(grafico_20_coluna_1), .col2(grafico_20_coluna_2),
    .col3(grafico_20_coluna_3), .col4(grafico_20_coluna_4), .col5(grafico_20_coluna_5),
    .col6(grafico_20_coluna_6), .col7(grafico_20_coluna_7), .col8(grafico_20_coluna_8),
    .col9(grafico_20_coluna_9), .col10(grafico_20_coluna_10), .col11(grafico_20_coluna_11),
    .col12(grafico_20_coluna_12), .col13(grafico_20_coluna_13), .col14(grafico_20_coluna_14));
  GRAFICO grafico_20 (
    .COLUNA_0(grafico_20_coluna_0), .COLUNA_1(grafico_20_coluna_1), .COLUNA_2(grafico_20_coluna_2),
    .COLUNA_3(grafico_20_coluna_3), .COLUNA_4(grafico_20_coluna_4), .COLUNA_5(grafico_20_coluna_5),
    .COLUNA_6(grafico_20_coluna_6), .COLUNA_7(grafico_20_coluna_7), .COLUNA_8(grafico_20_coluna_8),
    .COLUNA_9(grafico_20_coluna_9), .COLUNA_10(grafico_20_coluna_10), .COLUNA_11(grafico_20_coluna_11),
    .COLUNA_12(grafico_20_coluna_12), .COLUNA_13(grafico_20_coluna_13), .COLUNA_14(grafico_20_coluna_14),
    .X(4'b1110), .Y(4'b0010));
  DotMatrix #(.matrixcols(15), .matrixrows(15)) dotmatrix_21 (
    .col0(grafico_21_coluna_0), .col1(grafico_21_coluna_1), .col2(grafico_21_coluna_2),
    .col3(grafico_21_coluna_3), .col4(grafico_21_coluna_4), .col5(grafico_21_coluna_5),
    .col6(grafico_21_coluna_6), .col7(grafico_21_coluna_7), .col8(grafico_21_coluna_8),
    .col9(grafico_21_coluna_9), .col10(grafico_21_coluna_10), .col11(grafico_21_coluna_11),
    .col12(grafico_21_coluna_12), .col13(grafico_21_coluna_13), .col14(grafico_21_coluna_14));
  GRAFICO grafico_21 (
    .COLUNA_0(grafico_21_coluna_0), .COLUNA_1(grafico_21_coluna_1), .COLUNA_2(grafico_21_coluna_2),
    .COLUNA_3(grafico_21_coluna_3), .COLUNA_4(grafico_21_coluna_4), .COLUNA_5(grafico_21_coluna_5),
    .COLUNA_6(grafico_21_coluna_6), .COLUNA_7(grafico_21_coluna_7), .COLUNA_8(grafico_21_coluna_8),
    .COLUNA_9(grafico_21_coluna_9), .COLUNA_10(grafico_21_coluna_10), .COLUNA_11(grafico_21_coluna_11),
    .COLUNA_12(grafico_21_coluna_12), .COLUNA_13(grafico_21_coluna_13), .COLUNA_14(grafico_21_coluna_14),
    .X(4'b0110), .Y(4'b1010));
  Subtractor #(.width(4)) subtractor_1 (
    .a(4'b1111), .b(counter_2_q), .out(subtractor_1_out), .bout(subtractor_1_bout));  // open: bin
  Clock clock_3 (.out(clock_3_out));
  DotMatrix #(.matrixcols(15), .matrixrows(15)) dotmatrix_22 (
    .col0(grafico_22_coluna_0), .col1(grafico_22_coluna_1), .col2(grafico_22_coluna_2),
    .col3(grafico_22_coluna_3), .col4(grafico_22_coluna_4), .col5(grafico_22_coluna_5),
    .col6(grafico_22_coluna_6), .col7(grafico_22_coluna_7), .col8(grafico_22_coluna_8),
    .col9(grafico_22_coluna_9), .col10(grafico_22_coluna_10), .col11(grafico_22_coluna_11),
    .col12(grafico_22_coluna_12), .col13(grafico_22_coluna_13), .col14(grafico_22_coluna_14));
  GRAFICO grafico_22 (
    .COLUNA_0(grafico_22_coluna_0), .COLUNA_1(grafico_22_coluna_1), .COLUNA_2(grafico_22_coluna_2),
    .COLUNA_3(grafico_22_coluna_3), .COLUNA_4(grafico_22_coluna_4), .COLUNA_5(grafico_22_coluna_5),
    .COLUNA_6(grafico_22_coluna_6), .COLUNA_7(grafico_22_coluna_7), .COLUNA_8(grafico_22_coluna_8),
    .COLUNA_9(grafico_22_coluna_9), .COLUNA_10(grafico_22_coluna_10), .COLUNA_11(grafico_22_coluna_11),
    .COLUNA_12(grafico_22_coluna_12), .COLUNA_13(grafico_22_coluna_13), .COLUNA_14(grafico_22_coluna_14),
    .X(counter_4_q), .Y(counter_3_q));
  Counter #(.width(4), .max('hf)) counter_3 (
    .Q(counter_3_q), .clk(counter_4_carry));  // open: load, D, count, carry, clr, preset, down
  Counter #(.width(4), .max('hf)) counter_4 (
    .Q(counter_4_q), .carry(counter_4_carry), .clk(clock_3_out));  // open: load, D, count, clr, preset, down
  DotMatrix #(.matrixcols(15), .matrixrows(15)) dotmatrix_23 (
    .col0(grafico_23_coluna_0), .col1(grafico_23_coluna_1), .col2(grafico_23_coluna_2),
    .col3(grafico_23_coluna_3), .col4(grafico_23_coluna_4), .col5(grafico_23_coluna_5),
    .col6(grafico_23_coluna_6), .col7(grafico_23_coluna_7), .col8(grafico_23_coluna_8),
    .col9(grafico_23_coluna_9), .col10(grafico_23_coluna_10), .col11(grafico_23_coluna_11),
    .col12(grafico_23_coluna_12), .col13(grafico_23_coluna_13), .col14(grafico_23_coluna_14));
  GRAFICO grafico_23 (
    .COLUNA_0(grafico_23_coluna_0), .COLUNA_1(grafico_23_coluna_1), .COLUNA_2(grafico_23_coluna_2),
    .COLUNA_3(grafico_23_coluna_3), .COLUNA_4(grafico_23_coluna_4), .COLUNA_5(grafico_23_coluna_5),
    .COLUNA_6(grafico_23_coluna_6), .COLUNA_7(grafico_23_coluna_7), .COLUNA_8(grafico_23_coluna_8),
    .COLUNA_9(grafico_23_coluna_9), .COLUNA_10(grafico_23_coluna_10), .COLUNA_11(grafico_23_coluna_11),
    .COLUNA_12(grafico_23_coluna_12), .COLUNA_13(grafico_23_coluna_13), .COLUNA_14(grafico_23_coluna_14),
    .X(4'b1101), .Y(4'b0011));
  DotMatrix #(.matrixcols(15), .matrixrows(15)) dotmatrix_24 (
    .col0(grafico_24_coluna_0), .col1(grafico_24_coluna_1), .col2(grafico_24_coluna_2),
    .col3(grafico_24_coluna_3), .col4(grafico_24_coluna_4), .col5(grafico_24_coluna_5),
    .col6(grafico_24_coluna_6), .col7(grafico_24_coluna_7), .col8(grafico_24_coluna_8),
    .col9(grafico_24_coluna_9), .col10(grafico_24_coluna_10), .col11(grafico_24_coluna_11),
    .col12(grafico_24_coluna_12), .col13(grafico_24_coluna_13), .col14(grafico_24_coluna_14));
  GRAFICO grafico_24 (
    .COLUNA_0(grafico_24_coluna_0), .COLUNA_1(grafico_24_coluna_1), .COLUNA_2(grafico_24_coluna_2),
    .COLUNA_3(grafico_24_coluna_3), .COLUNA_4(grafico_24_coluna_4), .COLUNA_5(grafico_24_coluna_5),
    .COLUNA_6(grafico_24_coluna_6), .COLUNA_7(grafico_24_coluna_7), .COLUNA_8(grafico_24_coluna_8),
    .COLUNA_9(grafico_24_coluna_9), .COLUNA_10(grafico_24_coluna_10), .COLUNA_11(grafico_24_coluna_11),
    .COLUNA_12(grafico_24_coluna_12), .COLUNA_13(grafico_24_coluna_13), .COLUNA_14(grafico_24_coluna_14),
    .X(4'b0101), .Y(4'b1011));
  DotMatrix #(.matrixcols(15), .matrixrows(15)) dotmatrix_25 (
    .col0(grafico_25_coluna_0), .col1(grafico_25_coluna_1), .col2(grafico_25_coluna_2),
    .col3(grafico_25_coluna_3), .col4(grafico_25_coluna_4), .col5(grafico_25_coluna_5),
    .col6(grafico_25_coluna_6), .col7(grafico_25_coluna_7), .col8(grafico_25_coluna_8),
    .col9(grafico_25_coluna_9), .col10(grafico_25_coluna_10), .col11(grafico_25_coluna_11),
    .col12(grafico_25_coluna_12), .col13(grafico_25_coluna_13), .col14(grafico_25_coluna_14));
  GRAFICO grafico_25 (
    .COLUNA_0(grafico_25_coluna_0), .COLUNA_1(grafico_25_coluna_1), .COLUNA_2(grafico_25_coluna_2),
    .COLUNA_3(grafico_25_coluna_3), .COLUNA_4(grafico_25_coluna_4), .COLUNA_5(grafico_25_coluna_5),
    .COLUNA_6(grafico_25_coluna_6), .COLUNA_7(grafico_25_coluna_7), .COLUNA_8(grafico_25_coluna_8),
    .COLUNA_9(grafico_25_coluna_9), .COLUNA_10(grafico_25_coluna_10), .COLUNA_11(grafico_25_coluna_11),
    .COLUNA_12(grafico_25_coluna_12), .COLUNA_13(grafico_25_coluna_13), .COLUNA_14(grafico_25_coluna_14),
    .X(4'b1100), .Y(4'b0100));
  DotMatrix #(.matrixcols(15), .matrixrows(15)) dotmatrix_26 (
    .col0(grafico_26_coluna_0), .col1(grafico_26_coluna_1), .col2(grafico_26_coluna_2),
    .col3(grafico_26_coluna_3), .col4(grafico_26_coluna_4), .col5(grafico_26_coluna_5),
    .col6(grafico_26_coluna_6), .col7(grafico_26_coluna_7), .col8(grafico_26_coluna_8),
    .col9(grafico_26_coluna_9), .col10(grafico_26_coluna_10), .col11(grafico_26_coluna_11),
    .col12(grafico_26_coluna_12), .col13(grafico_26_coluna_13), .col14(grafico_26_coluna_14));
  GRAFICO grafico_26 (
    .COLUNA_0(grafico_26_coluna_0), .COLUNA_1(grafico_26_coluna_1), .COLUNA_2(grafico_26_coluna_2),
    .COLUNA_3(grafico_26_coluna_3), .COLUNA_4(grafico_26_coluna_4), .COLUNA_5(grafico_26_coluna_5),
    .COLUNA_6(grafico_26_coluna_6), .COLUNA_7(grafico_26_coluna_7), .COLUNA_8(grafico_26_coluna_8),
    .COLUNA_9(grafico_26_coluna_9), .COLUNA_10(grafico_26_coluna_10), .COLUNA_11(grafico_26_coluna_11),
    .COLUNA_12(grafico_26_coluna_12), .COLUNA_13(grafico_26_coluna_13), .COLUNA_14(grafico_26_coluna_14),
    .X(4'b0100), .Y(4'b1100));
  DotMatrix #(.matrixcols(15), .matrixrows(15)) dotmatrix_27 (
    .col0(grafico_27_coluna_0), .col1(grafico_27_coluna_1), .col2(grafico_27_coluna_2),
    .col3(grafico_27_coluna_3), .col4(grafico_27_coluna_4), .col5(grafico_27_coluna_5),
    .col6(grafico_27_coluna_6), .col7(grafico_27_coluna_7), .col8(grafico_27_coluna_8),
    .col9(grafico_27_coluna_9), .col10(grafico_27_coluna_10), .col11(grafico_27_coluna_11),
    .col12(grafico_27_coluna_12), .col13(grafico_27_coluna_13), .col14(grafico_27_coluna_14));
  GRAFICO grafico_27 (
    .COLUNA_0(grafico_27_coluna_0), .COLUNA_1(grafico_27_coluna_1), .COLUNA_2(grafico_27_coluna_2),
    .COLUNA_3(grafico_27_coluna_3), .COLUNA_4(grafico_27_coluna_4), .COLUNA_5(grafico_27_coluna_5),
    .COLUNA_6(grafico_27_coluna_6), .COLUNA_7(grafico_27_coluna_7), .COLUNA_8(grafico_27_coluna_8),
    .COLUNA_9(grafico_27_coluna_9), .COLUNA_10(grafico_27_coluna_10), .COLUNA_11(grafico_27_coluna_11),
    .COLUNA_12(grafico_27_coluna_12), .COLUNA_13(grafico_27_coluna_13), .COLUNA_14(grafico_27_coluna_14),
    .X(4'b1011), .Y(4'b0101));
  DotMatrix #(.matrixcols(15), .matrixrows(15)) dotmatrix_28 (
    .col0(grafico_28_coluna_0), .col1(grafico_28_coluna_1), .col2(grafico_28_coluna_2),
    .col3(grafico_28_coluna_3), .col4(grafico_28_coluna_4), .col5(grafico_28_coluna_5),
    .col6(grafico_28_coluna_6), .col7(grafico_28_coluna_7), .col8(grafico_28_coluna_8),
    .col9(grafico_28_coluna_9), .col10(grafico_28_coluna_10), .col11(grafico_28_coluna_11),
    .col12(grafico_28_coluna_12), .col13(grafico_28_coluna_13), .col14(grafico_28_coluna_14));
  GRAFICO grafico_28 (
    .COLUNA_0(grafico_28_coluna_0), .COLUNA_1(grafico_28_coluna_1), .COLUNA_2(grafico_28_coluna_2),
    .COLUNA_3(grafico_28_coluna_3), .COLUNA_4(grafico_28_coluna_4), .COLUNA_5(grafico_28_coluna_5),
    .COLUNA_6(grafico_28_coluna_6), .COLUNA_7(grafico_28_coluna_7), .COLUNA_8(grafico_28_coluna_8),
    .COLUNA_9(grafico_28_coluna_9), .COLUNA_10(grafico_28_coluna_10), .COLUNA_11(grafico_28_coluna_11),
    .COLUNA_12(grafico_28_coluna_12), .COLUNA_13(grafico_28_coluna_13), .COLUNA_14(grafico_28_coluna_14),
    .X(4'b0011), .Y(4'b1101));
  DotMatrix #(.matrixcols(15), .matrixrows(15)) dotmatrix_29 (
    .col0(grafico_29_coluna_0), .col1(grafico_29_coluna_1), .col2(grafico_29_coluna_2),
    .col3(grafico_29_coluna_3), .col4(grafico_29_coluna_4), .col5(grafico_29_coluna_5),
    .col6(grafico_29_coluna_6), .col7(grafico_29_coluna_7), .col8(grafico_29_coluna_8),
    .col9(grafico_29_coluna_9), .col10(grafico_29_coluna_10), .col11(grafico_29_coluna_11),
    .col12(grafico_29_coluna_12), .col13(grafico_29_coluna_13), .col14(grafico_29_coluna_14));
  GRAFICO grafico_29 (
    .COLUNA_0(grafico_29_coluna_0), .COLUNA_1(grafico_29_coluna_1), .COLUNA_2(grafico_29_coluna_2),
    .COLUNA_3(grafico_29_coluna_3), .COLUNA_4(grafico_29_coluna_4), .COLUNA_5(grafico_29_coluna_5),
    .COLUNA_6(grafico_29_coluna_6), .COLUNA_7(grafico_29_coluna_7), .COLUNA_8(grafico_29_coluna_8),
    .COLUNA_9(grafico_29_coluna_9), .COLUNA_10(grafico_29_coluna_10), .COLUNA_11(grafico_29_coluna_11),
    .COLUNA_12(grafico_29_coluna_12), .COLUNA_13(grafico_29_coluna_13), .COLUNA_14(grafico_29_coluna_14),
    .X(4'b1010), .Y(4'b0110));
  DotMatrix #(.matrixcols(15), .matrixrows(15)) dotmatrix_30 (
    .col0(grafico_30_coluna_0), .col1(grafico_30_coluna_1), .col2(grafico_30_coluna_2),
    .col3(grafico_30_coluna_3), .col4(grafico_30_coluna_4), .col5(grafico_30_coluna_5),
    .col6(grafico_30_coluna_6), .col7(grafico_30_coluna_7), .col8(grafico_30_coluna_8),
    .col9(grafico_30_coluna_9), .col10(grafico_30_coluna_10), .col11(grafico_30_coluna_11),
    .col12(grafico_30_coluna_12), .col13(grafico_30_coluna_13), .col14(grafico_30_coluna_14));
  GRAFICO grafico_30 (
    .COLUNA_0(grafico_30_coluna_0), .COLUNA_1(grafico_30_coluna_1), .COLUNA_2(grafico_30_coluna_2),
    .COLUNA_3(grafico_30_coluna_3), .COLUNA_4(grafico_30_coluna_4), .COLUNA_5(grafico_30_coluna_5),
    .COLUNA_6(grafico_30_coluna_6), .COLUNA_7(grafico_30_coluna_7), .COLUNA_8(grafico_30_coluna_8),
    .COLUNA_9(grafico_30_coluna_9), .COLUNA_10(grafico_30_coluna_10), .COLUNA_11(grafico_30_coluna_11),
    .COLUNA_12(grafico_30_coluna_12), .COLUNA_13(grafico_30_coluna_13), .COLUNA_14(grafico_30_coluna_14),
    .X(4'b0010), .Y(4'b1110));
  DotMatrix #(.matrixcols(15), .matrixrows(15)) dotmatrix_31 (
    .col0(grafico_31_coluna_0), .col1(grafico_31_coluna_1), .col2(grafico_31_coluna_2),
    .col3(grafico_31_coluna_3), .col4(grafico_31_coluna_4), .col5(grafico_31_coluna_5),
    .col6(grafico_31_coluna_6), .col7(grafico_31_coluna_7), .col8(grafico_31_coluna_8),
    .col9(grafico_31_coluna_9), .col10(grafico_31_coluna_10), .col11(grafico_31_coluna_11),
    .col12(grafico_31_coluna_12), .col13(grafico_31_coluna_13), .col14(grafico_31_coluna_14));
  GRAFICO grafico_31 (
    .COLUNA_0(grafico_31_coluna_0), .COLUNA_1(grafico_31_coluna_1), .COLUNA_2(grafico_31_coluna_2),
    .COLUNA_3(grafico_31_coluna_3), .COLUNA_4(grafico_31_coluna_4), .COLUNA_5(grafico_31_coluna_5),
    .COLUNA_6(grafico_31_coluna_6), .COLUNA_7(grafico_31_coluna_7), .COLUNA_8(grafico_31_coluna_8),
    .COLUNA_9(grafico_31_coluna_9), .COLUNA_10(grafico_31_coluna_10), .COLUNA_11(grafico_31_coluna_11),
    .COLUNA_12(grafico_31_coluna_12), .COLUNA_13(grafico_31_coluna_13), .COLUNA_14(grafico_31_coluna_14),
    .X(4'b1001), .Y(4'b0111));
  DotMatrix #(.matrixcols(15), .matrixrows(15)) dotmatrix_32 (
    .col0(grafico_32_coluna_0), .col1(grafico_32_coluna_1), .col2(grafico_32_coluna_2),
    .col3(grafico_32_coluna_3), .col4(grafico_32_coluna_4), .col5(grafico_32_coluna_5),
    .col6(grafico_32_coluna_6), .col7(grafico_32_coluna_7), .col8(grafico_32_coluna_8),
    .col9(grafico_32_coluna_9), .col10(grafico_32_coluna_10), .col11(grafico_32_coluna_11),
    .col12(grafico_32_coluna_12), .col13(grafico_32_coluna_13), .col14(grafico_32_coluna_14));
  GRAFICO grafico_32 (
    .COLUNA_0(grafico_32_coluna_0), .COLUNA_1(grafico_32_coluna_1), .COLUNA_2(grafico_32_coluna_2),
    .COLUNA_3(grafico_32_coluna_3), .COLUNA_4(grafico_32_coluna_4), .COLUNA_5(grafico_32_coluna_5),
    .COLUNA_6(grafico_32_coluna_6), .COLUNA_7(grafico_32_coluna_7), .COLUNA_8(grafico_32_coluna_8),
    .COLUNA_9(grafico_32_coluna_9), .COLUNA_10(grafico_32_coluna_10), .COLUNA_11(grafico_32_coluna_11),
    .COLUNA_12(grafico_32_coluna_12), .COLUNA_13(grafico_32_coluna_13), .COLUNA_14(grafico_32_coluna_14),
    .X(4'b0001), .Y(4'b1111));
  DotMatrix #(.matrixcols(15), .matrixrows(15)) dotmatrix_33 (
    .col0(grafico_33_coluna_0), .col1(grafico_33_coluna_1), .col2(grafico_33_coluna_2),
    .col3(grafico_33_coluna_3), .col4(grafico_33_coluna_4), .col5(grafico_33_coluna_5),
    .col6(grafico_33_coluna_6), .col7(grafico_33_coluna_7), .col8(grafico_33_coluna_8),
    .col9(grafico_33_coluna_9), .col10(grafico_33_coluna_10), .col11(grafico_33_coluna_11),
    .col12(grafico_33_coluna_12), .col13(grafico_33_coluna_13), .col14(grafico_33_coluna_14));
  GRAFICO grafico_33 (
    .COLUNA_0(grafico_33_coluna_0), .COLUNA_1(grafico_33_coluna_1), .COLUNA_2(grafico_33_coluna_2),
    .COLUNA_3(grafico_33_coluna_3), .COLUNA_4(grafico_33_coluna_4), .COLUNA_5(grafico_33_coluna_5),
    .COLUNA_6(grafico_33_coluna_6), .COLUNA_7(grafico_33_coluna_7), .COLUNA_8(grafico_33_coluna_8),
    .COLUNA_9(grafico_33_coluna_9), .COLUNA_10(grafico_33_coluna_10), .COLUNA_11(grafico_33_coluna_11),
    .COLUNA_12(grafico_33_coluna_12), .COLUNA_13(grafico_33_coluna_13), .COLUNA_14(grafico_33_coluna_14),
    .X(4'b1000), .Y(4'b1000));

  // Notes on the sheet:
  //   CTRL + k para iniciar a simulação
  //   Deixar todos os relógios com valor 1 antes de iniciar
  //   Configurar a frequência de pulso para 32Hz em: Simular > Frequência de pulso > 32 Hz
endmodule
