// Logisim project FEED THE DOT.circ as structural Verilog
module main (
);

  wire and_1_out, CLK, CLK_64HZ, DOWN, END_GAME, gpu_1_r, keyboard_1_avail, LEFT, RIGHT, UP;
  wire [3:0] controller_1_out_6, controller_1_out_7, manager_1_m1, manager_1_m2, manager_1_placar,
       manager_1_s1, manager_1_s2;
  wire [6:0] keyboard_1_data;
  wire [15:0] gpu_1__0, gpu_1__1, gpu_1__2, gpu_1__3, gpu_1__4, gpu_1__5, gpu_1__6, gpu_1__7, gpu_1__8,
       gpu_1__9, gpu_1__10, gpu_1__11, gpu_1__12, gpu_1__13, gpu_1__14, gpu_1__15;

  Clock clock_1 (.out(CLK_64HZ));
  Button button_1 ();  // open: out
  Button button_2 ();  // open: out
  Button button_3 ();  // open: out
  Button button_4 ();  // open: out
  GPU gpu_1 (
    .X(controller_1_out_6), ._0(gpu_1__0), ._11(gpu_1__11), ._12(gpu_1__12), ._13(gpu_1__13),
    ._14(gpu_1__14), ._15(gpu_1__15), ._10(gpu_1__10), ._9(gpu_1__9), ._8(gpu_1__8), ._7(gpu_1__7),
    ._6(gpu_1__6), ._5(gpu_1__5), ._4(gpu_1__4), ._3(gpu_1__3), ._2(gpu_1__2), ._1(gpu_1__1), .R(gpu_1_r),
    .Y(controller_1_out_7), .in_3(CLK));
  DotMatrix #(.matrixcols(16), .matrixrows(16), .persist(10)) dotmatrix_1 (
    .col0(gpu_1__0), .col1(gpu_1__1), .col2(gpu_1__2), .col3(gpu_1__3), .col4(gpu_1__4), .col5(gpu_1__5),
    .col6(gpu_1__6), .col7(gpu_1__7), .col8(gpu_1__8), .col9(gpu_1__9), .col10(gpu_1__10), .col11(gpu_1__11),
    .col12(gpu_1__12), .col13(gpu_1__13), .col14(gpu_1__14), .col15(gpu_1__15));
  CONTROLLER controller_1 (
    .out_6(controller_1_out_6), .UP(UP), .DOWN(DOWN), .LEFT(LEFT), .RIGHT(RIGHT), .clk(and_1_out),
    .out_7(controller_1_out_7));
  and and_1 (and_1_out, CLK, ~END_GAME);  // AND_Gate
  Keyboard keyboard_1 (.clr(keyboard_1_avail), .avail(keyboard_1_avail), .data(keyboard_1_data));  // open: clk, re
  Hex_Digit_Display hex_digit_display_1 (.value(manager_1_m1));  // open: dp
  KEYBOARD_PROCESS keyboard_process_1 (.in_1(keyboard_1_data), .LEFT(LEFT), .UP(UP), .RIGHT(RIGHT), .DOWN(DOWN));
  LED led_1 ();  // open: in
  LED led_2 ();  // open: in
  Hex_Digit_Display hex_digit_display_2 (.value(manager_1_m2));  // open: dp
  MANAGER manager_1 (
    .CLK_64HZ(CLK_64HZ), .in_2(gpu_1_r), .M2(manager_1_m2), .M1(manager_1_m1), .S2(manager_1_s2),
    .S1(manager_1_s1), .CLK(CLK), .PLACAR(manager_1_placar), .END_GAME(END_GAME));
  Hex_Digit_Display hex_digit_display_3 (.value(manager_1_s2));  // open: dp
  Hex_Digit_Display hex_digit_display_4 (.value(manager_1_s1));  // open: dp
  Hex_Digit_Display hex_digit_display_5 (.value(manager_1_placar));  // open: dp
endmodule

module GPU (
  input  [3:0] X,
  input  [3:0] Y,
  input  in_3,
  output [15:0] _0,
  output [15:0] _1,
  output [15:0] _2,
  output [15:0] _3,
  output [15:0] _4,
  output [15:0] _5,
  output [15:0] _6,
  output [15:0] _7,
  output [15:0] _8,
  output [15:0] _9,
  output [15:0] _10,
  output [15:0] _11,
  output [15:0] _12,
  output [15:0] _13,
  output [15:0] _14,
  output [15:0] _15,
  output R
);

  wire comparator_1_eq, comparator_2_eq;
  wire [3:0] random_1_out, random_2_out;
  wire [15:0] _0_t, _1_t, _2_t, _3_t, _4_t, _5_t, _6_t, _7_t, _8_t, _9_t, a, b, c, d, demultiplexer_1_out15,
       demultiplexer_3_out15, demultiplexer_4_out0, demultiplexer_4_out1, demultiplexer_4_out2,
       demultiplexer_4_out3, demultiplexer_4_out4, demultiplexer_4_out5, demultiplexer_4_out6,
       demultiplexer_4_out7, demultiplexer_4_out8, demultiplexer_4_out9, demultiplexer_4_out10,
       demultiplexer_4_out11, demultiplexer_4_out12, demultiplexer_4_out13, demultiplexer_4_out14,
       demultiplexer_4_out15, e, f;

  assign _0 = demultiplexer_4_out0 | _0_t;  // OR_Gate or_1, 16 bits wide
  Demultiplexer #(.select(4), .enable("false")) demultiplexer_1 (
    .out0(demultiplexer_1_out15[15]), .out1(demultiplexer_1_out15[14]), .out2(demultiplexer_1_out15[13]),
    .out3(demultiplexer_1_out15[12]), .out4(demultiplexer_1_out15[11]), .out5(demultiplexer_1_out15[10]),
    .out6(demultiplexer_1_out15[9]), .out7(demultiplexer_1_out15[8]), .out8(demultiplexer_1_out15[7]),
    .out9(demultiplexer_1_out15[6]), .out10(demultiplexer_1_out15[5]), .out11(demultiplexer_1_out15[4]),
    .out12(demultiplexer_1_out15[3]), .out13(demultiplexer_1_out15[2]), .out14(demultiplexer_1_out15[1]),
    .out15(demultiplexer_1_out15[0]), .sel(random_1_out));  // open: in
  Random #(.width(4)) random_1 (.clk(R), .out(random_1_out));  // open: next, clr
  assign _1 = demultiplexer_4_out1 | _1_t;  // OR_Gate or_2, 16 bits wide
  assign _2 = demultiplexer_4_out2 | _2_t;  // OR_Gate or_3, 16 bits wide
  assign _3 = demultiplexer_4_out3 | _3_t;  // OR_Gate or_4, 16 bits wide
  Demultiplexer #(.select(4), .width(16), .enable("false")) demultiplexer_2 (
    .out0(_0_t), .out1(_1_t), .out2(_2_t), .out3(_3_t), .out4(_4_t), .out5(_5_t), .out6(_6_t), .out7(_7_t),
    .out8(_8_t), .out9(_9_t), .out10(a), .out11(b), .out12(c), .out13(d), .out14(e), .out15(f),
    .in(demultiplexer_1_out15), .sel(random_2_out));
  assign _4 = demultiplexer_4_out4 | _4_t;  // OR_Gate or_5, 16 bits wide
  Random #(.width(4)) random_2 (.clk(R), .out(random_2_out));  // open: next, clr
  assign _5 = demultiplexer_4_out5 | _5_t;  // OR_Gate or_6, 16 bits wide
  Demultiplexer #(.select(4), .enable("false")) demultiplexer_3 (
    .out0(demultiplexer_3_out15[15]), .out1(demultiplexer_3_out15[14]), .out2(demultiplexer_3_out15[13]),
    .out3(demultiplexer_3_out15[12]), .out4(demultiplexer_3_out15[11]), .out5(demultiplexer_3_out15[10]),
    .out6(demultiplexer_3_out15[9]), .out7(demultiplexer_3_out15[8]), .out8(demultiplexer_3_out15[7]),
    .out9(demultiplexer_3_out15[6]), .out10(demultiplexer_3_out15[5]), .out11(demultiplexer_3_out15[4]),
    .out12(demultiplexer_3_out15[3]), .out13(demultiplexer_3_out15[2]), .out14(demultiplexer_3_out15[1]),
    .out15(demultiplexer_3_out15[0]), .in(1'b1), .sel(X));
  assign _6 = demultiplexer_4_out6 | _6_t;  // OR_Gate or_7, 16 bits wide
  assign _7 = demultiplexer_4_out7 | _7_t;  // OR_Gate or_8, 16 bits wide
  Comparator #(.width(4)) comparator_1 (.a(X), .b(random_1_out), .eq(comparator_1_eq));  // open: gt, lt
  Comparator #(.width(4)) comparator_2 (.a(Y), .b(random_2_out), .eq(comparator_2_eq));  // open: gt, lt
  assign _8 = demultiplexer_4_out8 | _8_t;  // OR_Gate or_9, 16 bits wide
  Demultiplexer #(.select(4), .width(16), .enable("false")) demultiplexer_4 (
    .out0(demultiplexer_4_out0), .out1(demultiplexer_4_out1), .out2(demultiplexer_4_out2),
    .out3(demultiplexer_4_out3), .out4(demultiplexer_4_out4), .out5(demultiplexer_4_out5),
    .out6(demultiplexer_4_out6), .out7(demultiplexer_4_out7), .out8(demultiplexer_4_out8),
    .out9(demultiplexer_4_out9), .out10(demultiplexer_4_out10), .out11(demultiplexer_4_out11),
    .out12(demultiplexer_4_out12), .out13(demultiplexer_4_out13), .out14(demultiplexer_4_out14),
    .out15(demultiplexer_4_out15), .in(demultiplexer_3_out15), .sel(Y));
  and and_1 (R, comparator_1_eq, comparator_2_eq);
  assign _9 = demultiplexer_4_out9 | _9_t;  // OR_Gate or_10, 16 bits wide
  assign _10 = demultiplexer_4_out10 | a;  // OR_Gate or_11, 16 bits wide
  assign _11 = demultiplexer_4_out11 | b;  // OR_Gate or_12, 16 bits wide
  assign _12 = demultiplexer_4_out12 | c;  // OR_Gate or_13, 16 bits wide
  assign _13 = demultiplexer_4_out13 | d;  // OR_Gate or_14, 16 bits wide
  assign _14 = demultiplexer_4_out14 | e;  // OR_Gate or_15, 16 bits wide
  assign _15 = demultiplexer_4_out15 | f;  // OR_Gate or_16, 16 bits wide

  // Other names for the same wires on the sheet: CLK = in_3

  // Notes on the sheet:
  //   Gerar novo erro
endmodule

module DOT_MEM_X (
  input  [3:0] X__in,
  input  CLK,
  input  [15:0] X__select,
  output [15:0] OUT,
  output [3:0] Q
);

  wire comparator_1_eq, multiplexer_1_out;
  wire [15:0] demultiplexer_1_out15;

  Demultiplexer #(.select(4), .enable("false")) demultiplexer_1 (
    .out0(demultiplexer_1_out15[15]), .out1(demultiplexer_1_out15[14]), .out2(demultiplexer_1_out15[13]),
    .out3(demultiplexer_1_out15[12]), .out4(demultiplexer_1_out15[11]), .out5(demultiplexer_1_out15[10]),
    .out6(demultiplexer_1_out15[9]), .out7(demultiplexer_1_out15[8]), .out8(demultiplexer_1_out15[7]),
    .out9(demultiplexer_1_out15[6]), .out10(demultiplexer_1_out15[5]), .out11(demultiplexer_1_out15[4]),
    .out12(demultiplexer_1_out15[3]), .out13(demultiplexer_1_out15[2]), .out14(demultiplexer_1_out15[1]),
    .out15(demultiplexer_1_out15[0]), .in(1'b1), .sel(Q));
  Register #(.width(4), .Select("low")) register_1 (.D(X__in), .en(multiplexer_1_out), .Q(Q), .clk(CLK));  // open: clr
  Multiplexer #(.enable("false")) multiplexer_1 (
    .in0(1'b1), .in1(1'b0), .out(multiplexer_1_out), .sel(comparator_1_eq));
  Comparator #(.width(4)) comparator_1 (.a(X__in), .b(Q), .eq(comparator_1_eq));  // open: gt, lt
  assign OUT = demultiplexer_1_out15 | X__select;  // OR_Gate or_1, 16 bits wide
endmodule

module DOT_MEM_Y (
  input  [3:0] Y__IN,
  input  CLK,
  output [3:0] OUT
);

  Register #(.width(4), .Select("low")) register_1 (.D(Y__IN), .Q(OUT), .clk(CLK));  // open: en, clr
endmodule

module CONTROLLER (
  input  clk,
  input  UP,
  input  DOWN,
  input  LEFT,
  input  RIGHT,
  output [3:0] out_6,
  output [3:0] out_7
);

  wire conv_1_direction, conv_1_left_right, conv_1_up_down, d_ff_1_q, d_ff_2_q, d_ff_3_q, d_ff_4_q, or_1_out,
       or_2_out, or_3_out, or_4_out;

  or or_1 (or_1_out, DOWN, LEFT, RIGHT);
  D_Flip_Flop d_ff_1 (.clk(clk), .Q(d_ff_1_q), .preset(UP), .reset(or_1_out));  // open: D, Qn
  COD_01 cod_01_1 (
    .Y(out_6), .X(out_7), .LEFT_RIGHT(conv_1_left_right), .UP_DOWN(conv_1_up_down),
    .DIRECTION(conv_1_direction), .CLOCK(clk));
  CONV conv_1 (
    .UP_DOWN(conv_1_up_down), .LEFT_RIGHT(conv_1_left_right), .DIRECTION(conv_1_direction), .DOWN(d_ff_2_q),
    .UP(d_ff_1_q), .LEFT(d_ff_3_q), .RIGHT(d_ff_4_q));
  or or_2 (or_2_out, UP, LEFT, RIGHT);
  D_Flip_Flop d_ff_2 (.clk(clk), .Q(d_ff_2_q), .preset(DOWN), .reset(or_2_out));  // open: D, Qn
  or or_3 (or_3_out, UP, DOWN, RIGHT);
  D_Flip_Flop d_ff_3 (.clk(clk), .Q(d_ff_3_q), .preset(LEFT), .reset(or_3_out));  // open: D, Qn
  D_Flip_Flop d_ff_4 (.clk(clk), .Q(d_ff_4_q), .preset(RIGHT), .reset(or_4_out));  // open: D, Qn
  or or_4 (or_4_out, UP, DOWN, LEFT);
endmodule

module CONV (
  input  UP,
  input  DOWN,
  input  LEFT,
  input  RIGHT,
  output UP_DOWN,
  output LEFT_RIGHT,
  output DIRECTION
);

  or or_1 (DIRECTION, UP, DOWN);

  assign LEFT_RIGHT = LEFT;
  assign UP_DOWN = UP;
endmodule

module COD_01 (
  input  LEFT_RIGHT,
  input  UP_DOWN,
  input  DIRECTION,
  input  CLOCK,
  output [3:0] Y,
  output [3:0] X
);

  wire not_1_out;
  wire [3:0] adder_1_out, adder_2_out, multiplexer_1_out, multiplexer_2_out;

  Multiplexer #(.width(4), .enable("false")) multiplexer_1 (
    .in0(4'b0001), .in1(4'b1111), .out(multiplexer_1_out), .sel(LEFT_RIGHT));
  Multiplexer #(.width(4), .enable("false")) multiplexer_2 (
    .in0(4'b0001), .in1(4'b1111), .out(multiplexer_2_out), .sel(UP_DOWN));
  Adder #(.width(4)) adder_1 (.a(Y), .b(multiplexer_2_out), .out(adder_1_out));  // open: cin, cout
  Adder #(.width(4)) adder_2 (.a(X), .b(multiplexer_1_out), .out(adder_2_out));  // open: cin, cout
  not not_1 (not_1_out, DIRECTION);
  Register #(.width(4), .Select("low")) register_1 (.D(adder_1_out), .en(DIRECTION), .Q(Y), .clk(CLOCK));  // open: clr
  Register #(.width(4), .Select("low")) register_2 (.D(adder_2_out), .en(not_1_out), .Q(X), .clk(CLOCK));  // open: clr

  // Other names for the same wires on the sheet: clk = CLOCK

  // Notes on the sheet:
  //   Y
  //   X
endmodule

module MANAGER (
  input  CLK_64HZ,
  input  in_2,
  output [3:0] M2,
  output [3:0] M1,
  output [3:0] S2,
  output [3:0] S1,
  output CLK,
  output [3:0] PLACAR,
  output END_GAME
);

  wire cont_0a59_2_next_clk, j_k_ff_1_q, j_k_ff_2_q, j_k_ff_3_q, j_k_ff_4_q, j_k_ff_5_q;
  wire [2:0] counter_1_q;

  J_K_Flip_Flop j_k_ff_1 (.J(1'b1), .clk(CLK_64HZ), .K(1'b1), .Q(j_k_ff_1_q));  // open: Qn, preset, reset
  J_K_Flip_Flop j_k_ff_2 (.J(1'b1), .clk(j_k_ff_1_q), .K(1'b1), .Q(j_k_ff_2_q));  // open: Qn, preset, reset
  J_K_Flip_Flop j_k_ff_3 (.J(1'b1), .clk(j_k_ff_2_q), .K(1'b1), .Q(j_k_ff_3_q));  // open: Qn, preset, reset
  J_K_Flip_Flop j_k_ff_4 (.J(1'b1), .clk(j_k_ff_3_q), .K(1'b1), .Q(j_k_ff_4_q));  // open: Qn, preset, reset
  CONT_0A59 cont_0a59_1 (.clk(cont_0a59_2_next_clk), .RESET(END_GAME), .SECONDS(M2), .MINUTS(M1));  // open: NEXT_CLK
  CONT_0A59 cont_0a59_2 (
    .clk(j_k_ff_5_q), .NEXT_CLK(cont_0a59_2_next_clk), .RESET(END_GAME), .SECONDS(S2), .MINUTS(S1));
  J_K_Flip_Flop j_k_ff_5 (.J(1'b1), .clk(j_k_ff_4_q), .K(1'b1), .Q(j_k_ff_5_q));  // open: Qn, preset, reset
  Counter #(.width(3), .max('h7)) counter_1 (
    .Q(counter_1_q), .clk(in_2), .clr(END_GAME));  // open: load, D, count, carry, preset, down
  J_K_Flip_Flop j_k_ff_6 (.J(1'b1), .clk(j_k_ff_5_q), .K(1'b1));  // open: Q, Qn, preset, reset
  Multiplexer #(.select(3), .enable("false")) multiplexer_1 (
    .in0(j_k_ff_4_q), .in1(j_k_ff_3_q), .in2(j_k_ff_2_q), .in3(j_k_ff_1_q), .in4(CLK_64HZ), .out(CLK),
    .sel(counter_1_q));  // open: in5, in6, in7
  Comparator #(.width(3), .mode("unsigned")) comparator_1 (.a(counter_1_q), .b(3'b100), .gt(END_GAME));  // open: eq, lt
  assign PLACAR = {{1{1'b0}}, counter_1_q};  // Bit_Extender bit_extender_1

  // Notes on the sheet:
  //   MM:SS
endmodule

module KEYBOARD_PROCESS (
  input  [6:0] in_1,
  output LEFT,
  output UP,
  output RIGHT,
  output DOWN
);

  wire [3:0] bit_extender_1_out;

  Bit_Extender #(.in_width(7), .out_width(4), .\type ("zero")) bit_extender_1 (.in(in_1), .out(bit_extender_1_out));
  and and_1 (LEFT, ~bit_extender_1_out[3], ~bit_extender_1_out[2], ~bit_extender_1_out[1], bit_extender_1_out[0]);  // AND_Gate
  and and_2 (UP, ~bit_extender_1_out[3], bit_extender_1_out[2], bit_extender_1_out[1], bit_extender_1_out[0]);  // AND_Gate
  and and_3 (RIGHT, ~bit_extender_1_out[3], bit_extender_1_out[2], ~bit_extender_1_out[1], ~bit_extender_1_out[0]);  // AND_Gate
  and and_4 (DOWN, ~bit_extender_1_out[3], ~bit_extender_1_out[2], bit_extender_1_out[1], bit_extender_1_out[0]);  // AND_Gate
endmodule

module CONT_0A59 (
  input  clk,
  input  RESET,
  output [3:0] SECONDS,
  output [3:0] MINUTS,
  output NEXT_CLK
);

  wire cont_0a9_1_next_clk, nor_1_out;

  CONT_0a9 cont_0a9_1 (.clk(clk), .RESET(NEXT_CLK), .OUT(SECONDS), .NEXT_CLK(cont_0a9_1_next_clk));
  or or_1 (NEXT_CLK, RESET, nor_1_out);
  CONT_0a9 cont_0a9_2 (.clk(cont_0a9_1_next_clk), .RESET(NEXT_CLK), .OUT(MINUTS));  // open: NEXT_CLK
  nor nor_1 (nor_1_out, SECONDS[3], SECONDS[2], SECONDS[1], SECONDS[0], MINUTS[3], ~MINUTS[2], ~MINUTS[1], MINUTS[0]);  // NOR_Gate

  // Other names for the same wires on the sheet: RESET_59 = NEXT_CLK
endmodule

module CONT_0a9 (
  input  clk,
  input  RESET,
  output [3:0] OUT,
  output NEXT_CLK
);

  wire or_1_out;
  wire [3:0] adder_1_out;

  Register #(.width(4), .Select("low")) register_1 (.D(adder_1_out), .Q(OUT), .clk(clk), .clr(or_1_out));  // open: en
  or or_1 (or_1_out, NEXT_CLK, RESET);
  Adder #(.width(4)) adder_1 (.a(OUT), .b(4'b0001), .out(adder_1_out));  // open: cin, cout
  nor NOR (NEXT_CLK, OUT[0], ~OUT[1], OUT[2], ~OUT[3]);  // NOR_Gate

  // Other names for the same wires on the sheet: RESET_9 = NEXT_CLK
endmodule

module TESTE_COD_01 (
);

  COD_01 cod_01_1 ();  // open: Y, X, LEFT_RIGHT, UP_DOWN, DIRECTION, CLOCK
endmodule

module tmp (
  input  [3:0] X,
  input  [3:0] Y,
  input  in_3,
  output [15:0] _0,
  output [15:0] _1,
  output [15:0] _2,
  output [15:0] _3,
  output [15:0] _4,
  output [15:0] _5,
  output [15:0] _6,
  output [15:0] _7,
  output [15:0] _8,
  output [15:0] _9,
  output [15:0] _10,
  output [15:0] _11,
  output [15:0] _12,
  output [15:0] _13,
  output [15:0] _14,
  output [15:0] _15,
  output R
);

  wire comparator_1_eq, comparator_2_eq;
  wire [3:0] dot_mem_x_2_q, dot_mem_y_1_out, random_1_out, random_2_out;
  wire [15:0] _00, _0_t, _1_t, _2_t, _3_t, _4_t, _5_t, _6_t, _7_t, _8_t, _9_t, _11_t, _22, _33, _44, _55,
       _66, _77, _88, _99, a, aa, b, bb, c, cc, d, dd, demultiplexer_1_out15, demultiplexer_3_out15,
       demultiplexer_4_out0, demultiplexer_4_out1, demultiplexer_4_out2, demultiplexer_4_out3,
       demultiplexer_4_out4, demultiplexer_4_out5, demultiplexer_4_out6, demultiplexer_4_out7,
       demultiplexer_4_out8, demultiplexer_4_out9, demultiplexer_4_out10, demultiplexer_4_out11,
       demultiplexer_4_out12, demultiplexer_4_out13, demultiplexer_4_out14, demultiplexer_4_out15,
       dot_mem_x_1_out, dot_mem_x_2_out, e, ee, f, ff;

  assign _0 = demultiplexer_4_out0 | _00 | _0_t;  // OR_Gate or_1, 16 bits wide
  Demultiplexer #(.select(4), .enable("false")) demultiplexer_1 (
    .out0(demultiplexer_1_out15[15]), .out1(demultiplexer_1_out15[14]), .out2(demultiplexer_1_out15[13]),
    .out3(demultiplexer_1_out15[12]), .out4(demultiplexer_1_out15[11]), .out5(demultiplexer_1_out15[10]),
    .out6(demultiplexer_1_out15[9]), .out7(demultiplexer_1_out15[8]), .out8(demultiplexer_1_out15[7]),
    .out9(demultiplexer_1_out15[6]), .out10(demultiplexer_1_out15[5]), .out11(demultiplexer_1_out15[4]),
    .out12(demultiplexer_1_out15[3]), .out13(demultiplexer_1_out15[2]), .out14(demultiplexer_1_out15[1]),
    .out15(demultiplexer_1_out15[0]), .sel(random_1_out));  // open: in
  Random #(.width(4)) random_1 (.clk(R), .out(random_1_out));  // open: next, clr
  assign _1 = demultiplexer_4_out1 | _11_t | _1_t;  // OR_Gate or_2, 16 bits wide
  assign _2 = demultiplexer_4_out2 | _22 | _2_t;  // OR_Gate or_3, 16 bits wide
  assign _3 = demultiplexer_4_out3 | _33 | _3_t;  // OR_Gate or_4, 16 bits wide
  Demultiplexer #(.select(4), .width(16), .enable("false")) demultiplexer_2 (
    .out0(_0_t), .out1(_1_t), .out2(_2_t), .out3(_3_t), .out4(_4_t), .out5(_5_t), .out6(_6_t), .out7(_7_t),
    .out8(_8_t), .out9(_9_t), .out10(a), .out11(b), .out12(c), .out13(d), .out14(e), .out15(f),
    .in(demultiplexer_1_out15), .sel(random_2_out));
  assign _4 = demultiplexer_4_out4 | _44 | _4_t;  // OR_Gate or_5, 16 bits wide
  Random #(.width(4)) random_2 (.clk(R), .out(random_2_out));  // open: next, clr
  assign _5 = demultiplexer_4_out5 | _55 | _5_t;  // OR_Gate or_6, 16 bits wide
  Demultiplexer #(.select(4), .enable("false")) demultiplexer_3 (
    .out0(demultiplexer_3_out15[15]), .out1(demultiplexer_3_out15[14]), .out2(demultiplexer_3_out15[13]),
    .out3(demultiplexer_3_out15[12]), .out4(demultiplexer_3_out15[11]), .out5(demultiplexer_3_out15[10]),
    .out6(demultiplexer_3_out15[9]), .out7(demultiplexer_3_out15[8]), .out8(demultiplexer_3_out15[7]),
    .out9(demultiplexer_3_out15[6]), .out10(demultiplexer_3_out15[5]), .out11(demultiplexer_3_out15[4]),
    .out12(demultiplexer_3_out15[3]), .out13(demultiplexer_3_out15[2]), .out14(demultiplexer_3_out15[1]),
    .out15(demultiplexer_3_out15[0]), .in(1'b1), .sel(X));
  assign _6 = demultiplexer_4_out6 | _66 | _6_t;  // OR_Gate or_7, 16 bits wide
  assign _7 = demultiplexer_4_out7 | _77 | _7_t;  // OR_Gate or_8, 16 bits wide
  Comparator #(.width(4)) comparator_1 (.a(X), .b(random_1_out), .eq(comparator_1_eq));  // open: gt, lt
  Comparator #(.width(4)) comparator_2 (.a(Y), .b(random_2_out), .eq(comparator_2_eq));  // open: gt, lt
  assign _8 = demultiplexer_4_out8 | _88 | _8_t;  // OR_Gate or_9, 16 bits wide
  Demultiplexer #(.select(4), .width(16), .enable("false")) demultiplexer_4 (
    .out0(demultiplexer_4_out0), .out1(demultiplexer_4_out1), .out2(demultiplexer_4_out2),
    .out3(demultiplexer_4_out3), .out4(demultiplexer_4_out4), .out5(demultiplexer_4_out5),
    .out6(demultiplexer_4_out6), .out7(demultiplexer_4_out7), .out8(demultiplexer_4_out8),
    .out9(demultiplexer_4_out9), .out10(demultiplexer_4_out10), .out11(demultiplexer_4_out11),
    .out12(demultiplexer_4_out12), .out13(demultiplexer_4_out13), .out14(demultiplexer_4_out14),
    .out15(demultiplexer_4_out15), .in(dot_mem_x_1_out), .sel(Y));
  DOT_MEM_X dot_mem_x_1 (
    .X__in(dot_mem_x_2_q), .X__select(dot_mem_x_2_out), .OUT(dot_mem_x_1_out), .CLK(in_3));  // open: Q
  DOT_MEM_X dot_mem_x_2 (
    .X__in(X), .X__select(demultiplexer_3_out15), .OUT(dot_mem_x_2_out), .CLK(in_3), .Q(dot_mem_x_2_q));
  and and_1 (R, comparator_1_eq, comparator_2_eq);
  assign _9 = demultiplexer_4_out9 | _99 | _9_t;  // OR_Gate or_10, 16 bits wide
  assign _10 = demultiplexer_4_out10 | aa | a;  // OR_Gate or_11, 16 bits wide
  assign _11 = demultiplexer_4_out11 | bb | b;  // OR_Gate or_12, 16 bits wide
  Demultiplexer #(.select(4), .width(16), .enable("false")) demultiplexer_5 (
    .out0(_00), .out1(_11_t), .out2(_22), .out3(_33), .out4(_44), .out5(_55), .out6(_66), .out7(_77),
    .out8(_88), .out9(_99), .out10(aa), .out11(bb), .out12(cc), .out13(dd), .out14(ee), .out15(ff),
    .in(dot_mem_x_1_out), .sel(dot_mem_y_1_out));
  assign _12 = demultiplexer_4_out12 | cc | c;  // OR_Gate or_13, 16 bits wide
  assign _13 = demultiplexer_4_out13 | dd | d;  // OR_Gate or_14, 16 bits wide
  DOT_MEM_Y dot_mem_y_1 (.Y__IN(Y), .CLK(in_3), .OUT(dot_mem_y_1_out));
  assign _14 = demultiplexer_4_out14 | ee | e;  // OR_Gate or_15, 16 bits wide
  assign _15 = demultiplexer_4_out15 | ff | f;  // OR_Gate or_16, 16 bits wide

  // Other names for the same wires on the sheet: CLK = in_3
endmodule
